// Logisim project Maszyna_Los_XY22.circ as structural Verilog: 1 circuit, main circuit main
module main (
  input  START,
  output [1:0] out_2,
  output [5:0] out_3,
  output S5,
  output S4
);

  wire and_1_out, and_2_out, and_3_out, clock_1_out, clock_2_out, clock_3_out, clock_4_out,
       controlled_buffer_1_out, not_1_out, not_2_out, S1, xor_1_out;
  wire [2:0] divider_1_out, divider_1_rem, divider_2_rem, random_1_out, random_2_out, W1;

  Clock clock_1 (.out(clock_1_out));
  Clock clock_2 (.out(clock_2_out));
  not not_1 (not_1_out, START);
  assign controlled_buffer_1_out = not_1_out ? clock_1_out : 1'bz;  // Controlled_Buffer controlled_buffer_1
  Pull_Resistor pull_resistor_1 (.node(controlled_buffer_1_out));
  S_R_Flip_Flop s_r_ff_1 (.S(S1), .clk(clock_2_out), .R(START), .Q(S5));  // open: Qn, preset, reset, en
  nand nand_1 (S4, controlled_buffer_1_out, ~S5);  // NAND_Gate
  Counter #(.width(4), .max('h4), .trigger("falling")) counter_1 (
    .load(1'b1), .carry(S1), .clk(S4));  // open: D, count, Q, clr
  and and_1 (and_1_out, S5, clock_3_out);
  Clock clock_3 (.out(clock_3_out));
  Random #(.width(3), .seed(1)) random_1 (.clk(S4), .out(random_1_out));  // open: next, clr
  Random #(.width(3), .seed(2)) random_2 (.clk(S4), .out(random_2_out));  // open: next, clr
  ROM #(.addrWidth(2), .dataWidth(3)) rom_1 (.addr(2'b00), .data(W1));  // open: sel
  Counter #(.width(2), .max('h3), .ongoal("continue")) counter_2 (
    .Q(out_2), .clk(xor_1_out));  // open: load, D, count, carry, clr
  xor xor_1 (xor_1_out, and_2_out, and_1_out);
  and and_2 (and_2_out, ~S5, S4);  // AND_Gate
  Divider #(.width(3)) divider_1 (.a(random_2_out), .b(W1), .out(divider_1_out), .rem(divider_1_rem));  // open: upper
  Divider #(.width(3)) divider_2 (.a(random_1_out), .b(W1), .rem(divider_2_rem));  // open: out, upper
  and and_3 (and_3_out, ~S5, S4);  // AND_Gate
  Clock clock_4 (.out(clock_4_out));
  not not_2 (not_2_out, and_3_out);
  RAM #(.addrWidth(2), .dataWidth(6), .bus("separate")) ram_1 (
    .addr(out_2), .din({divider_1_rem, divider_2_rem}), .data(out_3), .str(and_3_out), .sel(1'b1),
    .clk(clock_4_out), .ld(not_2_out), .clr(START));

  // Other names for the same wires on the sheet: M1[1:0] = out_2; S2 = START

  // Notes on the sheet:
  //   contents of rom_1 (hex, n*v repeats v):
  //   5
endmodule
