// Logisim project RNG.circ as structural Verilog: 1 circuit, main circuit main
module main (
  input  RESET
);

  wire and_1_out, and_2_out, and_3_out, and_4_out, clock_1_out, clock_2_out, clock_3_out, clock_4_out,
       clock_5_out, controlled_buffer_1_out, not_1_out, not_2_out, not_3_out, S1, S2, S4, S5, xor_1_out;
  wire [1:0] M1;
  wire [4:0] M2;

  Clock clock_1 (.out(clock_1_out));
  Clock clock_2 (.out(clock_2_out));
  Button \RESET_zewnętrzny  (.out(S2));
  not not_1 (not_1_out, S2);
  assign controlled_buffer_1_out = not_1_out ? clock_1_out : 1'bz;  // Controlled_Buffer controlled_buffer_1
  S_R_Flip_Flop s_r_ff_1 (.S(S1), .clk(clock_2_out), .R(S2), .Q(S5));  // open: Qn, preset, reset, en
  Pull_Resistor pull_resistor_1 (.node(controlled_buffer_1_out));
  Counter #(.width(4), .max('h4), .trigger("falling")) counter_1 (
    .load(1'b1), .carry(S1), .clk(S4));  // open: D, count, Q, clr
  nand nand_1 (S4, controlled_buffer_1_out, ~S5);  // NAND_Gate
  and and_1 (and_1_out, S5, clock_3_out);
  Clock clock_3 (.out(clock_3_out));
  Random #(.width(5)) random_1 (.clk(S4), .out(M2));  // open: next, clr
  Counter #(.width(2), .max('h3), .ongoal("continue")) counter_2 (
    .Q(M1), .clk(xor_1_out));  // open: load, D, count, carry, clr
  xor xor_1 (xor_1_out, and_2_out, and_1_out);
  and and_2 (and_2_out, ~S5, S4);  // AND_Gate
  and and_3 (and_3_out, ~S5, S4);  // AND_Gate
  and and_4 (and_4_out, ~S5, S4);  // AND_Gate
  Clock clock_4 (.out(clock_4_out));
  not not_2 (not_2_out, and_3_out);
  Clock clock_5 (.out(clock_5_out));
  not not_3 (not_3_out, and_4_out);
  RAM #(.addrWidth(2), .dataWidth(5), .bus("separate")) ram_1 (
    .addr(M1), .din(M2), .str(and_3_out), .sel(1'b1), .clk(clock_4_out), .ld(not_2_out), .clr(S2));  // open: data
  RAM #(.addrWidth(2), .dataWidth(5), .bus("separate")) ram_2 (
    .addr(M1), .din(M2), .str(and_4_out), .sel(1'b1), .clk(clock_5_out), .ld(not_3_out), .clr(S2));  // open: data
endmodule
