// Logisim project RNG_XY.circ as structural Verilog: 1 circuit, main circuit main
module main (
  input  RESET,
  input  [2:0] in_2
);

  wire and_1_out, and_2_out, and_3_out, and_4_out, and_5_out, clock_1_out, clock_2_out, clock_3_out,
       clock_4_out, clock_5_out, clock_6_out, comparator_1_eq, comparator_1_gt, comparator_1_lt,
       controlled_buffer_1_out, K2, K3s, not_1_out, not_2_out, not_3_out, S1, S2, S4, S5, xor_1_out;
  wire [1:0] M1;
  wire [2:0] K1, random_2_out;

  Clock clock_1 (.out(clock_1_out));
  Clock clock_2 (.out(clock_2_out));
  Button \RESET_zewnętrzny  (.out(S2));
  not not_1 (not_1_out, S2);
  assign controlled_buffer_1_out = not_1_out ? clock_1_out : 1'bz;  // Controlled_Buffer controlled_buffer_1
  S_R_Flip_Flop s_r_ff_1 (.S(S1), .clk(clock_2_out), .R(S2), .Q(S5));  // open: Qn, preset, reset, en
  Pull_Resistor pull_resistor_1 (.node(controlled_buffer_1_out));
  Counter #(.width(4), .max('h4), .trigger("falling")) counter_1 (
    .load(1'b1), .carry(S1), .clk(S4));  // open: D, count, Q, clr
  nand nand_1 (S4, controlled_buffer_1_out, ~S5);  // NAND_Gate
  Comparator #(.width(3), .mode("unsigned")) comparator_1 (
    .a(K1), .b(in_2), .gt(comparator_1_gt), .eq(comparator_1_eq), .lt(comparator_1_lt));
  Clock clock_3 (.out(clock_3_out));
  and and_1 (and_1_out, S5, clock_4_out);
  Clock clock_4 (.out(clock_4_out));
  Random #(.width(3), .seed(1)) random_1 (.clk(S4), .out(K1));  // open: next, clr
  Random #(.width(3), .seed(2)) random_2 (.clk(S4), .out(random_2_out));  // open: next, clr
  or or_1 (K3s, comparator_1_eq, comparator_1_lt);
  Counter #(.width(2), .max('h3), .ongoal("continue")) counter_2 (
    .Q(M1), .clk(xor_1_out));  // open: load, D, count, carry, clr
  xor xor_1 (xor_1_out, and_2_out, and_1_out);
  and and_2 (and_2_out, ~S5, K2);  // AND_Gate
  and and_3 (and_3_out, K3s, clock_3_out);
  or or_2 (K2, comparator_1_gt, and_3_out);
  and and_4 (and_4_out, ~S5, S4);  // AND_Gate
  and and_5 (and_5_out, ~S5, S4);  // AND_Gate
  Clock clock_5 (.out(clock_5_out));
  not not_2 (not_2_out, and_4_out);
  Clock clock_6 (.out(clock_6_out));
  not not_3 (not_3_out, and_5_out);
  RAM #(.addrWidth(2), .dataWidth(3), .bus("separate")) ram_1 (
    .addr(M1), .din(K1), .str(and_4_out), .sel(1'b1), .clk(clock_5_out), .ld(not_2_out), .clr(S2));  // open: data
  RAM #(.addrWidth(2), .dataWidth(3), .bus("separate")) ram_2 (
    .addr(M1), .din(random_2_out), .str(and_5_out), .sel(1'b1), .clk(clock_6_out), .ld(not_3_out), .clr(S2));  // open: data

  // Notes on the sheet:
  //   X
  //   Y
endmodule
