// Logisim project komparator_1_bitowy.circ as structural Verilog: 1 circuit, main circuit main
module main (
  input  A,
  input  B,
  input  in_3,
  output A___B,
  output A___B_2,
  output A___B_3
);

  wire nand_1_out, nand_2_out, nand_3_out, not_1_out, not_2_out;

  not not_1 (not_1_out, A);
  not not_2 (not_2_out, B);
  nand nand_1 (nand_1_out, A, not_2_out, in_3);
  nand nand_2 (nand_2_out, not_1_out, B, in_3);
  not not_3 (A___B, nand_1_out);
  nand nand_3 (nand_3_out, nand_1_out, in_3, nand_2_out);
  not not_4 (A___B_2, nand_2_out);
  not not_5 (A___B_3, nand_3_out);
endmodule
