// Logisim project komparator_4bit_sklejka.circ as structural Verilog: 1 circuit, main circuit main
module main (
  input  [3:0] A,
  input  [3:0] B,
  output A_B,
  output A_B_2,
  output A_B_3
);

  wire main_1_a___b, main_1_a___b_2, main_1_a___b_3, main_2_a___b, main_2_a___b_2, main_2_a___b_3,
       main_3_a___b, main_3_a___b_2, main_3_a___b_3, main_4_a___b, main_4_a___b_2, not_1_out, not_2_out,
       not_3_out, not_4_out, not_5_out, not_6_out, not_7_out, not_8_out;

  komparator_1_bitowy_main main_1 (
    .A(A[3]), .B(B[3]), .in_3(1'b1), .A___B(main_1_a___b), .A___B_2(main_1_a___b_2), .A___B_3(main_1_a___b_3));
  komparator_1_bitowy_main main_2 (
    .A(A[2]), .B(B[2]), .in_3(main_1_a___b_3), .A___B(main_2_a___b), .A___B_2(main_2_a___b_2),
    .A___B_3(main_2_a___b_3));
  komparator_1_bitowy_main main_3 (
    .A(A[1]), .B(B[1]), .in_3(main_2_a___b_3), .A___B(main_3_a___b), .A___B_2(main_3_a___b_2),
    .A___B_3(main_3_a___b_3));
  komparator_1_bitowy_main main_4 (
    .A(A[0]), .B(B[0]), .in_3(main_3_a___b_3), .A___B(main_4_a___b), .A___B_2(main_4_a___b_2), .A___B_3(A_B_3));
  not not_1 (not_1_out, main_4_a___b);
  not not_2 (not_2_out, main_3_a___b);
  not not_3 (not_3_out, main_2_a___b);
  not not_4 (not_4_out, main_1_a___b);
  not not_5 (not_5_out, main_4_a___b_2);
  not not_6 (not_6_out, main_3_a___b_2);
  not not_7 (not_7_out, main_2_a___b_2);
  not not_8 (not_8_out, main_1_a___b_2);
  nand nand_1 (A_B, not_1_out, not_2_out, not_3_out, not_4_out);
  nand nand_2 (A_B_2, not_5_out, not_6_out, not_7_out, not_8_out);
endmodule
