// Logisim project porównywacz.circ as structural Verilog: 1 circuit, main circuit main
module main (
  input  [5:0] in_1,
  input  [1:0] in_2,
  output [2:0] out_3,
  output [5:0] out_4
);

  wire and_2_out, clock_1_out, clock_2_out, clock_3_out, clock_4_out, clock_5_out, comparator_1_eq,
       controlled_buffer_1_out, controlled_buffer_2_out, not_1_out, not_2_out, not_3_out, S1, S2, S4, Z1, Z2,
       Z4, Z5;
  wire [1:0] and_1_out, counter_2_q, counter_3_q, main_1_out_2, or_1_out;
  wire [1:1] K1;
  wire [5:0] main_1_out_3;

  Button button_1 (.out(S2));
  Clock clock_1 (.out(clock_1_out));
  Clock clock_2 (.out(clock_2_out));
  not not_1 (not_1_out, S2);
  assign controlled_buffer_1_out = not_1_out ? clock_1_out : 1'bz;  // Controlled_Buffer controlled_buffer_1
  S_R_Flip_Flop s_r_ff_1 (.S(S1), .clk(clock_2_out), .R(S2), .Q(K1[1]));  // open: Qn, preset, reset, en
  Maszyna_Los_XY22_main main_1 (.START(S2), .out_3(main_1_out_3), .out_2(main_1_out_2));
  Pull_Resistor pull_resistor_1 (.node(controlled_buffer_1_out));
  nand nand_1 (S4, controlled_buffer_1_out, ~K1[1]);  // NAND_Gate
  Counter #(.width(4), .max('h8), .trigger("falling")) counter_1 (
    .load(1'b1), .carry(S1), .clk(S4));  // open: D, count, Q, clr
  assign and_1_out = main_1_out_2 & ~{2{K1[1]}};  // AND_Gate and_1, 2 bits wide
  assign or_1_out = and_1_out | counter_2_q;  // OR_Gate or_1, 2 bits wide
  and and_2 (and_2_out, ~K1[1], S4);  // AND_Gate
  Button button_2 (.out(Z2));
  Clock clock_3 (.out(clock_3_out));
  Clock clock_4 (.out(clock_4_out));
  Counter #(.width(2), .max('h2), .ongoal("continue"), .trigger("falling")) counter_2 (
    .Q(counter_2_q), .clk(Z4), .clr(Z5));  // open: load, D, count, carry
  Clock clock_5 (.out(clock_5_out));
  not not_2 (not_2_out, and_2_out);
  not not_3 (not_3_out, Z2);
  assign controlled_buffer_2_out = not_3_out ? clock_3_out : 1'bz;  // Controlled_Buffer controlled_buffer_2
  S_R_Flip_Flop s_r_ff_2 (.S(Z1), .clk(clock_4_out), .R(Z2), .Q(Z5));  // open: Qn, preset, reset, en
  RAM #(.addrWidth(2), .dataWidth(6), .bus("separate")) ram_1 (
    .addr(or_1_out), .din(main_1_out_3), .data(out_4), .str(and_2_out), .sel(1'b1), .clk(clock_5_out),
    .clr(S2));  // open: ld
  Pull_Resistor pull_resistor_2 (.node(controlled_buffer_2_out));
  and and_3 (Z4, controlled_buffer_2_out, ~Z5);  // AND_Gate
  Counter #(.width(2), .max('h2), .ongoal("continue"), .trigger("falling")) counter_3 (.Q(counter_3_q));  // open: load, D, count, carry, clk, clr
  Counter #(.width(4), .max('h4), .trigger("falling")) counter_4 (
    .load(1'b1), .carry(Z1), .clk(Z4));  // open: D, count, Q, clr
  Counter #(.width(3), .max('h4), .trigger("falling")) counter_5 (
    .Q(out_3), .clk(comparator_1_eq), .clr(Z2));  // open: load, D, count, carry
  Comparator #(.width(6)) comparator_1 (.a(in_1), .b(out_4), .eq(comparator_1_eq));  // open: gt, lt

  // Other names for the same wires on the sheet: D1[1:0] = in_2; K1[0] = K1[1]; S5 = K1[1]
endmodule
