// Logisim project Układ wyświetlania1.circ as structural Verilog: 1 circuit, main circuit main
module main (
  input  [24:0] in_1,
  input  [24:0] in_2,
  input  [24:0] in_3,
  input  [24:0] in_4,
  input  [24:0] in_5,
  output [30:0] out_6,
  output [30:0] out_7,
  output [30:0] out_8,
  output [30:0] out_9,
  output [30:0] out_10
);


  assign out_6 = {1'b1, in_5[4:0], 1'b1, in_4[4:0], 1'b1, in_3[4:0], 1'b1, in_2[4:0], 1'b1, in_1[4:0], 1'b1};
  assign out_7 = {1'b1, in_5[9:5], 1'b1, in_4[9:5], 1'b1, in_3[9:5], 1'b1, in_2[9:5], 1'b1, in_1[9:5], 1'b1};
  assign out_8 = {1'b1, in_5[14:10], 1'b1, in_4[14:10], 1'b1, in_3[14:10], 1'b1, in_2[14:10], 1'b1, in_1[14:10], 1'b1};
  assign out_9 = {1'b1, in_5[19:15], 1'b1, in_4[19:15], 1'b1, in_3[19:15], 1'b1, in_2[19:15], 1'b1, in_1[19:15], 1'b1};
  assign out_10 = {1'b1, in_5[24:20], 1'b1, in_4[24:20], 1'b1, in_3[24:20], 1'b1, in_2[24:20], 1'b1, in_1[24:20], 1'b1};
endmodule
