// Logisim project 4bityx.circ as structural Verilog: 1 circuit, main circuit main
module main (
  input  ENTER,
  input  [3:0] \WEJŚCIE ,
  input  RESET,
  output [3:0] \WYJŚCIE 
);

  wire and_1_out, d_ff_1_q, or_1_out, or_2_out, or_3_out, s_r_ff_1_q;
  wire [3:0] d_ff_2_q, undriven;

  and and_1 (and_1_out, ENTER, or_1_out);
  D_Flip_Flop #(.trigger("falling")) d_ff_1 (
    .clk(and_1_out), .D(1'b1), .Q(d_ff_1_q), .reset(RESET));  // open: Qn, preset, en
  D_Flip_Flop d_ff_2 (.clk(d_ff_1_q), .D(undriven[0]), .Q(d_ff_2_q[0]), .reset(RESET));  // open: Qn, preset, en
  S_R_Flip_Flop #(.trigger("high")) s_r_ff_1 (
    .S(ENTER), .clk(1'b1), .R(RESET), .Q(s_r_ff_1_q));  // open: Qn, preset, reset, en
  D_Flip_Flop d_ff_3 (.clk(d_ff_1_q), .D(undriven[1]), .Q(d_ff_2_q[1]), .reset(RESET));  // open: Qn, preset, en
  or or_1 (or_1_out, or_2_out, or_3_out);
  or or_2 (or_2_out, undriven[0], undriven[1]);
  or or_3 (or_3_out, undriven[2], undriven[3]);
  D_Flip_Flop d_ff_4 (.clk(d_ff_1_q), .D(undriven[2]), .Q(d_ff_2_q[2]), .reset(RESET));  // open: Qn, preset, en
  D_Flip_Flop d_ff_5 (.clk(d_ff_1_q), .D(undriven[3]), .Q(d_ff_2_q[3]), .reset(RESET));  // open: Qn, preset, en
  Register #(.width(4)) register_1 (.D(\WEJŚCIE ), .Q(\WYJŚCIE ), .clk(s_r_ff_1_q));  // open: en, clr
endmodule
