// Logisim project 4bityx_1.circ as structural Verilog: 1 circuit, main circuit main
module main (
  input  ENTER,
  input  Focus,
  input  [3:0] \WEJŚCIE ,
  input  RESET,
  output [3:0] \WYJŚCIE 
);

  wire and_1_out;

  and and_1 (and_1_out, ENTER, Focus);
  Register #(.width(4), .trigger("falling")) register_1 (
    .D(\WEJŚCIE ), .Q(\WYJŚCIE ), .clk(and_1_out));  // open: en, clr
  Controlled_Buffer controlled_buffer_1 ();  // open: in, out, en
  Controlled_Buffer controlled_buffer_2 ();  // open: in, out, en
endmodule
