// Logisim project SAPER.circ as structural Verilog: 1 circuit, main circuit main
module main (
  output [3:0] out_1,
  output [5:0] out_2,
  output koniec_gry,
  output [4:0] out_4,
  output [4:0] out_5
);

  wire clock_1_out, main_2_p3, main_2_p4, main_2_p6, sterowanie_z_klawiatury_1_przemiesc_kursor;
  wire [1:0] main_1_out_2;
  wire [2:0] sterowanie_z_klawiatury_1__3_a_4_s_1_d_6_w_5_enter;
  wire [5:0] main_1_out_3;
  wire [6:0] keyboard_1_data;
  wire [24:0] rom_1_data;
  wire [30:0] main_3_out_7, main_3_out_8, main_3_out_9, main_3_out_10, main_3_out_11, main_3_out_12,
       main_3_out_13, main_3_out_14, main_3_out_15, main_3_out_16, main_3_out_17, main_3_out_18,
       main_3_out_19, main_3_out_20, main_3_out_21, main_3_out_22, main_3_out_23, main_3_out_24,
       main_3_out_25, main_3_out_26, main_3_out_27, main_3_out_28, main_3_out_29, main_3_out_30,
       main_3_out_31, main_3_out_32, main_3_out_33, main_3_out_34, main_3_out_35, main_3_out_36,
       main_3_out_37;

  Maszyna_Los_XY22_main main_1 (.START(main_2_p3), .out_3(main_1_out_3), .out_2(main_1_out_2));
  // porównywacz_main main_2: pin names not known; wires that end beside it: main_1_out_2, main_1_out_3, main_2_p3, main_2_p4, out_5, main_2_p6, out_4, out_1, out_2
  Pull_Resistor pull_resistor_1 (.node(main_2_p6));
  Sterowanie_z_klawiatury sterowanie_z_klawiatury_1 (
    .\input (keyboard_1_data), ._3_a_4_s_1_d_6_w_5_enter(sterowanie_z_klawiatury_1__3_a_4_s_1_d_6_w_5_enter),
    .przemiesc_kursor(sterowanie_z_klawiatury_1_przemiesc_kursor));
  S_R_Flip_Flop #(.trigger("high")) s_r_ff_1 (
    .S(main_2_p6), .clk(1'b1), .R(main_2_p3), .Q(koniec_gry));  // open: Qn, preset, reset, en
  and and_1 (main_2_p4, sterowanie_z_klawiatury_1__3_a_4_s_1_d_6_w_5_enter[0], sterowanie_z_klawiatury_1__3_a_4_s_1_d_6_w_5_enter[2]);
  Clock clock_1 (.out(clock_1_out));
  Keyboard #(.buflen(1)) keyboard_1 (.clk(clock_1_out), .data(keyboard_1_data));  // open: re, clr, avail
  uklad_zwracajacy_pozycje uklad_zwracajacy_pozycje_1 (
    .Sterowanie(sterowanie_z_klawiatury_1__3_a_4_s_1_d_6_w_5_enter),
    .Move(sterowanie_z_klawiatury_1_przemiesc_kursor), .Poz_X(out_4), .Poz_Y(out_5));
  Button START (.out(main_2_p3));
  ROM #(.addrWidth(10), .dataWidth(25)) rom_1 (.addr({out_5, out_4}), .data(rom_1_data));  // open: sel
  SAPER2_main main_3 (
    .x(out_4), .Y(out_5), .WYJSCIE(out_1), .START(main_2_p3), .PAMIEC(rom_1_data), .ENTER(main_2_p4),
    .out_7(main_3_out_7), .out_8(main_3_out_8), .out_9(main_3_out_9), .out_10(main_3_out_10),
    .out_11(main_3_out_11), .out_12(main_3_out_12), .out_13(main_3_out_13), .out_14(main_3_out_14),
    .out_15(main_3_out_15), .out_16(main_3_out_16), .out_17(main_3_out_17), .out_18(main_3_out_18),
    .out_19(main_3_out_19), .out_20(main_3_out_20), .out_21(main_3_out_21), .out_22(main_3_out_22),
    .out_23(main_3_out_23), .out_24(main_3_out_24), .out_25(main_3_out_25), .out_26(main_3_out_26),
    .out_27(main_3_out_27), .out_28(main_3_out_28), .out_29(main_3_out_29), .out_30(main_3_out_30),
    .out_31(main_3_out_31), .out_32(main_3_out_32), .out_33(main_3_out_33), .out_34(main_3_out_34),
    .out_35(main_3_out_35), .out_36(main_3_out_36), .out_37(main_3_out_37));
  DotMatrix #(.inputtype("row"), .matrixcols(31), .matrixrows(31)) dotmatrix_1 (
    .row0(main_3_out_7), .row1(main_3_out_8), .row2(main_3_out_9), .row3(main_3_out_10),
    .row4(main_3_out_11), .row5(main_3_out_12), .row6(main_3_out_13), .row7(main_3_out_14),
    .row8(main_3_out_15), .row9(main_3_out_16), .row10(main_3_out_17), .row11(main_3_out_18),
    .row12(main_3_out_19), .row13(main_3_out_20), .row14(main_3_out_21), .row15(main_3_out_22),
    .row16(main_3_out_23), .row17(main_3_out_24), .row18(main_3_out_25), .row19(main_3_out_26),
    .row20(main_3_out_27), .row21(main_3_out_28), .row22(main_3_out_29), .row23(main_3_out_30),
    .row24(main_3_out_31), .row25(main_3_out_32), .row26(main_3_out_33), .row27(main_3_out_34),
    .row28(main_3_out_35), .row29(main_3_out_36), .row30(main_3_out_37));

  // Other names for the same wires on the sheet: X1[4:0] = out_4; Y1[4:0] = out_5

  // Notes on the sheet:
  //   contents of rom_1 (hex, n*v repeats v):
  //   33*0 1efffff 1dfffff 0 1bfffff 0 0 0 17fffff 7*0 ffffff 16*0 1ff7fff 1feffff 0 1fdffff 0 0 0 1fbffff
  //   7*0 1f7ffff 48*0 1fffbff 1fff7ff 0 1ffefff 0 0 0 1ffdfff 7*0 1ffbfff 111*0 1fffdff 1ffffdf 1ffffbf 0
  //   1ffff7f 0 0 0 1fffeff 7*0 1fffdff 1ffffdf 1ffffbf 0 1ffff7f 236*0 1fffffe 1fffffd 0 1fffffb 0 0 0
  //   1fffff7 7*0 1ffffef
endmodule
