// Logisim project Układ wyświetlania2.circ as structural Verilog: 1 circuit, main circuit main
module main (
  input  in_1,
  input  [3:0] in_2,
  output [24:0] out_3
);

  ROM #(.addrWidth(2), .dataWidth(4)) rom_1 (
    .addr({1'b0, in_1}), .data({out_3[24], out_3[20], out_3[4], out_3[0]}));  // open: sel
  ROM #(.addrWidth(4), .dataWidth(21)) rom_2 (
    .addr(in_2), .data({out_3[23:21], out_3[19:5], out_3[3:1]}));  // open: sel

  // Notes on the sheet:
  //   contents of rom_1 (hex, n*v repeats v):
  //   f
  //   contents of rom_2 (hex, n*v repeats v):
  //   0 88422 1d0e17 1c4e17 44e55 1c4e47 1d4e47 44217 1d4e57 1d4a57
endmodule
