// Logisim project bramka.circ as structural Verilog: 1 circuit, main circuit main
module main (
  input  [3:0] WE,
  input  Wl_WY,
  output [3:0] WY
);

  wire not_1_out;

  not not_1 (not_1_out, Wl_WY);
  assign WY = not_1_out ? 4'b1001 : 4'bz;  // Controlled_Buffer controlled_buffer_1
  assign WY = Wl_WY ? WE : 4'bz;  // Controlled_Buffer controlled_buffer_2
endmodule
