// Logisim project porównywacz.circ as structural Verilog: 1 circuit, main circuit main
module main (
  input  [1:0] in_1,
  input  [5:0] in_2,
  input  in_3,
  input  [2:0] Y,
  input  [2:0] X,
  input  in_6,
  output [3:0] out_7,
  output [5:0] out_8,
  output out_9,
  output out_10,
  output out_11
);

  wire and_3_out, clock_1_out, clock_2_out, clock_3_out, clock_4_out, clock_5_out, clock_6_out, clock_7_out,
       clock_8_out, comparator_2_eq, comparator_3_eq, comparator_4_eq, comparator_5_eq, comparator_6_eq,
       comparator_7_eq, comparator_8_eq, comparator_9_eq, controlled_buffer_2_out, controlled_buffer_3_out,
       H9, not_1_out, not_2_out, not_3_out, not_5_out, not_6_out, not_7_out, or_1_out, or_3_out, or_4_out,
       or_5_out, or_6_out, or_7_out, or_8_out, or_9_out, or_10_out, RZE, S1, S4, s_r_ff_3_q, s_r_ff_4_q, Z2,
       Z5;
  wire [1:0] and_2_out, counter_5_q, or_2_out;
  wire [1:1] K1;
  wire [2:0] uklad_zmiany_sterowania_z_3bit_na_5bit_1_out_x__3bit,
       uklad_zmiany_sterowania_z_3bit_na_5bit_1_out_xy_3bit;
  wire [3:0] adder_1_out, adder_2_out, adder_3_out, adder_4_out, adder_5_out, adder_6_out, adder_7_out,
       counter_6_q, counter_7_q, counter_8_q, counter_9_q, counter_10_q, counter_11_q, counter_12_q,
       counter_13_q;
  wire [4:0] X5, Y5;
  wire [5:0] controlled_buffer_4_out, D1, D2, D3, D4, D5, D6, D7, D8, ram_1_data;
  wire [6:0] counter_4_q;

  Pull_Resistor pull_resistor_1 (.node(Z2));
  assign Z2 = s_r_ff_3_q ? S1 : 1'bz;  // Controlled_Buffer controlled_buffer_1
  Clock clock_1 (.out(clock_1_out));
  Clock clock_2 (.out(clock_2_out));
  Clock clock_3 (.out(clock_3_out));
  Clock clock_4 (.out(clock_4_out));
  Clock clock_5 (.out(clock_5_out));
  not not_1 (not_1_out, in_3);
  assign controlled_buffer_2_out = not_1_out ? clock_1_out : 1'bz;  // Controlled_Buffer controlled_buffer_2
  S_R_Flip_Flop s_r_ff_1 (.S(S1), .clk(clock_2_out), .R(in_3), .Q(K1[1]));  // open: Qn, preset, reset, en
  not not_2 (not_2_out, Z2);
  assign controlled_buffer_3_out = not_2_out ? clock_3_out : 1'bz;  // Controlled_Buffer controlled_buffer_3
  S_R_Flip_Flop s_r_ff_2 (.S(H9), .clk(clock_4_out), .R(Z2), .Q(Z5));  // open: Qn, preset, reset, en
  S_R_Flip_Flop s_r_ff_3 (.S(in_3), .clk(clock_5_out), .R(H9), .Q(s_r_ff_3_q));  // open: Qn, preset, reset, en
  Pull_Resistor pull_resistor_2 (.node(controlled_buffer_2_out));
  nand nand_1 (S4, controlled_buffer_2_out, ~K1[1]);  // NAND_Gate
  Pull_Resistor pull_resistor_3 (.node(controlled_buffer_3_out));
  and and_1 (out_10, controlled_buffer_3_out, ~Z5);  // AND_Gate
  Counter #(.width(4), .max('h8), .trigger("falling")) counter_1 (
    .load(1'b1), .carry(S1), .clk(S4));  // open: D, count, Q, clr
  Counter #(.width(7), .max('h19), .trigger("falling")) counter_2 (
    .load(1'b1), .carry(H9), .clk(or_1_out));  // open: D, count, Q, clr
  or or_1 (or_1_out, Z2, out_9);
  Counter #(.width(4), .max('h4), .trigger("falling")) counter_3 (
    .load(1'b1), .carry(out_9), .clk(out_10));  // open: D, count, Q, clr
  assign and_2_out = in_1 & ~{2{K1[1]}};  // AND_Gate and_2, 2 bits wide
  assign or_2_out = and_2_out | counter_5_q;  // OR_Gate or_2, 2 bits wide
  and and_3 (and_3_out, ~K1[1], S4);  // AND_Gate
  Counter #(.width(7), .max('h7f), .trigger("falling")) counter_4 (
    .Q(counter_4_q), .clk(out_9));  // open: load, D, count, carry, clr
  Comparator #(.width(6)) comparator_1 (.a({Y, X}), .b(ram_1_data), .eq(out_11));  // open: gt, lt
  Counter #(.width(2), .max('h2), .ongoal("continue"), .trigger("falling")) counter_5 (
    .Q(counter_5_q), .clk(out_10), .clr(Z5));  // open: load, D, count, carry
  Clock clock_6 (.out(clock_6_out));
  not not_3 (not_3_out, and_3_out);
  Uklad_zwracania_pozycji_sasiednich_bitow uklad_zwracania_pozycji_sasiednich_bitow_1 (
    .Input_Y(X5), .Input_X(Y5), .LG(D1), .G(D2), .P(D4), .DP(D5), .D(D6), .LD(D7), .L(D8), .PG(D3));  // open: O_X, O_Y
  // Probe on counter_4_q
  RAM #(.addrWidth(2), .dataWidth(6), .bus("separate")) ram_1 (
    .addr(or_2_out), .din(in_2), .data(ram_1_data), .str(and_3_out), .sel(1'b1), .clk(clock_6_out), .clr(in_3));  // open: ld
  Clock clock_7 (.out(clock_7_out));
  S_R_Flip_Flop s_r_ff_4 (.S(out_9), .clk(clock_7_out), .R(Z2), .Q(s_r_ff_4_q));  // open: Qn, preset, reset, en
  not not_4 (RZE, s_r_ff_4_q);
  Counter #(.width(4), .max('hf), .trigger("falling")) counter_6 (
    .Q(counter_6_q), .clk(comparator_2_eq), .clr(or_3_out));  // open: load, D, count, carry
  Comparator #(.width(6)) comparator_2 (.a(D1), .b(ram_1_data), .eq(comparator_2_eq));  // open: gt, lt
  Counter #(.width(4), .max('hf), .trigger("falling")) counter_7 (
    .Q(counter_7_q), .clk(comparator_3_eq), .clr(or_4_out));  // open: load, D, count, carry
  Comparator #(.width(6)) comparator_3 (.a(D2), .b(ram_1_data), .eq(comparator_3_eq));  // open: gt, lt
  Counter #(.width(4), .max('hf), .trigger("falling")) counter_8 (
    .Q(counter_8_q), .clk(comparator_4_eq), .clr(or_5_out));  // open: load, D, count, carry
  Comparator #(.width(6)) comparator_4 (.a(D3), .b(ram_1_data), .eq(comparator_4_eq));  // open: gt, lt
  Counter #(.width(4), .max('hf), .trigger("falling")) counter_9 (
    .Q(counter_9_q), .clk(comparator_5_eq), .clr(or_6_out));  // open: load, D, count, carry
  Comparator #(.width(6)) comparator_5 (.a(D4), .b(ram_1_data), .eq(comparator_5_eq));  // open: gt, lt
  Counter #(.width(4), .max('hf), .trigger("falling")) counter_10 (
    .Q(counter_10_q), .clk(comparator_6_eq), .clr(or_7_out));  // open: load, D, count, carry
  Comparator #(.width(6)) comparator_6 (.a(D5), .b(ram_1_data), .eq(comparator_6_eq));  // open: gt, lt
  Counter #(.width(4), .max('hf), .trigger("falling")) counter_11 (
    .Q(counter_11_q), .clk(comparator_7_eq), .clr(or_8_out));  // open: load, D, count, carry
  Comparator #(.width(6)) comparator_7 (.a(D6), .b(ram_1_data), .eq(comparator_7_eq));  // open: gt, lt
  Counter #(.width(4), .max('hf), .trigger("falling")) counter_12 (
    .Q(counter_12_q), .clk(comparator_8_eq), .clr(or_9_out));  // open: load, D, count, carry
  Comparator #(.width(6)) comparator_8 (.a(D7), .b(ram_1_data), .eq(comparator_8_eq));  // open: gt, lt
  Counter #(.width(4), .max('hf), .trigger("falling")) counter_13 (
    .Q(counter_13_q), .clk(comparator_9_eq), .clr(or_10_out));  // open: load, D, count, carry
  Comparator #(.width(6)) comparator_9 (.a(D8), .b(ram_1_data), .eq(comparator_9_eq));  // open: gt, lt
  or or_3 (or_3_out, Z2, out_9);
  or or_4 (or_4_out, Z2, out_9);
  or or_5 (or_5_out, Z2, out_9);
  or or_6 (or_6_out, Z2, out_9);
  or or_7 (or_7_out, Z2, out_9);
  or or_8 (or_8_out, Z2, out_9);
  or or_9 (or_9_out, Z2, out_9);
  or or_10 (or_10_out, Z2, out_9);
  wypisanie_pul_main main_1 (.CLK(out_9), .\Wyjścia_X_pierwszy_Y_drugi__2x_5_bit ({Y5, X5}));
  Adder #(.width(4)) adder_1 (.a(counter_6_q), .b(counter_7_q), .out(adder_1_out));  // open: cin, cout
  Adder #(.width(4)) adder_2 (.a(counter_8_q), .b(counter_9_q), .out(adder_2_out));  // open: cin, cout
  Adder #(.width(4)) adder_3 (.a(counter_10_q), .b(counter_11_q), .out(adder_3_out));  // open: cin, cout
  Adder #(.width(4)) adder_4 (.a(counter_12_q), .b(counter_13_q), .out(adder_4_out));  // open: cin, cout
  Uklad_zmiany_sterowania_z_3bit_na_5bit uklad_zmiany_sterowania_z_3bit_na_5bit_1 (
    .IN_X_5bit(X5), .IN_Y_5bit(Y5), .OUT_X__3bit(uklad_zmiany_sterowania_z_3bit_na_5bit_1_out_x__3bit),
    .OUT_XY_3bit(uklad_zmiany_sterowania_z_3bit_na_5bit_1_out_xy_3bit));
  Adder #(.width(4)) adder_5 (.a(adder_1_out), .b(adder_2_out), .out(adder_5_out));  // open: cin, cout
  assign controlled_buffer_4_out = H9 ? {Y, X} : 6'bz;  // Controlled_Buffer controlled_buffer_4
  assign controlled_buffer_4_out = not_5_out ? {uklad_zmiany_sterowania_z_3bit_na_5bit_1_out_xy_3bit, uklad_zmiany_sterowania_z_3bit_na_5bit_1_out_x__3bit} : 6'bz;  // Controlled_Buffer controlled_buffer_5
  not not_5 (not_5_out, H9);
  Adder #(.width(4)) adder_6 (.a(adder_3_out), .b(adder_4_out), .out(adder_6_out));  // open: cin, cout
  Adder #(.width(4)) adder_7 (.a(adder_5_out), .b(adder_6_out), .out(adder_7_out));  // open: cin, cout
  not not_6 (not_6_out, Z5);
  Clock clock_8 (.out(clock_8_out));
  not not_7 (not_7_out, not_6_out);
  RAM #(.addrWidth(6), .dataWidth(4), .bus("separate")) ram_2 (
    .addr(controlled_buffer_4_out), .din(adder_7_out), .data(out_7), .str(not_6_out), .sel(1'b1),
    .clk(clock_8_out), .clr(in_3));  // open: ld

  assign out_8 = {Y, X};

  // Other names for the same wires on the sheet: K1[0] = K1[1]; S5 = K1[1]; S2 = in_3; WSPŁ[5:0] = {Y, X}; Z1 = out_9;
  //   Z4 = out_10
endmodule
