// Logisim project przezutnik_4_bitkowy.circ as structural Verilog: 1 circuit, main circuit main
module main (
  input  in_1,
  input  [3:0] in_2,
  output [3:0] out_3
);

  wire [3:0] d_ff_1_q, undriven;

  D_Flip_Flop d_ff_1 (.clk(in_1), .D(undriven[0]), .Q(d_ff_1_q[0]));  // open: Qn, preset, en, reset
  D_Flip_Flop d_ff_2 (.clk(in_1), .D(undriven[1]), .Q(d_ff_1_q[1]));  // open: Qn, preset, en, reset
  D_Flip_Flop d_ff_3 (.clk(in_1), .D(undriven[2]), .Q(d_ff_1_q[2]));  // open: Qn, preset, en, reset
  D_Flip_Flop d_ff_4 (.clk(in_1), .D(undriven[3]), .Q(d_ff_1_q[3]));  // open: Qn, preset, en, reset
  Register #(.width(4)) register_1 (.D(in_2), .Q(out_3), .clk(in_1));  // open: en, clr
endmodule
