// Logisim project ukadtest4.circ as structural Verilog: 1 circuit, main circuit main
module main (
  input  [3:0] in_1,
  input  [3:0] in_2,
  input  [3:0] in_3,
  input  [3:0] in_4,
  input  [3:0] in_5,
  input  [3:0] in_6,
  input  [3:0] in_7,
  input  [3:0] in_8,
  input  [3:0] in_9,
  input  [3:0] in_10,
  input  [3:0] in_11,
  input  [3:0] in_12,
  input  [3:0] in_13,
  input  [3:0] in_14,
  input  [3:0] in_15,
  input  [3:0] in_16,
  input  [3:0] in_17,
  input  [3:0] in_18,
  input  [3:0] in_19,
  input  [3:0] in_20,
  input  [3:0] in_21,
  input  [3:0] in_22,
  input  [3:0] in_23,
  input  [3:0] in_24,
  input  [3:0] in_25,
  input  [24:0] \pamięć ,
  input  [24:0] wy,
  input  przycisk,
  input  RESET,
  output [30:0] out_30,
  output [30:0] out_31,
  output [30:0] out_32,
  output [30:0] out_33,
  output [30:0] out_34,
  output [30:0] out_35,
  output [30:0] out_36,
  output [30:0] out_37,
  output [30:0] out_38,
  output [30:0] out_39,
  output [30:0] out_40,
  output [30:0] out_41,
  output [30:0] out_42,
  output [30:0] out_43,
  output [30:0] out_44,
  output [30:0] out_45,
  output [30:0] out_46,
  output [30:0] out_47,
  output [30:0] out_48,
  output [30:0] out_49,
  output [30:0] out_50,
  output [30:0] out_51,
  output [30:0] out_52,
  output [30:0] out_53,
  output [30:0] out_54,
  output [30:0] out_55,
  output [30:0] out_56,
  output [30:0] out_57,
  output [30:0] out_58,
  output [30:0] out_59,
  output [30:0] out_60,
  output [24:0] we
);

  wire d_ff_1_q, d_ff_2_q, d_ff_3_q, d_ff_4_q, d_ff_5_q, d_ff_6_q, d_ff_7_q, d_ff_8_q, d_ff_9_q, d_ff_10_q,
       d_ff_11_q, d_ff_12_q, d_ff_13_q, d_ff_14_q, d_ff_15_q, d_ff_16_q, d_ff_17_q, d_ff_18_q, d_ff_19_q,
       d_ff_20_q, d_ff_21_q, d_ff_22_q, d_ff_23_q, d_ff_24_q, d_ff_25_q, not_2_out, or_1_out, or_2_out,
       or_3_out, or_4_out, or_5_out, or_6_out, or_7_out, or_8_out, or_9_out, or_10_out, or_11_out, or_12_out,
       or_13_out, or_14_out, or_15_out, or_16_out, or_17_out, or_18_out, or_19_out, or_20_out, or_21_out,
       or_22_out, or_23_out, or_24_out, or_25_out;
  wire [3:0] controlled_buffer_1_out, controlled_buffer_2_out, controlled_buffer_3_out,
       controlled_buffer_5_out, controlled_buffer_6_out, controlled_buffer_7_out, controlled_buffer_8_out,
       controlled_buffer_9_out, controlled_buffer_10_out, controlled_buffer_11_out, controlled_buffer_12_out,
       controlled_buffer_13_out, controlled_buffer_14_out, controlled_buffer_15_out,
       controlled_buffer_16_out, controlled_buffer_17_out, controlled_buffer_18_out,
       controlled_buffer_19_out, controlled_buffer_20_out, controlled_buffer_21_out,
       controlled_buffer_22_out, controlled_buffer_23_out, controlled_buffer_24_out,
       controlled_buffer_25_out, controlled_buffer_26_out;

  assign we = ~\pamięć ;  // NOT_Gate not_1, 25 bits wide
  D_Flip_Flop d_ff_1 (.clk(wy[0]), .D(1'b1), .Q(d_ff_1_q), .reset(RESET));  // open: Qn, preset, en
  D_Flip_Flop d_ff_2 (.clk(wy[1]), .D(1'b1), .Q(d_ff_2_q), .reset(RESET));  // open: Qn, preset, en
  D_Flip_Flop d_ff_3 (.clk(wy[2]), .D(1'b1), .Q(d_ff_3_q), .reset(RESET));  // open: Qn, preset, en
  D_Flip_Flop d_ff_4 (.clk(wy[3]), .D(1'b1), .Q(d_ff_4_q), .reset(RESET));  // open: Qn, preset, en
  D_Flip_Flop d_ff_5 (.clk(wy[4]), .D(1'b1), .Q(d_ff_5_q), .reset(RESET));  // open: Qn, preset, en
  D_Flip_Flop d_ff_6 (.clk(wy[5]), .D(1'b1), .Q(d_ff_6_q), .reset(RESET));  // open: Qn, preset, en
  D_Flip_Flop d_ff_7 (.clk(wy[6]), .D(1'b1), .Q(d_ff_7_q), .reset(RESET));  // open: Qn, preset, en
  D_Flip_Flop d_ff_8 (.clk(wy[7]), .D(1'b1), .Q(d_ff_8_q), .reset(RESET));  // open: Qn, preset, en
  D_Flip_Flop d_ff_9 (.clk(wy[8]), .D(1'b1), .Q(d_ff_9_q), .reset(RESET));  // open: Qn, preset, en
  D_Flip_Flop d_ff_10 (.clk(wy[9]), .D(1'b1), .Q(d_ff_10_q), .reset(RESET));  // open: Qn, preset, en
  D_Flip_Flop d_ff_11 (.clk(wy[10]), .D(1'b1), .Q(d_ff_11_q), .reset(RESET));  // open: Qn, preset, en
  D_Flip_Flop d_ff_12 (.clk(wy[11]), .D(1'b1), .Q(d_ff_12_q), .reset(RESET));  // open: Qn, preset, en
  D_Flip_Flop d_ff_13 (.clk(wy[12]), .D(1'b1), .Q(d_ff_13_q), .reset(RESET));  // open: Qn, preset, en
  D_Flip_Flop d_ff_14 (.clk(wy[13]), .D(1'b1), .Q(d_ff_14_q), .reset(RESET));  // open: Qn, preset, en
  D_Flip_Flop d_ff_15 (.clk(wy[14]), .D(1'b1), .Q(d_ff_15_q), .reset(RESET));  // open: Qn, preset, en
  D_Flip_Flop d_ff_16 (.clk(wy[15]), .D(1'b1), .Q(d_ff_16_q), .reset(RESET));  // open: Qn, preset, en
  D_Flip_Flop d_ff_17 (.clk(wy[16]), .D(1'b1), .Q(d_ff_17_q), .reset(RESET));  // open: Qn, preset, en
  D_Flip_Flop d_ff_18 (.clk(wy[17]), .D(1'b1), .Q(d_ff_18_q), .reset(RESET));  // open: Qn, preset, en
  D_Flip_Flop d_ff_19 (.clk(wy[18]), .D(1'b1), .Q(d_ff_19_q), .reset(RESET));  // open: Qn, preset, en
  D_Flip_Flop d_ff_20 (.clk(wy[19]), .D(1'b1), .Q(d_ff_20_q), .reset(RESET));  // open: Qn, preset, en
  D_Flip_Flop d_ff_21 (.clk(wy[20]), .D(1'b1), .Q(d_ff_21_q), .reset(RESET));  // open: Qn, preset, en
  D_Flip_Flop d_ff_22 (.clk(wy[21]), .D(1'b1), .Q(d_ff_22_q), .reset(RESET));  // open: Qn, preset, en
  D_Flip_Flop d_ff_23 (.clk(wy[22]), .D(1'b1), .Q(d_ff_23_q), .reset(RESET));  // open: Qn, preset, en
  D_Flip_Flop d_ff_24 (.clk(wy[23]), .D(1'b1), .Q(d_ff_24_q), .reset(RESET));  // open: Qn, preset, en
  D_Flip_Flop d_ff_25 (.clk(wy[24]), .D(1'b1), .Q(d_ff_25_q), .reset(RESET));  // open: Qn, preset, en
  or or_1 (or_1_out, d_ff_1_q, przycisk);
  or or_2 (or_2_out, d_ff_2_q, przycisk);
  or or_3 (or_3_out, d_ff_3_q, przycisk);
  or or_4 (or_4_out, d_ff_4_q, przycisk);
  or or_5 (or_5_out, d_ff_5_q, przycisk);
  or or_6 (or_6_out, d_ff_6_q, przycisk);
  or or_7 (or_7_out, d_ff_7_q, przycisk);
  or or_8 (or_8_out, d_ff_8_q, przycisk);
  or or_9 (or_9_out, d_ff_9_q, przycisk);
  or or_10 (or_10_out, d_ff_10_q, przycisk);
  or or_11 (or_11_out, d_ff_11_q, przycisk);
  or or_12 (or_12_out, d_ff_12_q, przycisk);
  or or_13 (or_13_out, d_ff_13_q, przycisk);
  or or_14 (or_14_out, d_ff_14_q, przycisk);
  or or_15 (or_15_out, d_ff_15_q, przycisk);
  or or_16 (or_16_out, d_ff_16_q, przycisk);
  or or_17 (or_17_out, d_ff_17_q, przycisk);
  or or_18 (or_18_out, d_ff_18_q, przycisk);
  or or_19 (or_19_out, d_ff_19_q, przycisk);
  or or_20 (or_20_out, d_ff_20_q, przycisk);
  or or_21 (or_21_out, d_ff_21_q, przycisk);
  or or_22 (or_22_out, d_ff_22_q, przycisk);
  or or_23 (or_23_out, d_ff_23_q, przycisk);
  or or_24 (or_24_out, d_ff_24_q, przycisk);
  or or_25 (or_25_out, d_ff_25_q, przycisk);
  not not_2 (not_2_out, or_1_out);
  assign controlled_buffer_1_out = not_2_out ? 4'b1001 : 4'bz;  // Controlled_Buffer controlled_buffer_1
  assign controlled_buffer_2_out = or_11_out ? in_11 : 4'bz;  // Controlled_Buffer controlled_buffer_2
  assign controlled_buffer_3_out = or_12_out ? in_12 : 4'bz;  // Controlled_Buffer controlled_buffer_3
  assign controlled_buffer_1_out = or_1_out ? in_1 : 4'bz;  // Controlled_Buffer controlled_buffer_4
  assign controlled_buffer_5_out = or_2_out ? in_2 : 4'bz;  // Controlled_Buffer controlled_buffer_5
  assign controlled_buffer_6_out = or_3_out ? in_3 : 4'bz;  // Controlled_Buffer controlled_buffer_6
  assign controlled_buffer_7_out = or_4_out ? in_4 : 4'bz;  // Controlled_Buffer controlled_buffer_7
  assign controlled_buffer_8_out = or_13_out ? in_13 : 4'bz;  // Controlled_Buffer controlled_buffer_8
  assign controlled_buffer_9_out = or_14_out ? in_14 : 4'bz;  // Controlled_Buffer controlled_buffer_9
  assign controlled_buffer_10_out = or_15_out ? in_15 : 4'bz;  // Controlled_Buffer controlled_buffer_10
  assign controlled_buffer_11_out = or_5_out ? in_5 : 4'bz;  // Controlled_Buffer controlled_buffer_11
  assign controlled_buffer_12_out = or_6_out ? in_6 : 4'bz;  // Controlled_Buffer controlled_buffer_12
  assign controlled_buffer_13_out = or_7_out ? in_7 : 4'bz;  // Controlled_Buffer controlled_buffer_13
  assign controlled_buffer_14_out = or_8_out ? in_8 : 4'bz;  // Controlled_Buffer controlled_buffer_14
  assign controlled_buffer_15_out = or_16_out ? in_16 : 4'bz;  // Controlled_Buffer controlled_buffer_15
  assign controlled_buffer_16_out = or_17_out ? in_17 : 4'bz;  // Controlled_Buffer controlled_buffer_16
  assign controlled_buffer_17_out = or_18_out ? in_18 : 4'bz;  // Controlled_Buffer controlled_buffer_17
  assign controlled_buffer_18_out = or_19_out ? in_19 : 4'bz;  // Controlled_Buffer controlled_buffer_18
  assign controlled_buffer_19_out = or_9_out ? in_9 : 4'bz;  // Controlled_Buffer controlled_buffer_19
  assign controlled_buffer_20_out = or_10_out ? in_10 : 4'bz;  // Controlled_Buffer controlled_buffer_20
  assign controlled_buffer_21_out = or_20_out ? in_20 : 4'bz;  // Controlled_Buffer controlled_buffer_21
  assign controlled_buffer_22_out = or_21_out ? in_21 : 4'bz;  // Controlled_Buffer controlled_buffer_22
  assign controlled_buffer_23_out = or_22_out ? in_22 : 4'bz;  // Controlled_Buffer controlled_buffer_23
  assign controlled_buffer_24_out = or_23_out ? in_23 : 4'bz;  // Controlled_Buffer controlled_buffer_24
  assign controlled_buffer_25_out = or_24_out ? in_24 : 4'bz;  // Controlled_Buffer controlled_buffer_25
  assign controlled_buffer_26_out = or_25_out ? in_25 : 4'bz;  // Controlled_Buffer controlled_buffer_26
  \Układ_wyświetlania_3_main  main_1 (
    .in_1({31{1'b0}}), ._15(controlled_buffer_1_out), ._14(controlled_buffer_5_out),
    ._13(controlled_buffer_6_out), ._12(controlled_buffer_7_out), ._11(controlled_buffer_11_out),
    .in_7(controlled_buffer_12_out), .in_8(controlled_buffer_13_out), .in_9(controlled_buffer_14_out),
    .in_10(controlled_buffer_19_out), .in_11(controlled_buffer_20_out), .in_12(controlled_buffer_2_out),
    .in_13(controlled_buffer_3_out), .in_14(controlled_buffer_8_out), .in_15(controlled_buffer_9_out),
    .in_16(controlled_buffer_10_out), .in_17(\pamięć ), .in_18(controlled_buffer_15_out),
    .in_19(controlled_buffer_16_out), .in_20(controlled_buffer_17_out), .in_21(controlled_buffer_18_out),
    .in_22(controlled_buffer_21_out), .in_23(controlled_buffer_22_out), .in_24(controlled_buffer_23_out),
    .in_25(controlled_buffer_24_out), .in_26(controlled_buffer_25_out), .in_27(controlled_buffer_26_out),
    .out_28(out_30), .out_29(out_31), .out_30(out_32), .out_31(out_33), .out_32(out_34), .out_33(out_35),
    .out_34(out_36), .out_35(out_37), .out_36(out_38), .out_37(out_39), .out_38(out_40), .out_39(out_41),
    .out_40(out_42), .out_41(out_43), .out_42(out_44), .out_43(out_45), .out_44(out_46), .out_45(out_47),
    .out_46(out_48), .out_47(out_49), .out_48(out_50), .out_49(out_51), .out_50(out_52), .out_51(out_53),
    .out_52(out_54), .out_53(out_55), .out_54(out_56), .out_55(out_57), .out_56(out_58), .out_57(out_59),
    .out_58(out_60));

  // Other names for the same wires on the sheet: R1 = RESET
endmodule
