// Logisim project Maszyna_Los_XY22.circ as structural Verilog: 1 circuit, main circuit main
module main (
  input  START,
  output [1:0] out_2,
  output [5:0] out_3
);

  wire and_1_out, and_2_out, and_3_out, clock_1_out, clock_2_out, clock_3_out, clock_4_out, clock_5_out,
       clock_6_out, not_1_out, not_2_out, pull_resistor_1_node, S1, S4, S5, xor_1_out;
  wire [2:0] counter_3_q, counter_4_q;

  Clock clock_1 (.out(clock_1_out));
  Clock clock_2 (.out(clock_2_out));
  not not_1 (not_1_out, START);
  S_R_Flip_Flop s_r_ff_1 (.S(S1), .clk(clock_2_out), .R(START), .Q(S5));  // open: Qn, preset, reset, en
  Pull_Resistor pull_resistor_1 (.node(pull_resistor_1_node));
  nand nand_1 (S4, clock_1_out, ~S5);  // NAND_Gate
  Counter #(.width(4), .max('h4), .trigger("falling")) counter_1 (
    .load(1'b1), .carry(S1), .clk(pull_resistor_1_node));  // open: D, count, Q, clr
  assign pull_resistor_1_node = not_1_out ? S4 : 1'bz;  // Controlled_Buffer controlled_buffer_1
  and and_1 (and_1_out, S5, clock_3_out);
  Clock clock_3 (.out(clock_3_out));
  Clock #(.highDuration(2), .lowDuration(3)) clock_4 (.out(clock_4_out));
  Clock clock_5 (.out(clock_5_out));
  Counter #(.width(2), .max('h3), .ongoal("continue")) counter_2 (
    .Q(out_2), .clk(xor_1_out));  // open: load, D, count, carry, clr
  xor xor_1 (xor_1_out, and_2_out, and_1_out);
  and and_2 (and_2_out, ~S5, S4);  // AND_Gate
  Counter #(.width(3), .max('h4), .trigger("falling")) counter_3 (
    .Q(counter_3_q), .clk(clock_4_out));  // open: load, D, count, carry, clr
  Counter #(.width(3), .max('h4), .trigger("falling")) counter_4 (
    .Q(counter_4_q), .clk(clock_5_out));  // open: load, D, count, carry, clr
  and and_3 (and_3_out, ~S5, S4);  // AND_Gate
  Clock clock_6 (.out(clock_6_out));
  not not_2 (not_2_out, and_3_out);
  RAM #(.addrWidth(2), .dataWidth(6), .bus("separate")) ram_1 (
    .addr(out_2), .din({counter_4_q, counter_3_q}), .data(out_3), .str(and_3_out), .sel(1'b1),
    .clk(clock_6_out), .ld(not_2_out), .clr(START));

  // Other names for the same wires on the sheet: M1[1:0] = out_2; S2 = START

  // Notes on the sheet:
  //   Bloki losujące zostały zastąpione przez zwykłe liczniki
  //   Było to konieczne ponieważ po pewnych modyfikacjach zacząły losować te same liczby lub powtarzały się pewne sekwencje :(
  //   Liczniki mają gorszą pseudolosowość ale dla zwykłego użytkownika grającego w sapera nie zrobi to różnicy 
endmodule
