// Logisim project Logika.circ as structural Verilog: 2 circuits, main circuit Komparator 1bit
module Komparator_1bit (
  input  A,
  input  B,
  input  in_3,
  output A___B,
  output A___B_2,
  output A___B_3
);

  wire nand_1_out, nand_2_out, nand_3_out, not_1_out, not_2_out;

  not not_1 (not_1_out, A);
  not not_2 (not_2_out, B);
  nand nand_1 (nand_1_out, A, not_2_out, in_3);
  nand nand_2 (nand_2_out, not_1_out, B, in_3);
  nand nand_3 (nand_3_out, nand_1_out, in_3, nand_2_out);
  not not_3 (A___B, nand_1_out);
  not not_4 (A___B_2, nand_2_out);
  not not_5 (A___B_3, nand_3_out);
endmodule

module Komparator_7bit_do_sterowania (
  input  [6:0] A,
  input  [6:0] B,
  output _1_oznacza_ze_jest_rowne
);

  wire komparator_1bit_1_a___b_3, komparator_1bit_2_a___b_3, komparator_1bit_3_a___b_3,
       komparator_1bit_4_a___b_3, komparator_1bit_5_a___b_3, komparator_1bit_6_a___b_3;

  Komparator_1bit komparator_1bit_1 (
    .A(A[6]), .B(B[6]), .in_3(1'b1), .A___B_3(komparator_1bit_1_a___b_3));  // open: A___B, A___B_2
  Komparator_1bit komparator_1bit_2 (
    .A(A[5]), .B(B[5]), .in_3(komparator_1bit_1_a___b_3), .A___B_3(komparator_1bit_2_a___b_3));  // open: A___B, A___B_2
  Komparator_1bit komparator_1bit_3 (
    .A(A[4]), .B(B[4]), .in_3(komparator_1bit_2_a___b_3), .A___B_3(komparator_1bit_3_a___b_3));  // open: A___B, A___B_2
  Komparator_1bit komparator_1bit_4 (
    .A(A[3]), .B(B[3]), .in_3(komparator_1bit_3_a___b_3), .A___B_3(komparator_1bit_4_a___b_3));  // open: A___B, A___B_2
  Komparator_1bit komparator_1bit_5 (
    .A(A[2]), .B(B[2]), .in_3(komparator_1bit_4_a___b_3), .A___B_3(komparator_1bit_5_a___b_3));  // open: A___B, A___B_2
  Komparator_1bit komparator_1bit_6 (
    .A(A[1]), .B(B[1]), .in_3(komparator_1bit_5_a___b_3), .A___B_3(komparator_1bit_6_a___b_3));  // open: A___B, A___B_2
  Komparator_1bit komparator_1bit_7 (
    .A(A[0]), .B(B[0]), .in_3(komparator_1bit_6_a___b_3), .A___B_3(_1_oznacza_ze_jest_rowne));  // open: A___B, A___B_2
endmodule
