// Logisim project SAPER.circ as structural Verilog: 1 circuit, main circuit main
module main (
  input  [3:0] in_1,
  input  [3:0] in_2,
  input  [3:0] in_3,
  input  [3:0] in_4,
  input  [3:0] in_5,
  input  [3:0] in_6,
  input  [3:0] in_7,
  input  [3:0] in_8,
  input  [3:0] in_9,
  input  [3:0] in_10,
  input  [3:0] in_11,
  input  [3:0] in_12,
  input  [3:0] in_13,
  input  [3:0] in_14,
  input  [3:0] in_15,
  input  [3:0] in_16,
  input  [3:0] in_17,
  input  [3:0] in_18,
  input  [3:0] in_19,
  input  [3:0] in_20,
  input  [3:0] in_21,
  input  [3:0] in_22,
  input  [3:0] in_23,
  input  [3:0] in_24,
  input  [3:0] in_25,
  output [3:0] out_26,
  output koniec_gry
);

  wire and_1_out, clock_1_out, main_2_out_8, START_out, sterowanie_z_klawiatury_1_przemiesc_kursor;
  wire [1:0] main_1_out_2;
  wire [2:0] sterowanie_z_klawiatury_1__3_a_4_s_1_d_6_w_5_enter;
  wire [4:0] X1, Y1;
  wire [5:0] main_1_out_3;
  wire [6:0] keyboard_1_data;
  wire [24:0] controlled_buffer_2_out, main_3_p27, main_3_p28, rom_1_data;
  wire [30:0] main_3_p30, main_3_p31, main_3_p32, main_3_p33, main_3_p34, main_3_p35, main_3_p36, main_3_p37,
       main_3_p38, main_3_p39, main_3_p40, main_3_p41, main_3_p42, main_3_p43, main_3_p44, main_3_p45,
       main_3_p46, main_3_p47, main_3_p48, main_3_p49, main_3_p50, main_3_p51, main_3_p52, main_3_p53,
       main_3_p54, main_3_p55, main_3_p56, main_3_p57, main_3_p58, main_3_p59, main_3_p60;

  Maszyna_Los_XY22_main main_1 (.START(START_out), .out_3(main_1_out_3), .out_2(main_1_out_2));  // open: S5, S4
  \porównywacz_main  main_2 (
    .in_1(main_1_out_2), .in_2(main_1_out_3), .in_3(START_out), .in_6(and_1_out), .out_7(out_26), .in_4(X1),
    .in_5(Y1), .out_8(main_2_out_8));
  Pull_Resistor pull_resistor_1 (.node(main_2_out_8));
  Sterowanie_z_klawiatury sterowanie_z_klawiatury_1 (
    .\input (keyboard_1_data), ._3_a_4_s_1_d_6_w_5_enter(sterowanie_z_klawiatury_1__3_a_4_s_1_d_6_w_5_enter),
    .przemiesc_kursor(sterowanie_z_klawiatury_1_przemiesc_kursor));
  S_R_Flip_Flop #(.trigger("high")) s_r_ff_1 (
    .S(main_2_out_8), .clk(1'b1), .R(1'b0), .Q(koniec_gry));  // open: Qn, preset, reset, en
  and and_1 (and_1_out, sterowanie_z_klawiatury_1__3_a_4_s_1_d_6_w_5_enter[0], sterowanie_z_klawiatury_1__3_a_4_s_1_d_6_w_5_enter[2]);
  Clock clock_1 (.out(clock_1_out));
  Keyboard #(.buflen(1)) keyboard_1 (.clk(clock_1_out), .data(keyboard_1_data));  // open: re, clr, avail
  uklad_zwracajacy_pozycje uklad_zwracajacy_pozycje_1 (
    .Sterowanie(sterowanie_z_klawiatury_1__3_a_4_s_1_d_6_w_5_enter),
    .Move(sterowanie_z_klawiatury_1_przemiesc_kursor), .Poz_X(X1), .Poz_Y(Y1));
  Button START (.out(START_out));
  ROM #(.addrWidth(10), .dataWidth(25)) rom_1 (.addr({Y1, X1}), .data(rom_1_data));  // open: sel
  // ukadtest4_main main_3: pin names not known; wires that end beside it: in_1, in_2, in_3, in_4, in_5, in_6, in_7, in_8, in_9, in_10, in_11, in_12, in_13, in_14, in_15, in_16, in_17, in_18, in_19, in_20, in_21, in_22, in_23, in_24, in_25, START_out, main_3_p27, main_3_p28, rom_1_data, main_3_p30, main_3_p31, main_3_p32, main_3_p33, main_3_p34, main_3_p35, main_3_p36, main_3_p37, main_3_p38, main_3_p39, main_3_p40, main_3_p41, main_3_p42, main_3_p43, main_3_p44, main_3_p45, main_3_p46, main_3_p47, main_3_p48, main_3_p49, main_3_p50, main_3_p51, main_3_p52, main_3_p53, main_3_p54, main_3_p55, main_3_p56, main_3_p57, main_3_p58, main_3_p59, main_3_p60
  Pull_Resistor pull_resistor_2 (.node(main_3_p27));
  assign main_3_p27 = and_1_out ? controlled_buffer_2_out : 25'bz;  // Controlled_Buffer controlled_buffer_1
  assign controlled_buffer_2_out = and_1_out ? main_3_p28 : 25'bz;  // Controlled_Buffer controlled_buffer_2
  DotMatrix #(.inputtype("row"), .matrixcols(31), .matrixrows(31)) dotmatrix_1 (
    .row0(main_3_p30), .row1(main_3_p31), .row2(main_3_p32), .row3(main_3_p33), .row4(main_3_p34),
    .row5(main_3_p35), .row6(main_3_p36), .row7(main_3_p37), .row8(main_3_p38), .row9(main_3_p39),
    .row10(main_3_p40), .row11(main_3_p41), .row12(main_3_p42), .row13(main_3_p43), .row14(main_3_p44),
    .row15(main_3_p45), .row16(main_3_p46), .row17(main_3_p47), .row18(main_3_p48), .row19(main_3_p49),
    .row20(main_3_p50), .row21(main_3_p51), .row22(main_3_p52), .row23(main_3_p53), .row24(main_3_p54),
    .row25(main_3_p55), .row26(main_3_p56), .row27(main_3_p57), .row28(main_3_p58), .row29(main_3_p59),
    .row30(main_3_p60));

  // Notes on the sheet:
  //   contents of rom_1 (hex, n*v repeats v):
  //   33*0 1efffff 1dfffff 0 1bfffff 0 0 0 17fffff 7*0 ffffff 16*0 1ff7fff 1feffff 0 1fdffff 0 0 0 1fbffff
  //   7*0 1f7ffff 48*0 1fffbff 1fff7ff 0 1ffefff 0 0 0 1ffdfff 7*0 1ffbfff 111*0 1fffdff 1ffffdf 1ffffbf 0
  //   1ffff7f 0 0 0 1fffeff 7*0 1fffdff 1ffffdf 1ffffbf 0 1ffff7f 236*0 1fffffe 1fffffd 0 1fffffb 0 0 0
  //   1fffff7 7*0 1ffffef
endmodule
