// Logisim project 4bityx_1.circ as structural Verilog: 1 circuit, main circuit main
module main (
  input  Koniec,
  input  ENTER,
  input  Focus,
  input  RESET,
  input  [3:0] \WEJŚCIE ,
  output [3:0] \WYJŚCIE 
);

  wire and_1_out, and_2_out, not_1_out, not_2_out, or_1_out, or_2_out, or_3_out;
  wire [3:0] controlled_buffer_1_out, controlled_buffer_3_out;

  and and_1 (and_1_out, ENTER, Focus);
  and and_2 (and_2_out, Koniec, Focus);
  or or_1 (or_1_out, and_1_out, RESET);
  or or_2 (or_2_out, Koniec, RESET);
  not not_1 (not_1_out, or_2_out);
  assign controlled_buffer_1_out = not_1_out ? \WEJŚCIE  : 4'bz;  // Controlled_Buffer controlled_buffer_1
  assign controlled_buffer_1_out = or_2_out ? controlled_buffer_3_out : 4'bz;  // Controlled_Buffer controlled_buffer_2
  not not_2 (not_2_out, and_2_out);
  assign controlled_buffer_3_out = not_2_out ? 4'b1001 : 4'bz;  // Controlled_Buffer controlled_buffer_3
  assign controlled_buffer_3_out = and_2_out ? 4'b1010 : 4'bz;  // Controlled_Buffer controlled_buffer_4
  or or_3 (or_3_out, or_1_out, and_2_out);
  Register #(.width(4), .trigger("high")) register_1 (
    .D(controlled_buffer_1_out), .Q(\WYJŚCIE ), .clk(or_3_out));  // open: en, clr
endmodule
