// Logisim project BOOMBOX.circ as structural Verilog: 1 circuit, main circuit main
module main (
  input  [1:0] EGAR,
  input  [5:0] DANE,
  input  START,
  input  [5:0] \wspł ,
  input  in_5,
  input  ENTER,
  output WYBUCH
);

  wire and_2_out, clock_1_out, clock_2_out, clock_3_out, clock_4_out, clock_5_out, clock_6_out, clock_7_out,
       comparator_1_eq, controlled_buffer_2_out, not_1_out, not_2_out, not_3_out, pull_resistor_1_node, S1,
       S4, s_r_ff_3_q, Z1, Z4, Z5;
  wire [1:0] and_1_out, counter_2_q, or_1_out;
  wire [1:1] K1;
  wire [5:0] controlled_buffer_3_out, ram_1_data;

  not not_1 (not_1_out, START);
  Clock clock_1 (.out(clock_1_out));
  Clock clock_2 (.out(clock_2_out));
  Pull_Resistor pull_resistor_1 (.node(pull_resistor_1_node));
  assign pull_resistor_1_node = not_1_out ? clock_1_out : 1'bz;  // Controlled_Buffer controlled_buffer_1
  S_R_Flip_Flop s_r_ff_1 (.S(S1), .clk(clock_2_out), .R(START), .Q(K1[1]));  // open: Qn, preset, reset, en
  nand nand_1 (S4, pull_resistor_1_node, ~K1[1]);  // NAND_Gate
  Counter #(.width(4), .max('h8), .trigger("falling")) counter_1 (
    .load(1'b1), .carry(S1), .clk(S4));  // open: D, count, Q, clr
  Clock clock_3 (.out(clock_3_out));
  Clock clock_4 (.out(clock_4_out));
  assign and_1_out = EGAR & ~{2{K1[1]}};  // AND_Gate and_1, 2 bits wide
  assign or_1_out = and_1_out | counter_2_q;  // OR_Gate or_1, 2 bits wide
  and and_2 (and_2_out, ~K1[1], S4);  // AND_Gate
  not not_2 (not_2_out, ENTER);
  assign controlled_buffer_2_out = not_2_out ? clock_3_out : 1'bz;  // Controlled_Buffer controlled_buffer_2
  S_R_Flip_Flop s_r_ff_2 (.S(Z1), .clk(clock_4_out), .R(ENTER), .Q(Z5));  // open: Qn, preset, reset, en
  Counter #(.width(2), .max('h2), .ongoal("continue"), .trigger("falling")) counter_2 (
    .Q(counter_2_q), .clk(Z4), .clr(Z5));  // open: load, D, count, carry
  Clock clock_5 (.out(clock_5_out));
  not not_3 (not_3_out, and_2_out);
  Pull_Resistor pull_resistor_2 (.node(controlled_buffer_2_out));
  and and_3 (Z4, controlled_buffer_2_out, ~Z5);  // AND_Gate
  RAM #(.addrWidth(2), .dataWidth(6), .bus("separate")) ram_1 (
    .addr(or_1_out), .din(DANE), .data(ram_1_data), .str(and_2_out), .sel(1'b1), .clk(clock_5_out),
    .clr(START));  // open: ld
  Clock clock_6 (.out(clock_6_out));
  Counter #(.width(4), .max('h4), .trigger("falling")) counter_3 (
    .load(1'b1), .carry(Z1), .clk(Z4));  // open: D, count, Q, clr
  assign controlled_buffer_3_out = s_r_ff_3_q ? ram_1_data : 6'bz;  // Controlled_Buffer controlled_buffer_3
  S_R_Flip_Flop s_r_ff_3 (.S(ENTER), .clk(clock_6_out), .R(Z1), .Q(s_r_ff_3_q));  // open: Qn, preset, reset, en
  Comparator #(.width(6), .mode("unsigned")) comparator_1 (
    .a(controlled_buffer_3_out), .b(\wspł ), .eq(comparator_1_eq));  // open: gt, lt
  Pull_Resistor pull_resistor_3 (.node(comparator_1_eq));
  Clock clock_7 (.out(clock_7_out));
  S_R_Flip_Flop s_r_ff_4 (.S(comparator_1_eq), .clk(clock_7_out), .R(in_5), .Q(WYBUCH));  // open: Qn, preset, reset, en

  // Other names for the same wires on the sheet: K1[0] = K1[1]; S5 = K1[1]; S2 = START; Z2 = ENTER
endmodule
