// Logisim project SAPER2.circ as structural Verilog: 1 circuit, main circuit main
module main (
  input  [4:0] x,
  input  [4:0] Y,
  input  [3:0] WYJSCIE,
  input  START,
  input  [24:0] PAMIEC,
  input  ENTER,
  input  lose,
  output [30:0] out_8,
  output [30:0] out_9,
  output [30:0] out_10,
  output [30:0] out_11,
  output [30:0] out_12,
  output [30:0] out_13,
  output [30:0] out_14,
  output [30:0] out_15,
  output [30:0] out_16,
  output [30:0] out_17,
  output [30:0] out_18,
  output [30:0] out_19,
  output [30:0] out_20,
  output [30:0] out_21,
  output [30:0] out_22,
  output [30:0] out_23,
  output [30:0] out_24,
  output [30:0] out_25,
  output [30:0] out_26,
  output [30:0] out_27,
  output [30:0] out_28,
  output [30:0] out_29,
  output [30:0] out_30,
  output [30:0] out_31,
  output [30:0] out_32,
  output [30:0] out_33,
  output [30:0] out_34,
  output [30:0] out_35,
  output [30:0] out_36,
  output [30:0] out_37,
  output [30:0] out_38,
  output Win
);

  wire _11, _12, _13, _14, _15, _21, _22, _23, _24, _25, _31, _32, _33, _34, _35, _41, _42, _43, _44, _45,
       _51, _52, _53, _54, _55, controlled_buffer_2_out, main_26_win, not_2_out, pull_resistor_1_node;
  wire [2:0] uklad_zmiany_sterowania_z_3bit_na_5bit_1_out_x__3bit,
       uklad_zmiany_sterowania_z_3bit_na_5bit_1_out_xy_3bit;
  wire [3:0] \main_1_wyjście , \main_2_wyjście , \main_3_wyjście , \main_4_wyjście , \main_5_wyjście ,
       \main_6_wyjście , \main_7_wyjście , \main_8_wyjście , \main_9_wyjście , \main_10_wyjście ,
       \main_11_wyjście , \main_12_wyjście , \main_13_wyjście , \main_14_wyjście , \main_15_wyjście ,
       \main_16_wyjście , \main_17_wyjście , \main_18_wyjście , \main_19_wyjście , \main_20_wyjście ,
       \main_21_wyjście , \main_22_wyjście , \main_23_wyjście , \main_24_wyjście , \main_25_wyjście ,
       uklad_przesylu_wartosci_do_wyswietlania_1_o_00, uklad_przesylu_wartosci_do_wyswietlania_1_o_01,
       uklad_przesylu_wartosci_do_wyswietlania_1_o_02, uklad_przesylu_wartosci_do_wyswietlania_1_o_03,
       uklad_przesylu_wartosci_do_wyswietlania_1_o_04, uklad_przesylu_wartosci_do_wyswietlania_1_o_05,
       uklad_przesylu_wartosci_do_wyswietlania_1_o_06, uklad_przesylu_wartosci_do_wyswietlania_1_o_07,
       uklad_przesylu_wartosci_do_wyswietlania_1_o_08, uklad_przesylu_wartosci_do_wyswietlania_1_o_09,
       uklad_przesylu_wartosci_do_wyswietlania_1_o_10, uklad_przesylu_wartosci_do_wyswietlania_1_o_11,
       uklad_przesylu_wartosci_do_wyswietlania_1_o_12, uklad_przesylu_wartosci_do_wyswietlania_1_o_13,
       uklad_przesylu_wartosci_do_wyswietlania_1_o_14, uklad_przesylu_wartosci_do_wyswietlania_1_o_15,
       uklad_przesylu_wartosci_do_wyswietlania_1_o_16, uklad_przesylu_wartosci_do_wyswietlania_1_o_17,
       uklad_przesylu_wartosci_do_wyswietlania_1_o_18, uklad_przesylu_wartosci_do_wyswietlania_1_o_19,
       uklad_przesylu_wartosci_do_wyswietlania_1_o_20, uklad_przesylu_wartosci_do_wyswietlania_1_o_21,
       uklad_przesylu_wartosci_do_wyswietlania_1_o_22, uklad_przesylu_wartosci_do_wyswietlania_1_o_23,
       uklad_przesylu_wartosci_do_wyswietlania_1_o_24;
  wire [24:0] controlled_buffer_5_out, main_26_we, pull_resistor_2_node;

  assign {_55, _54, _53, _52, _51, _45, _44, _43, _42, _41, _35, _34, _33, _32, _31, _25, _24, _23, _22, _21, _15, _14, _13, _12, _11} = ~PAMIEC;  // NOT_Gate not_1, 25 bits wide
  Uklad_zmiany_sterowania_z_3bit_na_5bit uklad_zmiany_sterowania_z_3bit_na_5bit_1 (
    .IN_X_5bit(x), .IN_Y_5bit(Y), .OUT_X__3bit(uklad_zmiany_sterowania_z_3bit_na_5bit_1_out_x__3bit),
    .OUT_XY_3bit(uklad_zmiany_sterowania_z_3bit_na_5bit_1_out_xy_3bit));
  Uklad_przesylu_wartosci_do_wyswietlania uklad_przesylu_wartosci_do_wyswietlania_1 (
    .IN_Value(WYJSCIE), .IN_X(uklad_zmiany_sterowania_z_3bit_na_5bit_1_out_x__3bit),
    .IN_Y(uklad_zmiany_sterowania_z_3bit_na_5bit_1_out_xy_3bit),
    .O_00(uklad_przesylu_wartosci_do_wyswietlania_1_o_00),
    .O_01(uklad_przesylu_wartosci_do_wyswietlania_1_o_01),
    .O_02(uklad_przesylu_wartosci_do_wyswietlania_1_o_02),
    .O_03(uklad_przesylu_wartosci_do_wyswietlania_1_o_03),
    .O_04(uklad_przesylu_wartosci_do_wyswietlania_1_o_04),
    .O_05(uklad_przesylu_wartosci_do_wyswietlania_1_o_05),
    .O_06(uklad_przesylu_wartosci_do_wyswietlania_1_o_06),
    .O_07(uklad_przesylu_wartosci_do_wyswietlania_1_o_07),
    .O_08(uklad_przesylu_wartosci_do_wyswietlania_1_o_08),
    .O_09(uklad_przesylu_wartosci_do_wyswietlania_1_o_09),
    .O_10(uklad_przesylu_wartosci_do_wyswietlania_1_o_10),
    .O_11(uklad_przesylu_wartosci_do_wyswietlania_1_o_11),
    .O_12(uklad_przesylu_wartosci_do_wyswietlania_1_o_12),
    .O_13(uklad_przesylu_wartosci_do_wyswietlania_1_o_13),
    .O_14(uklad_przesylu_wartosci_do_wyswietlania_1_o_14),
    .O_15(uklad_przesylu_wartosci_do_wyswietlania_1_o_15),
    .O_16(uklad_przesylu_wartosci_do_wyswietlania_1_o_16),
    .O_17(uklad_przesylu_wartosci_do_wyswietlania_1_o_17),
    .O_18(uklad_przesylu_wartosci_do_wyswietlania_1_o_18),
    .O_19(uklad_przesylu_wartosci_do_wyswietlania_1_o_19),
    .O_20(uklad_przesylu_wartosci_do_wyswietlania_1_o_20),
    .O_21(uklad_przesylu_wartosci_do_wyswietlania_1_o_21),
    .O_22(uklad_przesylu_wartosci_do_wyswietlania_1_o_22),
    .O_23(uklad_przesylu_wartosci_do_wyswietlania_1_o_23),
    .O_24(uklad_przesylu_wartosci_do_wyswietlania_1_o_24));
  Pull_Resistor pull_resistor_1 (.node(pull_resistor_1_node));
  assign pull_resistor_1_node = ENTER ? controlled_buffer_2_out : 1'bz;  // Controlled_Buffer controlled_buffer_1
  assign controlled_buffer_2_out = ENTER ? ENTER : 1'bz;  // Controlled_Buffer controlled_buffer_2
  _4bityx_1_main main_1 (
    .ENTER(pull_resistor_1_node), .\WEJŚCIE (uklad_przesylu_wartosci_do_wyswietlania_1_o_00),
    .\WYJŚCIE (\main_1_wyjście ), .Focus(_15), .RESET(START), .Koniec(lose));
  _4bityx_1_main main_2 (
    .ENTER(pull_resistor_1_node), .\WEJŚCIE (uklad_przesylu_wartosci_do_wyswietlania_1_o_01),
    .\WYJŚCIE (\main_2_wyjście ), .Focus(_14), .RESET(START), .Koniec(lose));
  _4bityx_1_main main_3 (
    .ENTER(pull_resistor_1_node), .\WEJŚCIE (uklad_przesylu_wartosci_do_wyswietlania_1_o_02),
    .\WYJŚCIE (\main_3_wyjście ), .Focus(_13), .RESET(START), .Koniec(lose));
  _4bityx_1_main main_4 (
    .ENTER(pull_resistor_1_node), .\WEJŚCIE (uklad_przesylu_wartosci_do_wyswietlania_1_o_03),
    .\WYJŚCIE (\main_4_wyjście ), .Focus(_12), .RESET(START), .Koniec(lose));
  _4bityx_1_main main_5 (
    .ENTER(pull_resistor_1_node), .\WEJŚCIE (uklad_przesylu_wartosci_do_wyswietlania_1_o_04),
    .\WYJŚCIE (\main_5_wyjście ), .Focus(_11), .RESET(START), .Koniec(lose));
  _4bityx_1_main main_6 (
    .ENTER(pull_resistor_1_node), .\WEJŚCIE (uklad_przesylu_wartosci_do_wyswietlania_1_o_05),
    .\WYJŚCIE (\main_6_wyjście ), .Focus(_25), .RESET(START), .Koniec(lose));
  _4bityx_1_main main_7 (
    .ENTER(pull_resistor_1_node), .\WEJŚCIE (uklad_przesylu_wartosci_do_wyswietlania_1_o_06),
    .\WYJŚCIE (\main_7_wyjście ), .Focus(_24), .RESET(START), .Koniec(lose));
  _4bityx_1_main main_8 (
    .ENTER(pull_resistor_1_node), .\WEJŚCIE (uklad_przesylu_wartosci_do_wyswietlania_1_o_07),
    .\WYJŚCIE (\main_8_wyjście ), .Focus(_23), .RESET(START), .Koniec(lose));
  _4bityx_1_main main_9 (
    .ENTER(pull_resistor_1_node), .\WEJŚCIE (uklad_przesylu_wartosci_do_wyswietlania_1_o_08),
    .\WYJŚCIE (\main_9_wyjście ), .Focus(_22), .RESET(START), .Koniec(lose));
  _4bityx_1_main main_10 (
    .ENTER(pull_resistor_1_node), .\WEJŚCIE (uklad_przesylu_wartosci_do_wyswietlania_1_o_09),
    .\WYJŚCIE (\main_10_wyjście ), .Focus(_21), .RESET(START), .Koniec(lose));
  _4bityx_1_main main_11 (
    .ENTER(pull_resistor_1_node), .\WEJŚCIE (uklad_przesylu_wartosci_do_wyswietlania_1_o_10),
    .\WYJŚCIE (\main_11_wyjście ), .Focus(_35), .RESET(START), .Koniec(lose));
  _4bityx_1_main main_12 (
    .ENTER(pull_resistor_1_node), .\WEJŚCIE (uklad_przesylu_wartosci_do_wyswietlania_1_o_11),
    .\WYJŚCIE (\main_12_wyjście ), .Focus(_34), .RESET(START), .Koniec(lose));
  _4bityx_1_main main_13 (
    .ENTER(pull_resistor_1_node), .\WEJŚCIE (uklad_przesylu_wartosci_do_wyswietlania_1_o_12),
    .\WYJŚCIE (\main_13_wyjście ), .Focus(_33), .RESET(START), .Koniec(lose));
  _4bityx_1_main main_14 (
    .ENTER(pull_resistor_1_node), .\WEJŚCIE (uklad_przesylu_wartosci_do_wyswietlania_1_o_13),
    .\WYJŚCIE (\main_14_wyjście ), .Focus(_32), .RESET(START), .Koniec(lose));
  _4bityx_1_main main_15 (
    .ENTER(pull_resistor_1_node), .\WEJŚCIE (uklad_przesylu_wartosci_do_wyswietlania_1_o_14),
    .\WYJŚCIE (\main_15_wyjście ), .Focus(_31), .RESET(START), .Koniec(lose));
  _4bityx_1_main main_16 (
    .ENTER(pull_resistor_1_node), .\WEJŚCIE (uklad_przesylu_wartosci_do_wyswietlania_1_o_15),
    .\WYJŚCIE (\main_16_wyjście ), .Focus(_45), .RESET(START), .Koniec(lose));
  _4bityx_1_main main_17 (
    .ENTER(pull_resistor_1_node), .\WEJŚCIE (uklad_przesylu_wartosci_do_wyswietlania_1_o_16),
    .\WYJŚCIE (\main_17_wyjście ), .Focus(_44), .RESET(START), .Koniec(lose));
  _4bityx_1_main main_18 (
    .ENTER(pull_resistor_1_node), .\WEJŚCIE (uklad_przesylu_wartosci_do_wyswietlania_1_o_17),
    .\WYJŚCIE (\main_18_wyjście ), .Focus(_43), .RESET(START), .Koniec(lose));
  _4bityx_1_main main_19 (
    .ENTER(pull_resistor_1_node), .\WEJŚCIE (uklad_przesylu_wartosci_do_wyswietlania_1_o_18),
    .\WYJŚCIE (\main_19_wyjście ), .Focus(_42), .RESET(START), .Koniec(lose));
  _4bityx_1_main main_20 (
    .ENTER(pull_resistor_1_node), .\WEJŚCIE (uklad_przesylu_wartosci_do_wyswietlania_1_o_19),
    .\WYJŚCIE (\main_20_wyjście ), .Focus(_41), .RESET(START), .Koniec(lose));
  _4bityx_1_main main_21 (
    .ENTER(pull_resistor_1_node), .\WEJŚCIE (uklad_przesylu_wartosci_do_wyswietlania_1_o_20),
    .\WYJŚCIE (\main_21_wyjście ), .Focus(_55), .RESET(START), .Koniec(lose));
  _4bityx_1_main main_22 (
    .ENTER(pull_resistor_1_node), .\WEJŚCIE (uklad_przesylu_wartosci_do_wyswietlania_1_o_21),
    .\WYJŚCIE (\main_22_wyjście ), .Focus(_54), .RESET(START), .Koniec(lose));
  _4bityx_1_main main_23 (
    .ENTER(pull_resistor_1_node), .\WEJŚCIE (uklad_przesylu_wartosci_do_wyswietlania_1_o_22),
    .\WYJŚCIE (\main_23_wyjście ), .Focus(_53), .RESET(START), .Koniec(lose));
  _4bityx_1_main main_24 (
    .ENTER(pull_resistor_1_node), .\WEJŚCIE (uklad_przesylu_wartosci_do_wyswietlania_1_o_23),
    .\WYJŚCIE (\main_24_wyjście ), .Focus(_52), .RESET(START), .Koniec(lose));
  _4bityx_1_main main_25 (
    .ENTER(pull_resistor_1_node), .\WEJŚCIE (uklad_przesylu_wartosci_do_wyswietlania_1_o_24),
    .\WYJŚCIE (\main_25_wyjście ), .Focus(_51), .RESET(START), .Koniec(lose));
  not not_2 (not_2_out, lose);
  ukadtest4_main main_26 (
    ._14(\main_4_wyjście ), ._13(\main_3_wyjście ), ._12(\main_2_wyjście ), ._11(\main_1_wyjście ),
    .in_6(\main_10_wyjście ), .in_7(\main_9_wyjście ), .in_8(\main_8_wyjście ), .in_9(\main_7_wyjście ),
    .in_10(\main_6_wyjście ), .in_11(\main_15_wyjście ), .in_12(\main_14_wyjście ),
    .in_13(\main_13_wyjście ), .in_14(\main_12_wyjście ), .in_15(\main_11_wyjście ),
    .in_16(\main_20_wyjście ), .in_17(\main_19_wyjście ), .in_18(\main_18_wyjście ),
    .in_19(\main_17_wyjście ), .in_20(\main_16_wyjście ), .in_21(\main_25_wyjście ),
    .in_22(\main_24_wyjście ), .in_23(\main_23_wyjście ), .in_24(\main_22_wyjście ),
    .in_25(\main_21_wyjście ), .\pamięć (PAMIEC), .we(main_26_we), .wy(pull_resistor_2_node),
    .przycisk(START), .out_30(out_8), .out_31(out_9), .out_32(out_10), .out_33(out_11), .out_34(out_12),
    .out_35(out_13), .out_36(out_14), .out_37(out_15), .out_38(out_16), .out_39(out_17), .out_40(out_18),
    .out_41(out_19), .out_42(out_20), .out_43(out_21), .out_44(out_22), .out_45(out_23), .out_46(out_24),
    .out_47(out_25), .out_48(out_26), .out_49(out_27), .out_50(out_28), .out_51(out_29), .out_52(out_30),
    .out_53(out_31), .out_54(out_32), .out_55(out_33), .out_56(out_34), .out_57(out_35), .out_58(out_36),
    .out_59(out_37), .out_60(out_38), .RESET(START), ._15(\main_5_wyjście ), .Win(main_26_win));  // open: out_61
  assign Win = not_2_out ? main_26_win : 1'bz;  // Controlled_Buffer controlled_buffer_3
  Pull_Resistor pull_resistor_2 (.node(pull_resistor_2_node));
  assign pull_resistor_2_node = ENTER ? controlled_buffer_5_out : 25'bz;  // Controlled_Buffer controlled_buffer_4
  assign controlled_buffer_5_out = ENTER ? main_26_we : 25'bz;  // Controlled_Buffer controlled_buffer_5
  Pull_Resistor pull_resistor_3 (.node(Win));
endmodule
