// Logisim project Saper.circ as structural Verilog: 1 circuit, main circuit main
module main (
);

  wire blokada, Blokada_startu, clock_1_out, clock_2_out, clock_3_out, clock_4_out, clock_5_out,
       counter_1_carry, d_ff_1_qn, Enter, GRAJ, Koniec, Loss, M, not_1_out, not_2_out, not_3_out, not_4_out,
       Reset, s_r_ff_1_q, START, Win;
  wire [1:0] DISP, DISP2, main_4_zegar;
  wire [2:0] uklad_zmiany_sterowania_z_3bit_na_5bit_1_out_x__3bit,
       uklad_zmiany_sterowania_z_3bit_na_5bit_1_out_xy_3bit;
  wire [3:0] V;
  wire [4:0] main_2_out_5, main_2_out_6, main_2_out_7, main_2_out_8, main_2_out_9, main_2_out_10,
       main_2_out_11, main_2_out_12, main_2_out_13, main_2_out_14, main_2_out_15, main_2_out_16,
       main_2_out_17, main_2_out_18, main_2_out_19, main_2_out_20, main_2_out_21, main_2_out_22,
       main_2_out_23, main_2_out_24, main_2_out_25, main_2_out_26, main_2_out_27, main_2_out_28,
       main_2_out_29, main_2_out_30, main_2_out_31, main_2_out_32, main_2_out_33, main_2_out_34,
       main_2_out_35, wyswietlacz_czasu_1_o0, wyswietlacz_czasu_1_o1, wyswietlacz_czasu_1_o2,
       wyswietlacz_czasu_1_o3, wyswietlacz_czasu_1_o4, wyswietlacz_czasu_1_o5, wyswietlacz_czasu_1_o6,
       wyswietlacz_czasu_1_o7, wyswietlacz_czasu_1_o8, wyswietlacz_czasu_1_o9, wyswietlacz_czasu_1_o10,
       wyswietlacz_czasu_1_o11, wyswietlacz_czasu_1_o12, wyswietlacz_czasu_1_o13, wyswietlacz_czasu_1_o14,
       wyswietlacz_czasu_1_o15, wyswietlacz_czasu_1_o16, wyswietlacz_czasu_1_o17, wyswietlacz_czasu_1_o18,
       wyswietlacz_czasu_1_o19, wyswietlacz_czasu_1_o20, X5, Y5;
  wire [5:0] main_4_dane;
  wire [6:0] Klawiatura;
  wire [11:0] L;
  wire [24:0] S_25b;
  wire [30:0] main_1_out_8, main_1_out_9, main_1_out_10, main_1_out_11, main_1_out_12, main_1_out_13,
       main_1_out_14, main_1_out_15, main_1_out_16, main_1_out_17, main_1_out_18, main_1_out_19,
       main_1_out_20, main_1_out_21, main_1_out_22, main_1_out_23, main_1_out_24, main_1_out_25,
       main_1_out_26, main_1_out_27, main_1_out_28, main_1_out_29, main_1_out_30, main_1_out_31,
       main_1_out_32, main_1_out_33, main_1_out_34, main_1_out_35, main_1_out_36, main_1_out_37,
       main_1_out_38;

  Button button_1 (.out(START));
  Button button_2 (.out(Reset));
  or or_1 (Koniec, Loss, Win);
  not not_1 (not_1_out, blokada);
  not not_2 (not_2_out, Koniec);
  SAPER2_main main_1 (
    .x(X5), .Y(Y5), .WYJSCIE(V), .START(DISP2[1]), .PAMIEC(S_25b), .ENTER(Enter), .lose(Loss),
    .out_8(main_1_out_8), .out_9(main_1_out_9), .out_10(main_1_out_10), .out_11(main_1_out_11),
    .out_12(main_1_out_12), .out_13(main_1_out_13), .out_14(main_1_out_14), .out_15(main_1_out_15),
    .out_16(main_1_out_16), .out_17(main_1_out_17), .out_18(main_1_out_18), .out_19(main_1_out_19),
    .out_20(main_1_out_20), .out_21(main_1_out_21), .out_22(main_1_out_22), .out_23(main_1_out_23),
    .out_24(main_1_out_24), .out_25(main_1_out_25), .out_26(main_1_out_26), .out_27(main_1_out_27),
    .out_28(main_1_out_28), .out_29(main_1_out_29), .out_30(main_1_out_30), .out_31(main_1_out_31),
    .out_32(main_1_out_32), .out_33(main_1_out_33), .out_34(main_1_out_34), .out_35(main_1_out_35),
    .out_36(main_1_out_36), .out_37(main_1_out_37), .out_38(main_1_out_38), .Win(Win));
  DotMatrix #(.inputtype("row"), .matrixcols(31), .matrixrows(31)) dotmatrix_1 (
    .row0(main_1_out_8), .row1(main_1_out_9), .row2(main_1_out_10), .row3(main_1_out_11),
    .row4(main_1_out_12), .row5(main_1_out_13), .row6(main_1_out_14), .row7(main_1_out_15),
    .row8(main_1_out_16), .row9(main_1_out_17), .row10(main_1_out_18), .row11(main_1_out_19),
    .row12(main_1_out_20), .row13(main_1_out_21), .row14(main_1_out_22), .row15(main_1_out_23),
    .row16(main_1_out_24), .row17(main_1_out_25), .row18(main_1_out_26), .row19(main_1_out_27),
    .row20(main_1_out_28), .row21(main_1_out_29), .row22(main_1_out_30), .row23(main_1_out_31),
    .row24(main_1_out_32), .row25(main_1_out_33), .row26(main_1_out_34), .row27(main_1_out_35),
    .row28(main_1_out_36), .row29(main_1_out_37), .row30(main_1_out_38));
  lose_main main_2 (
    .in_3(DISP2), .\L__połączyć_z_L_z_licznika_czasu_main (L), .out_5(main_2_out_5), .out_6(main_2_out_6),
    .out_7(main_2_out_7), .out_8(main_2_out_8), .out_9(main_2_out_9), .out_10(main_2_out_10),
    .out_11(main_2_out_11), .out_12(main_2_out_12), .out_13(main_2_out_13), .out_14(main_2_out_14),
    .out_15(main_2_out_15), .out_16(main_2_out_16), .out_17(main_2_out_17), .out_18(main_2_out_18),
    .out_19(main_2_out_19), .out_20(main_2_out_20), .out_21(main_2_out_21), .out_22(main_2_out_22),
    .out_23(main_2_out_23), .out_24(main_2_out_24), .out_25(main_2_out_25), .out_26(main_2_out_26),
    .out_27(main_2_out_27), .out_28(main_2_out_28), .out_29(main_2_out_29), .out_30(main_2_out_30),
    .out_31(main_2_out_31), .out_32(main_2_out_32), .out_33(main_2_out_33), .out_34(main_2_out_34),
    .out_35(main_2_out_35), .in_1(Loss), .Wl_WY(Win));
  DotMatrix #(.matrixcols(31), .matrixrows(5)) dotmatrix_2 (
    .col0(main_2_out_5), .col1(main_2_out_6), .col2(main_2_out_7), .col3(main_2_out_8), .col4(main_2_out_9),
    .col5(main_2_out_10), .col6(main_2_out_11), .col7(main_2_out_12), .col8(main_2_out_13),
    .col9(main_2_out_14), .col10(main_2_out_15), .col11(main_2_out_16), .col12(main_2_out_17),
    .col13(main_2_out_18), .col14(main_2_out_19), .col15(main_2_out_20), .col16(main_2_out_21),
    .col17(main_2_out_22), .col18(main_2_out_23), .col19(main_2_out_24), .col20(main_2_out_25),
    .col21(main_2_out_26), .col22(main_2_out_27), .col23(main_2_out_28), .col24(main_2_out_29),
    .col25(main_2_out_30), .col26(main_2_out_31), .col27(main_2_out_32), .col28(main_2_out_33),
    .col29(main_2_out_34), .col30(main_2_out_35));
  Clock clock_1 (.out(clock_1_out));
  Keyboard keyboard_1 (.clk(clock_1_out), .clr(blokada), .data(Klawiatura));  // open: re, avail
  Clock clock_2 (.out(clock_2_out));
  and and_1 (GRAJ, not_1_out, not_2_out);
  Clock clock_3 (.out(clock_3_out));
  Counter #(.width(13), .max('ha0)) counter_1 (
    .carry(counter_1_carry), .clk(clock_2_out), .clr(DISP2[1]));  // open: load, D, count, Q
  Pull_Resistor pull_resistor_1 (.node(DISP2[0]));
  assign DISP2[0] = Win ? clock_3_out : 1'bz;  // Controlled_Buffer controlled_buffer_1
  LED led_1 (.in(GRAJ));
  D_Flip_Flop d_ff_1 (
    .clk(counter_1_carry), .D(counter_1_carry), .Qn(d_ff_1_qn), .reset(DISP2[1]));  // open: Q, preset, en
  LED led_2 (.in(blokada));
  or or_2 (blokada, Loss, d_ff_1_qn);
  Clock #(.highDuration(64), .lowDuration(64)) clock_4 (.out(clock_4_out));
  licznik_czasu_main main_3 (.Czas(L), .CLK(clock_4_out), .Stop(Koniec), .Start(d_ff_1_qn), .out_5(DISP));
  not not_3 (not_3_out, Blokada_startu);
  assign DISP2[1] = not_3_out ? START : 1'bz;  // Controlled_Buffer controlled_buffer_2
  DotMatrix #(.matrixcols(21), .matrixrows(5)) dotmatrix_3 (
    .col0(wyswietlacz_czasu_1_o20), .col1(wyswietlacz_czasu_1_o19), .col2(wyswietlacz_czasu_1_o18),
    .col3(wyswietlacz_czasu_1_o17), .col4(wyswietlacz_czasu_1_o16), .col5(wyswietlacz_czasu_1_o15),
    .col6(wyswietlacz_czasu_1_o14), .col7(wyswietlacz_czasu_1_o13), .col8(wyswietlacz_czasu_1_o12),
    .col9(wyswietlacz_czasu_1_o11), .col10(wyswietlacz_czasu_1_o10), .col11(wyswietlacz_czasu_1_o9),
    .col12(wyswietlacz_czasu_1_o8), .col13(wyswietlacz_czasu_1_o7), .col14(wyswietlacz_czasu_1_o6),
    .col15(wyswietlacz_czasu_1_o5), .col16(wyswietlacz_czasu_1_o4), .col17(wyswietlacz_czasu_1_o3),
    .col18(wyswietlacz_czasu_1_o2), .col19(wyswietlacz_czasu_1_o1), .col20(wyswietlacz_czasu_1_o0));
  Clock #(.highDuration(4), .lowDuration(4)) clock_5 (.out(clock_5_out));
  Pull_Resistor pull_resistor_2 (.node(DISP2[1]));
  wyswietlacz_czasu wyswietlacz_czasu_1 (
    .DISP_IN__1bit_reset_0bit_clk(DISP), .o0(wyswietlacz_czasu_1_o0), .o1(wyswietlacz_czasu_1_o1),
    .o2(wyswietlacz_czasu_1_o2), .o3(wyswietlacz_czasu_1_o3), .o4(wyswietlacz_czasu_1_o4),
    .o9(wyswietlacz_czasu_1_o9), .o8(wyswietlacz_czasu_1_o8), .o7(wyswietlacz_czasu_1_o7),
    .o6(wyswietlacz_czasu_1_o6), .o5(wyswietlacz_czasu_1_o5), .o15(wyswietlacz_czasu_1_o15),
    .o14(wyswietlacz_czasu_1_o14), .o13(wyswietlacz_czasu_1_o13), .o12(wyswietlacz_czasu_1_o12),
    .o11(wyswietlacz_czasu_1_o11), .o20(wyswietlacz_czasu_1_o20), .o19(wyswietlacz_czasu_1_o19),
    .o18(wyswietlacz_czasu_1_o18), .o17(wyswietlacz_czasu_1_o17), .o16(wyswietlacz_czasu_1_o16),
    .o10(wyswietlacz_czasu_1_o10));
  \Sterowanie_dużo  \sterowanie_dużo_1  (
    .Wejscie_Klawiatury(Klawiatura), .Nr_Zaznaczonego_pola(S_25b), .Enter(Enter), .M(M), .X(X5), .Y(Y5));
  Counter #(.width(2), .max('h3), .ongoal("stay")) counter_2 (
    .carry(Blokada_startu), .clk(clock_5_out), .clr(not_4_out));  // open: load, D, count, Q
  not not_4 (not_4_out, s_r_ff_1_q);
  S_R_Flip_Flop #(.trigger("high")) s_r_ff_1 (
    .S(START), .clk(1'b1), .R(Reset), .Q(s_r_ff_1_q));  // open: Qn, preset, reset, en
  Maszyna_Los_XY22_main main_4 (.START(DISP2[1]), .DANE(main_4_dane), .ZEGAR(main_4_zegar));
  Uklad_zmiany_sterowania_z_3bit_na_5bit uklad_zmiany_sterowania_z_3bit_na_5bit_1 (
    .IN_X_5bit(X5), .IN_Y_5bit(Y5), .OUT_X__3bit(uklad_zmiany_sterowania_z_3bit_na_5bit_1_out_x__3bit),
    .OUT_XY_3bit(uklad_zmiany_sterowania_z_3bit_na_5bit_1_out_xy_3bit));
  \porównywacz_main  main_5 (
    .in_1(main_4_zegar), .in_2(main_4_dane), .in_3(DISP2[1]), .in_6(Enter), .out_8(V),
    .Y(uklad_zmiany_sterowania_z_3bit_na_5bit_1_out_x__3bit),
    .X(uklad_zmiany_sterowania_z_3bit_na_5bit_1_out_xy_3bit), .out_9(Loss), .RESET(Reset));

  // Other names for the same wires on the sheet: STOP = blokada; Start_t = DISP2[1]

  // Notes on the sheet:
  //   Poruszanie WASD i "enter" aby sprawdzić pole 
  //   Przed rozpoczęciem rozgrywki należy wcisnąć przycisk START
  //   Symulacja 128Hz
endmodule
