// Logisim project Układ wyświetlania2.circ as structural Verilog: 1 circuit, main circuit main
module main (
  input  in_1,
  input  [3:0] in_2,
  output [24:0] out_3,
  output [3:0] out_4
);

  Multiplexer #(.width(4)) multiplexer_1 (
    .in0(4'b1111), .in1(4'b0000), .out({out_3[24], out_3[20], out_3[4], out_3[0]}), .sel(in_1));  // open: en
  ROM #(.addrWidth(4), .dataWidth(21)) rom_1 (
    .addr(in_2), .data({out_3[23:21], out_3[19:5], out_3[3:1]}));  // open: sel

  assign out_4 = {out_3[24], out_3[20], out_3[4], out_3[0]};

  // Notes on the sheet:
  //   contents of rom_1 (hex, n*v repeats v):
  //   1d4a57 88422 1d0e17 1c4e17 44e55 1c4e47 1d4e47 44217 0 0 8a20
endmodule
