// Logisim project bramka3.circ as structural Verilog: 1 circuit, main circuit main
module main (
  input  [4:0] \stała ,
  input  [4:0] WE,
  input  Wl_WY,
  output [4:0] WY
);

  wire not_1_out;

  not not_1 (not_1_out, Wl_WY);
  assign WY = not_1_out ? \stała  : 5'bz;  // Controlled_Buffer controlled_buffer_1
  assign WY = Wl_WY ? WE : 5'bz;  // Controlled_Buffer controlled_buffer_2
endmodule
