// Logisim project licznik czasu.circ as structural Verilog: 6 circuits, main circuit main
module main (
  input  CLK,
  input  Stop,
  input  Start,
  output [11:0] Czas,
  output [1:0] out_5
);

  wire d_ff_1_qn, d_ff_2_qn, d_ff_3_qn, d_ff_4_qn, d_ff_5_qn, d_ff_6_qn, d_ff_7_qn, d_ff_8_qn, d_ff_9_qn,
       d_ff_10_qn, d_ff_11_qn, d_ff_12_qn, not_1_out, Stop_t;

  not not_1 (not_1_out, Stop_t);
  assign out_5[0] = not_1_out ? CLK : 1'bz;  // Controlled_Buffer controlled_buffer_1
  S_R_Flip_Flop #(.trigger("high")) s_r_ff_1 (
    .S(Stop), .clk(1'b1), .R(Start), .Q(Stop_t));  // open: Qn, preset, reset, en
  D_Flip_Flop d_ff_1 (.clk(out_5[0]), .D(d_ff_1_qn), .Q(Czas[0]), .Qn(d_ff_1_qn), .reset(Start));  // open: preset, en
  D_Flip_Flop d_ff_2 (.clk(d_ff_10_qn), .D(d_ff_2_qn), .Q(Czas[4]), .Qn(d_ff_2_qn), .reset(Start));  // open: preset, en
  D_Flip_Flop d_ff_3 (.clk(d_ff_11_qn), .D(d_ff_3_qn), .Q(Czas[8]), .Qn(d_ff_3_qn), .reset(Start));  // open: preset, en
  D_Flip_Flop d_ff_4 (.clk(d_ff_1_qn), .D(d_ff_4_qn), .Q(Czas[1]), .Qn(d_ff_4_qn), .reset(Start));  // open: preset, en
  D_Flip_Flop d_ff_5 (.clk(d_ff_2_qn), .D(d_ff_5_qn), .Q(Czas[5]), .Qn(d_ff_5_qn), .reset(Start));  // open: preset, en
  D_Flip_Flop d_ff_6 (.clk(d_ff_3_qn), .D(d_ff_6_qn), .Q(Czas[9]), .Qn(d_ff_6_qn), .reset(Start));  // open: preset, en
  D_Flip_Flop d_ff_7 (.clk(d_ff_4_qn), .D(d_ff_7_qn), .Q(Czas[2]), .Qn(d_ff_7_qn), .reset(Start));  // open: preset, en
  D_Flip_Flop d_ff_8 (.clk(d_ff_5_qn), .D(d_ff_8_qn), .Q(Czas[6]), .Qn(d_ff_8_qn), .reset(Start));  // open: preset, en
  D_Flip_Flop d_ff_9 (.clk(d_ff_6_qn), .D(d_ff_9_qn), .Q(Czas[10]), .Qn(d_ff_9_qn), .reset(Start));  // open: preset, en
  D_Flip_Flop d_ff_10 (
    .clk(d_ff_7_qn), .D(d_ff_10_qn), .Q(Czas[3]), .Qn(d_ff_10_qn), .reset(Start));  // open: preset, en
  D_Flip_Flop d_ff_11 (
    .clk(d_ff_8_qn), .D(d_ff_11_qn), .Q(Czas[7]), .Qn(d_ff_11_qn), .reset(Start));  // open: preset, en
  D_Flip_Flop d_ff_12 (
    .clk(d_ff_9_qn), .D(d_ff_12_qn), .Q(Czas[11]), .Qn(d_ff_12_qn), .reset(Start));  // open: preset, en

  assign out_5[1] = Start;

  // Other names for the same wires on the sheet: CLK_t = out_5[0]
endmodule

module led_dekoder (
  input  I4,
  input  I3,
  input  I2,
  input  I1,
  output o1,
  output o2,
  output o3,
  output o5,
  output o6,
  output o7,
  output o8
);

  wire and_1_out, and_2_out, and_3_out, and_4_out, and_5_out, and_6_out, and_7_out, and_8_out, and_9_out,
       and_10_out, and_11_out, and_12_out, and_13_out, and_14_out, and_15_out, and_16_out, and_17_out,
       and_18_out, and_19_out, and_20_out, and_21_out, and_22_out, and_23_out, and_24_out, and_25_out,
       and_26_out, and_27_out, and_28_out, and_29_out, and_30_out, and_31_out, and_32_out, and_33_out,
       and_34_out, and_35_out, and_36_out, not_1_out, not_2_out, not_3_out, not_4_out, not_5_out, not_6_out,
       not_7_out, not_8_out, not_9_out, not_10_out, not_11_out, not_12_out, not_13_out, not_14_out,
       not_15_out, not_16_out, not_17_out, not_18_out, not_19_out, not_20_out, not_21_out, not_22_out,
       not_23_out, not_24_out, not_25_out, not_26_out, not_27_out, not_28_out, not_29_out, not_30_out,
       not_31_out, not_32_out, not_33_out, not_34_out, not_35_out, not_36_out, not_37_out, not_38_out,
       not_39_out, not_40_out, not_41_out, not_42_out, not_43_out, not_44_out, not_45_out;

  not not_1 (not_1_out, I3);
  and and_1 (and_1_out, not_1_out, not_2_out);
  not not_2 (not_2_out, I1);
  and and_2 (and_2_out, I2, not_3_out);
  not not_3 (not_3_out, I1);
  and and_3 (and_3_out, I4, I2);
  and and_4 (and_4_out, I4, I3);
  not not_4 (not_4_out, I3);
  and and_5 (and_5_out, not_4_out, not_5_out, not_6_out);
  not not_5 (not_5_out, I2);
  not not_6 (not_6_out, I1);
  not not_7 (not_7_out, I4);
  and and_6 (and_6_out, not_7_out, I2, not_8_out);
  not not_8 (not_8_out, I1);
  not not_9 (not_9_out, I3);
  and and_7 (and_7_out, not_9_out, I2, I1);
  not not_10 (not_10_out, I2);
  and and_8 (and_8_out, I3, not_10_out, I1);
  and and_9 (and_9_out, I4, I3, not_11_out);
  not not_11 (not_11_out, I1);
  not not_12 (not_12_out, I3);
  and and_10 (and_10_out, not_12_out, not_13_out);
  not not_13 (not_13_out, I2);
  not not_14 (not_14_out, I3);
  and and_11 (and_11_out, not_14_out, I1);
  not not_15 (not_15_out, I2);
  and and_12 (and_12_out, not_15_out, I1);
  not not_16 (not_16_out, I4);
  and and_13 (and_13_out, not_16_out, I3);
  and and_14 (and_14_out, I4, not_17_out);
  not not_17 (not_17_out, I3);
  not not_18 (not_18_out, I3);
  and and_15 (and_15_out, not_18_out, I2);
  and and_16 (and_16_out, I2, not_19_out);
  not not_19 (not_19_out, I1);
  not not_20 (not_20_out, I4);
  and and_17 (and_17_out, not_20_out, I3, not_21_out);
  not not_21 (not_21_out, I1);
  and and_18 (and_18_out, I3, not_22_out, I1);
  not not_22 (not_22_out, I2);
  and and_19 (and_19_out, I4, not_23_out);
  not not_23 (not_23_out, I3);
  and and_20 (and_20_out, I4, I2);
  not not_24 (not_24_out, I2);
  and and_21 (and_21_out, not_24_out, not_25_out);
  not not_25 (not_25_out, I1);
  not not_26 (not_26_out, I4);
  and and_22 (and_22_out, not_26_out, I3, not_27_out);
  not not_27 (not_27_out, I2);
  and and_23 (and_23_out, I3, not_28_out);
  not not_28 (not_28_out, I1);
  and and_24 (and_24_out, I4, not_29_out);
  not not_29 (not_29_out, I3);
  and and_25 (and_25_out, I4, I2);
  not not_30 (not_30_out, I3);
  and and_26 (and_26_out, not_30_out, not_31_out);
  not not_31 (not_31_out, I1);
  not not_32 (not_32_out, I4);
  and and_27 (and_27_out, not_32_out, I2, I1);
  not not_33 (not_33_out, I4);
  and and_28 (and_28_out, not_33_out, I3, I1);
  and and_29 (and_29_out, I3, I2, I1);
  not not_34 (not_34_out, I3);
  and and_30 (and_30_out, I4, not_34_out, not_35_out);
  not not_35 (not_35_out, I2);
  and and_31 (and_31_out, I4, not_36_out);
  not not_36 (not_36_out, I1);
  not not_37 (not_37_out, I4);
  not not_38 (not_38_out, I2);
  and and_32 (and_32_out, not_37_out, not_38_out, not_39_out);
  not not_39 (not_39_out, I1);
  not not_40 (not_40_out, I3);
  and and_33 (and_33_out, not_40_out, not_41_out);
  not not_41 (not_41_out, I2);
  not not_42 (not_42_out, I3);
  and and_34 (and_34_out, not_42_out, not_43_out);
  not not_43 (not_43_out, I1);
  not not_44 (not_44_out, I4);
  and and_35 (and_35_out, not_44_out, I2, I1);
  and and_36 (and_36_out, I4, not_45_out, I1);
  not not_45 (not_45_out, I2);
  or or_1 (o1, and_1_out, and_2_out, and_3_out, and_4_out);
  or or_2 (o2, and_5_out, and_6_out, and_7_out, and_8_out, and_9_out);
  or or_3 (o3, and_10_out, and_11_out, and_12_out, and_13_out, and_14_out);
  or or_4 (o6, and_21_out, and_22_out, and_23_out, and_24_out, and_25_out);
  or or_5 (o8, and_32_out, and_33_out, and_34_out, and_35_out, and_36_out);
  or or_6 (o5, and_15_out, and_16_out, and_17_out, and_18_out, and_19_out, and_20_out);
  or or_7 (o7, and_26_out, and_27_out, and_28_out, and_29_out, and_30_out, and_31_out);
endmodule

module wyswietlacz_czasu (
  input  [1:0] DISP_IN__1bit_reset_0bit_clk,
  output [4:0] o10,
  output [4:0] o20,
  output [4:0] o15,
  output [4:0] o9,
  output [4:0] o4,
  output [4:0] o19,
  output [4:0] o14,
  output [4:0] o8,
  output [4:0] o3,
  output [4:0] o18,
  output [4:0] o13,
  output [4:0] o7,
  output [4:0] o2,
  output [4:0] o17,
  output [4:0] o12,
  output [4:0] o6,
  output [4:0] o1,
  output [4:0] o16,
  output [4:0] o11,
  output [4:0] o5,
  output [4:0] o0
);

  wire and_1_out, and_2_out, and_3_out, and_4_out, controlled_buffer_1_out, controlled_buffer_3_out,
       controlled_buffer_5_out, controlled_buffer_7_out, licznik_4_bitowy_1_q0, licznik_4_bitowy_1_q1,
       licznik_4_bitowy_1_q2, licznik_4_bitowy_1_q3, licznik_4_bitowy_2_q0, licznik_4_bitowy_2_q1,
       licznik_4_bitowy_2_q2, licznik_4_bitowy_2_q3, licznik_4_bitowy_3_q0, licznik_4_bitowy_3_q1,
       licznik_4_bitowy_3_q2, licznik_4_bitowy_3_q3, licznik_4_bitowy_4_q0, licznik_4_bitowy_4_q1,
       licznik_4_bitowy_4_q2, licznik_4_bitowy_4_q3, not_1_out, not_2_out, not_3_out, not_4_out;

  and and_1 (and_1_out, licznik_4_bitowy_1_q2, licznik_4_bitowy_1_q1);
  not not_1 (not_1_out, DISP_IN__1bit_reset_0bit_clk[1]);
  Matrix_Dekoder matrix_dekoder_1 (
    .I_3(licznik_4_bitowy_1_q3), .I_2(licznik_4_bitowy_1_q2), .I_1(licznik_4_bitowy_1_q1),
    .I_O(licznik_4_bitowy_1_q0), .R(o19), .C(o18), .L(o17));
  licznik_4_bitowy licznik_4_bitowy_1 (
    .T(and_2_out), .Reset(controlled_buffer_1_out), .Q3(licznik_4_bitowy_1_q3), .Q2(licznik_4_bitowy_1_q2),
    .Q1(licznik_4_bitowy_1_q1), .Q0(licznik_4_bitowy_1_q0));
  assign controlled_buffer_1_out = DISP_IN__1bit_reset_0bit_clk[1] ? 1'b1 : 1'bz;  // Controlled_Buffer controlled_buffer_1
  assign controlled_buffer_1_out = not_1_out ? and_1_out : 1'bz;  // Controlled_Buffer controlled_buffer_2
  and and_2 (and_2_out, licznik_4_bitowy_2_q3, licznik_4_bitowy_2_q1);
  licznik_4_bitowy licznik_4_bitowy_2 (
    .T(and_3_out), .Reset(controlled_buffer_3_out), .Q3(licznik_4_bitowy_2_q3), .Q2(licznik_4_bitowy_2_q2),
    .Q1(licznik_4_bitowy_2_q1), .Q0(licznik_4_bitowy_2_q0));
  not not_2 (not_2_out, DISP_IN__1bit_reset_0bit_clk[1]);
  Matrix_Dekoder matrix_dekoder_2 (
    .I_3(licznik_4_bitowy_2_q3), .I_2(licznik_4_bitowy_2_q2), .I_1(licznik_4_bitowy_2_q1),
    .I_O(licznik_4_bitowy_2_q0), .R(o14), .C(o13), .L(o12));
  assign controlled_buffer_3_out = not_2_out ? and_2_out : 1'bz;  // Controlled_Buffer controlled_buffer_3
  assign controlled_buffer_3_out = DISP_IN__1bit_reset_0bit_clk[1] ? 1'b1 : 1'bz;  // Controlled_Buffer controlled_buffer_4
  Matrix_Dekoder matrix_dekoder_3 (
    .I_3(licznik_4_bitowy_3_q3), .I_2(licznik_4_bitowy_3_q2), .I_1(licznik_4_bitowy_3_q1),
    .I_O(licznik_4_bitowy_3_q0), .R(o8), .C(o7), .L(o6));
  and and_3 (and_3_out, licznik_4_bitowy_3_q2, licznik_4_bitowy_3_q1);
  licznik_4_bitowy licznik_4_bitowy_3 (
    .T(and_4_out), .Reset(controlled_buffer_5_out), .Q3(licznik_4_bitowy_3_q3), .Q2(licznik_4_bitowy_3_q2),
    .Q1(licznik_4_bitowy_3_q1), .Q0(licznik_4_bitowy_3_q0));
  assign controlled_buffer_5_out = DISP_IN__1bit_reset_0bit_clk[1] ? 1'b1 : 1'bz;  // Controlled_Buffer controlled_buffer_5
  assign controlled_buffer_5_out = not_3_out ? and_3_out : 1'bz;  // Controlled_Buffer controlled_buffer_6
  not not_3 (not_3_out, DISP_IN__1bit_reset_0bit_clk[1]);
  and and_4 (and_4_out, licznik_4_bitowy_4_q3, licznik_4_bitowy_4_q1);
  Matrix_Dekoder matrix_dekoder_4 (
    .I_3(licznik_4_bitowy_4_q3), .I_2(licznik_4_bitowy_4_q2), .I_1(licznik_4_bitowy_4_q1),
    .I_O(licznik_4_bitowy_4_q0), .R(o3), .C(o2), .L(o1));
  licznik_4_bitowy licznik_4_bitowy_4 (
    .T(DISP_IN__1bit_reset_0bit_clk[0]), .Reset(controlled_buffer_7_out), .Q3(licznik_4_bitowy_4_q3),
    .Q2(licznik_4_bitowy_4_q2), .Q1(licznik_4_bitowy_4_q1), .Q0(licznik_4_bitowy_4_q0));
  assign controlled_buffer_7_out = not_4_out ? and_4_out : 1'bz;  // Controlled_Buffer controlled_buffer_7
  assign controlled_buffer_7_out = DISP_IN__1bit_reset_0bit_clk[1] ? 1'b1 : 1'bz;  // Controlled_Buffer controlled_buffer_8
  not not_4 (not_4_out, DISP_IN__1bit_reset_0bit_clk[1]);

  assign o0 = {5{1'b0}};
  assign o4 = {5{1'b0}};
  assign o5 = {5{1'b0}};
  assign o9 = {5{1'b0}};
  assign o10 = 5'b01010;
  assign o11 = {5{1'b0}};
  assign o15 = {5{1'b0}};
  assign o16 = {5{1'b0}};
  assign o20 = {5{1'b0}};

  // Other names for the same wires on the sheet: CLK = DISP_IN__1bit_reset_0bit_clk[0];
  //   R = DISP_IN__1bit_reset_0bit_clk[1]
endmodule

module licznik_4_bitowy (
  input  T,
  input  Reset,
  output Q3,
  output Q2,
  output Q1,
  output Q0
);

  wire t_ff_1_qn, t_ff_2_qn, t_ff_3_qn;

  T_Flip_Flop t_ff_1 (.clk(T), .T(1'b1), .Q(Q0), .Qn(t_ff_1_qn), .reset(Reset));  // open: preset, en
  T_Flip_Flop t_ff_2 (.clk(t_ff_1_qn), .T(1'b1), .Q(Q1), .Qn(t_ff_2_qn), .reset(Reset));  // open: preset, en
  T_Flip_Flop t_ff_3 (.clk(t_ff_2_qn), .T(1'b1), .Q(Q2), .Qn(t_ff_3_qn), .reset(Reset));  // open: preset, en
  T_Flip_Flop t_ff_4 (.clk(t_ff_3_qn), .T(1'b1), .Q(Q3), .reset(Reset));  // open: Qn, preset, en
endmodule

module Wyswietlanie_wyniku (
  input  [1:0] in_1,
  input  [11:0] \L__połączyć_z_L_z_licznika_czasu_main ,
  output [4:0] o10,
  output [4:0] o20,
  output [4:0] o15,
  output [4:0] o9,
  output [4:0] o4,
  output [4:0] o19,
  output [4:0] o14,
  output [4:0] o8,
  output [4:0] o3,
  output [4:0] o18,
  output [4:0] o13,
  output [4:0] o7,
  output [4:0] o2,
  output [4:0] o17,
  output [4:0] o12,
  output [4:0] o6,
  output [4:0] o1,
  output [4:0] o16,
  output [4:0] o11,
  output [4:0] o5,
  output [4:0] o0
);

  wire and_1_out, and_2_out, and_3_out, and_4_out, controlled_buffer_1_out, controlled_buffer_3_out,
       controlled_buffer_5_out, controlled_buffer_8_out, Licz, licznik_4_bitowy_1_q0, licznik_4_bitowy_1_q1,
       licznik_4_bitowy_1_q2, licznik_4_bitowy_1_q3, licznik_4_bitowy_2_q0, licznik_4_bitowy_2_q1,
       licznik_4_bitowy_2_q2, licznik_4_bitowy_2_q3, licznik_4_bitowy_3_q0, licznik_4_bitowy_3_q1,
       licznik_4_bitowy_3_q2, licznik_4_bitowy_3_q3, licznik_4_bitowy_4_q0, licznik_4_bitowy_4_q1,
       licznik_4_bitowy_4_q2, licznik_4_bitowy_4_q3, not_1_out, not_2_out, not_3_out, not_4_out,
       pull_resistor_1_node;
  wire [11:0] counter_1_q, subtractor_1_out;

  Counter #(.width(12), .max('h3ff), .ongoal("stay")) counter_1 (
    .Q(counter_1_q), .clk(in_1[0]), .clr(in_1[1]));  // open: load, D, count, carry
  Subtractor #(.width(12)) subtractor_1 (
    .a(12'h3ff), .b({1'b0, \L__połączyć_z_L_z_licznika_czasu_main [10:0]}), .out(subtractor_1_out));  // open: bin, bout
  Comparator #(.width(12)) comparator_1 (.a(counter_1_q), .b(subtractor_1_out), .lt(Licz));  // open: gt, eq
  and and_1 (and_1_out, licznik_4_bitowy_1_q3, licznik_4_bitowy_1_q1);
  not not_1 (not_1_out, in_1[1]);
  Matrix_Dekoder matrix_dekoder_1 (
    .I_3(licznik_4_bitowy_1_q3), .I_2(licznik_4_bitowy_1_q2), .I_1(licznik_4_bitowy_1_q1),
    .I_O(licznik_4_bitowy_1_q0), .R(o19), .C(o18), .L(o17));
  licznik_4_bitowy licznik_4_bitowy_1 (
    .T(and_2_out), .Reset(controlled_buffer_1_out), .Q3(licznik_4_bitowy_1_q3), .Q2(licznik_4_bitowy_1_q2),
    .Q1(licznik_4_bitowy_1_q1), .Q0(licznik_4_bitowy_1_q0));
  assign controlled_buffer_1_out = in_1[1] ? 1'b1 : 1'bz;  // Controlled_Buffer controlled_buffer_1
  assign controlled_buffer_1_out = not_1_out ? and_1_out : 1'bz;  // Controlled_Buffer controlled_buffer_2
  and and_2 (and_2_out, licznik_4_bitowy_2_q3, licznik_4_bitowy_2_q1);
  licznik_4_bitowy licznik_4_bitowy_2 (
    .T(and_3_out), .Reset(controlled_buffer_3_out), .Q3(licznik_4_bitowy_2_q3), .Q2(licznik_4_bitowy_2_q2),
    .Q1(licznik_4_bitowy_2_q1), .Q0(licznik_4_bitowy_2_q0));
  not not_2 (not_2_out, in_1[1]);
  Matrix_Dekoder matrix_dekoder_2 (
    .I_3(licznik_4_bitowy_2_q3), .I_2(licznik_4_bitowy_2_q2), .I_1(licznik_4_bitowy_2_q1),
    .I_O(licznik_4_bitowy_2_q0), .R(o14), .C(o13), .L(o12));
  assign controlled_buffer_3_out = not_2_out ? and_2_out : 1'bz;  // Controlled_Buffer controlled_buffer_3
  assign controlled_buffer_3_out = in_1[1] ? 1'b1 : 1'bz;  // Controlled_Buffer controlled_buffer_4
  Matrix_Dekoder matrix_dekoder_3 (
    .I_3(licznik_4_bitowy_3_q3), .I_2(licznik_4_bitowy_3_q2), .I_1(licznik_4_bitowy_3_q1),
    .I_O(licznik_4_bitowy_3_q0), .R(o8), .C(o7), .L(o6));
  and and_3 (and_3_out, licznik_4_bitowy_3_q3, licznik_4_bitowy_3_q1);
  licznik_4_bitowy licznik_4_bitowy_3 (
    .T(and_4_out), .Reset(controlled_buffer_5_out), .Q3(licznik_4_bitowy_3_q3), .Q2(licznik_4_bitowy_3_q2),
    .Q1(licznik_4_bitowy_3_q1), .Q0(licznik_4_bitowy_3_q0));
  assign controlled_buffer_5_out = in_1[1] ? 1'b1 : 1'bz;  // Controlled_Buffer controlled_buffer_5
  assign controlled_buffer_5_out = not_3_out ? and_3_out : 1'bz;  // Controlled_Buffer controlled_buffer_6
  not not_3 (not_3_out, in_1[1]);
  and and_4 (and_4_out, licznik_4_bitowy_4_q3, licznik_4_bitowy_4_q1);
  Matrix_Dekoder matrix_dekoder_4 (
    .I_3(licznik_4_bitowy_4_q3), .I_2(licznik_4_bitowy_4_q2), .I_1(licznik_4_bitowy_4_q1),
    .I_O(licznik_4_bitowy_4_q0), .R(o3), .C(o2), .L(o1));
  licznik_4_bitowy licznik_4_bitowy_4 (
    .T(pull_resistor_1_node), .Reset(controlled_buffer_8_out), .Q3(licznik_4_bitowy_4_q3),
    .Q2(licznik_4_bitowy_4_q2), .Q1(licznik_4_bitowy_4_q1), .Q0(licznik_4_bitowy_4_q0));
  Pull_Resistor pull_resistor_1 (.node(pull_resistor_1_node));
  assign pull_resistor_1_node = Licz ? in_1[0] : 1'bz;  // Controlled_Buffer controlled_buffer_7
  assign controlled_buffer_8_out = not_4_out ? and_4_out : 1'bz;  // Controlled_Buffer controlled_buffer_8
  assign controlled_buffer_8_out = in_1[1] ? 1'b1 : 1'bz;  // Controlled_Buffer controlled_buffer_9
  not not_4 (not_4_out, in_1[1]);

  assign o0 = {5{1'b0}};
  assign o4 = {5{1'b0}};
  assign o5 = {5{1'b0}};
  assign o9 = {5{1'b0}};
  assign o10 = {5{1'b0}};
  assign o11 = {5{1'b0}};
  assign o15 = {5{1'b0}};
  assign o16 = {5{1'b0}};
  assign o20 = {5{1'b0}};

  // Other names for the same wires on the sheet: CLK = in_1[0]; R = in_1[1]
endmodule

module Matrix_Dekoder (
  input  I_3,
  input  I_2,
  input  I_1,
  input  I_O,
  output [4:0] R,
  output [4:0] C,
  output [4:0] L
);

  ROM #(.addrWidth(4), .dataWidth(15)) rom_1 (.addr({I_3, I_2, I_1, I_O}), .data({R, C, L}));  // open: sel

  // Notes on the sheet:
  //   contents of rom_1 (hex, n*v repeats v):
  //   7e3f 3e0 5ebd 56bf 709f 76b7 7eb7 421f 7ebf 76bf
endmodule
