// Logisim project lose.circ as structural Verilog: 1 circuit, main circuit main
module main (
  input  in_1,
  input  [11:0] \L__połączyć_z_L_z_licznika_czasu_main ,
  input  [1:0] in_3,
  input  Wl_WY,
  output [4:0] out_5,
  output [4:0] out_6,
  output [4:0] out_7,
  output [4:0] out_8,
  output [4:0] out_9,
  output [4:0] out_10,
  output [4:0] out_11,
  output [4:0] out_12,
  output [4:0] out_13,
  output [4:0] out_14,
  output [4:0] out_15,
  output [4:0] out_16,
  output [4:0] out_17,
  output [4:0] out_18,
  output [4:0] out_19,
  output [4:0] out_20,
  output [4:0] out_21,
  output [4:0] out_22,
  output [4:0] out_23,
  output [4:0] out_24,
  output [4:0] out_25,
  output [4:0] out_26,
  output [4:0] out_27,
  output [4:0] out_28,
  output [4:0] out_29,
  output [4:0] out_30,
  output [4:0] out_31,
  output [4:0] out_32,
  output [4:0] out_33,
  output [4:0] out_34,
  output [4:0] out_35
);

  wire and_1_out, and_2_out, and_3_out, and_4_out, controlled_buffer_1_out, controlled_buffer_3_out,
       controlled_buffer_5_out, controlled_buffer_10_out, Licz, licznik_4_bitowy_1_q0, licznik_4_bitowy_1_q1,
       licznik_4_bitowy_1_q2, licznik_4_bitowy_1_q3, licznik_4_bitowy_2_q0, licznik_4_bitowy_2_q1,
       licznik_4_bitowy_2_q2, licznik_4_bitowy_2_q3, licznik_4_bitowy_3_q0, licznik_4_bitowy_3_q1,
       licznik_4_bitowy_3_q2, licznik_4_bitowy_3_q3, licznik_4_bitowy_4_q0, licznik_4_bitowy_4_q1,
       licznik_4_bitowy_4_q2, licznik_4_bitowy_4_q3, not_1_out, not_2_out, not_3_out, not_4_out, not_5_out,
       pull_resistor_1_node;
  wire [1:0] controlled_buffer_7_out;
  wire [4:0] matrix_dekoder_1_c, matrix_dekoder_1_l, matrix_dekoder_1_r, matrix_dekoder_2_c,
       matrix_dekoder_2_l, matrix_dekoder_2_r, matrix_dekoder_3_c, matrix_dekoder_3_l, matrix_dekoder_3_r,
       matrix_dekoder_4_c, matrix_dekoder_4_l, matrix_dekoder_4_r;
  wire [11:0] counter_1_q, subtractor_1_out;
  wire [19:0] rom_3_data;
  wire [29:0] rom_1_data, rom_2_data, rom_4_data, rom_5_data;

  Matrix_Dekoder matrix_dekoder_1 (
    .I_3(licznik_4_bitowy_1_q3), .I_2(licznik_4_bitowy_1_q2), .I_1(licznik_4_bitowy_1_q1),
    .I_O(licznik_4_bitowy_1_q0), .R(matrix_dekoder_1_r), .C(matrix_dekoder_1_c), .L(matrix_dekoder_1_l));
  and and_1 (and_1_out, licznik_4_bitowy_1_q3, licznik_4_bitowy_1_q1);
  licznik_4_bitowy licznik_4_bitowy_1 (
    .T(and_2_out), .Reset(controlled_buffer_1_out), .Q3(licznik_4_bitowy_1_q3), .Q2(licznik_4_bitowy_1_q2),
    .Q1(licznik_4_bitowy_1_q1), .Q0(licznik_4_bitowy_1_q0));
  assign controlled_buffer_1_out = not_1_out ? and_1_out : 1'bz;  // Controlled_Buffer controlled_buffer_1
  assign controlled_buffer_1_out = in_3[1] ? 1'b1 : 1'bz;  // Controlled_Buffer controlled_buffer_2
  not not_1 (not_1_out, in_3[1]);
  and and_2 (and_2_out, licznik_4_bitowy_2_q3, licznik_4_bitowy_2_q1);
  Matrix_Dekoder matrix_dekoder_2 (
    .I_3(licznik_4_bitowy_2_q3), .I_2(licznik_4_bitowy_2_q2), .I_1(licznik_4_bitowy_2_q1),
    .I_O(licznik_4_bitowy_2_q0), .R(matrix_dekoder_2_r), .C(matrix_dekoder_2_c), .L(matrix_dekoder_2_l));
  licznik_4_bitowy licznik_4_bitowy_2 (
    .T(and_3_out), .Reset(controlled_buffer_3_out), .Q3(licznik_4_bitowy_2_q3), .Q2(licznik_4_bitowy_2_q2),
    .Q1(licznik_4_bitowy_2_q1), .Q0(licznik_4_bitowy_2_q0));
  assign controlled_buffer_3_out = in_3[1] ? 1'b1 : 1'bz;  // Controlled_Buffer controlled_buffer_3
  assign controlled_buffer_3_out = not_2_out ? and_2_out : 1'bz;  // Controlled_Buffer controlled_buffer_4
  not not_2 (not_2_out, in_3[1]);
  and and_3 (and_3_out, licznik_4_bitowy_3_q3, licznik_4_bitowy_3_q1);
  not not_3 (not_3_out, in_3[1]);
  ROM #(.addrWidth(2), .dataWidth(30)) rom_1 (.addr(2'b01), .data(rom_1_data));  // open: sel
  ROM #(.addrWidth(2), .dataWidth(30)) rom_2 (.addr(2'b01), .data(rom_2_data));  // open: sel
  ROM #(.addrWidth(2), .dataWidth(20)) rom_3 (.addr(2'b01), .data(rom_3_data));  // open: sel
  Matrix_Dekoder matrix_dekoder_3 (
    .I_3(licznik_4_bitowy_3_q3), .I_2(licznik_4_bitowy_3_q2), .I_1(licznik_4_bitowy_3_q1),
    .I_O(licznik_4_bitowy_3_q0), .R(matrix_dekoder_3_r), .C(matrix_dekoder_3_c), .L(matrix_dekoder_3_l));
  licznik_4_bitowy licznik_4_bitowy_3 (
    .T(and_4_out), .Reset(controlled_buffer_5_out), .Q3(licznik_4_bitowy_3_q3), .Q2(licznik_4_bitowy_3_q2),
    .Q1(licznik_4_bitowy_3_q1), .Q0(licznik_4_bitowy_3_q0));
  assign controlled_buffer_5_out = not_3_out ? and_3_out : 1'bz;  // Controlled_Buffer controlled_buffer_5
  assign controlled_buffer_5_out = in_3[1] ? 1'b1 : 1'bz;  // Controlled_Buffer controlled_buffer_6
  not not_4 (not_4_out, Wl_WY);
  and and_4 (and_4_out, licznik_4_bitowy_4_q3, licznik_4_bitowy_4_q1);
  licznik_4_bitowy licznik_4_bitowy_4 (
    .T(pull_resistor_1_node), .Reset(controlled_buffer_10_out), .Q3(licznik_4_bitowy_4_q3),
    .Q2(licznik_4_bitowy_4_q2), .Q1(licznik_4_bitowy_4_q1), .Q0(licznik_4_bitowy_4_q0));
  Pull_Resistor pull_resistor_1 (.node(pull_resistor_1_node));
  assign controlled_buffer_7_out = not_4_out ? 2'b11 : 2'bz;  // Controlled_Buffer controlled_buffer_7
  assign controlled_buffer_7_out = Wl_WY ? 2'b00 : 2'bz;  // Controlled_Buffer controlled_buffer_8
  Matrix_Dekoder matrix_dekoder_4 (
    .I_3(licznik_4_bitowy_4_q3), .I_2(licznik_4_bitowy_4_q2), .I_1(licznik_4_bitowy_4_q1),
    .I_O(licznik_4_bitowy_4_q0), .R(matrix_dekoder_4_r), .C(matrix_dekoder_4_c), .L(matrix_dekoder_4_l));
  not not_5 (not_5_out, in_3[1]);
  assign pull_resistor_1_node = Licz ? in_3[0] : 1'bz;  // Controlled_Buffer controlled_buffer_9
  assign controlled_buffer_10_out = in_3[1] ? 1'b1 : 1'bz;  // Controlled_Buffer controlled_buffer_10
  assign controlled_buffer_10_out = not_5_out ? and_4_out : 1'bz;  // Controlled_Buffer controlled_buffer_11
  bramka3_main main_1 (.Wl_WY(in_1), .WY(out_7), .WE({5{1'b0}}), .\stała (matrix_dekoder_1_c));
  bramka3_main main_2 (.Wl_WY(in_1), .WY(out_6), .WE({5{1'b0}}), .\stała (matrix_dekoder_1_r));
  bramka3_main main_3 (.Wl_WY(in_1), .WY(out_5), .WE({5{1'b0}}), .\stała ({5{1'b0}}));
  ROM #(.addrWidth(2), .dataWidth(30)) rom_4 (.addr(controlled_buffer_7_out), .data(rom_4_data));  // open: sel
  bramka3_main main_4 (.Wl_WY(in_1), .WY(out_15), .WE(rom_1_data[14:10]), .\stała (matrix_dekoder_3_r));
  bramka3_main main_5 (.Wl_WY(in_1), .WY(out_14), .WE(rom_1_data[9:5]), .\stała ({5{1'b0}}));
  bramka3_main main_6 (.Wl_WY(in_1), .WY(out_13), .WE(rom_1_data[4:0]), .\stała ({5{1'b0}}));
  bramka3_main main_7 (.Wl_WY(in_1), .WY(out_12), .WE({5{1'b0}}), .\stała (matrix_dekoder_2_l));
  bramka3_main main_8 (.Wl_WY(in_1), .WY(out_11), .WE({5{1'b0}}), .\stała (matrix_dekoder_2_c));
  bramka3_main main_9 (.Wl_WY(in_1), .WY(out_10), .WE({5{1'b0}}), .\stała (matrix_dekoder_2_r));
  bramka3_main main_10 (.Wl_WY(in_1), .WY(out_9), .WE({5{1'b0}}), .\stała ({5{1'b0}}));
  bramka3_main main_11 (.Wl_WY(in_1), .WY(out_8), .WE({5{1'b0}}), .\stała (matrix_dekoder_1_l));
  ROM #(.addrWidth(2), .dataWidth(30)) rom_5 (.addr(controlled_buffer_7_out), .data(rom_5_data));  // open: sel
  bramka3_main main_12 (.Wl_WY(in_1), .WY(out_23), .WE(rom_2_data[24:20]), .\stała (rom_5_data[4:0]));
  bramka3_main main_13 (.Wl_WY(in_1), .WY(out_22), .WE(rom_2_data[19:15]), .\stała ({5{1'b0}}));
  bramka3_main main_14 (.Wl_WY(in_1), .WY(out_21), .WE(rom_2_data[14:10]), .\stała (matrix_dekoder_4_l));
  bramka3_main main_15 (.Wl_WY(in_1), .WY(out_20), .WE(rom_2_data[9:5]), .\stała (matrix_dekoder_4_c));
  bramka3_main main_16 (.Wl_WY(in_1), .WY(out_19), .WE(rom_2_data[4:0]), .\stała (matrix_dekoder_4_r));
  bramka3_main main_17 (.Wl_WY(in_1), .WY(out_18), .WE(rom_1_data[29:25]), .\stała ({5{1'b0}}));
  bramka3_main main_18 (.Wl_WY(in_1), .WY(out_17), .WE(rom_1_data[24:20]), .\stała (matrix_dekoder_3_l));
  bramka3_main main_19 (.Wl_WY(in_1), .WY(out_16), .WE(rom_1_data[19:15]), .\stała (matrix_dekoder_3_c));
  bramka3_main main_20 (.Wl_WY(in_1), .WY(out_31), .WE({5{1'b0}}), .\stała (rom_4_data[14:10]));
  bramka3_main main_21 (.Wl_WY(in_1), .WY(out_30), .WE({5{1'b0}}), .\stała (rom_4_data[9:5]));
  bramka3_main main_22 (.Wl_WY(in_1), .WY(out_29), .WE({5{1'b0}}), .\stała (rom_4_data[4:0]));
  bramka3_main main_23 (.Wl_WY(in_1), .WY(out_28), .WE(rom_3_data[19:15]), .\stała (rom_5_data[29:25]));
  bramka3_main main_24 (.Wl_WY(in_1), .WY(out_27), .WE(rom_3_data[14:10]), .\stała (rom_5_data[24:20]));
  bramka3_main main_25 (.Wl_WY(in_1), .WY(out_26), .WE(rom_3_data[9:5]), .\stała (rom_5_data[19:15]));
  bramka3_main main_26 (.Wl_WY(in_1), .WY(out_25), .WE(rom_3_data[4:0]), .\stała (rom_5_data[14:10]));
  bramka3_main main_27 (.Wl_WY(in_1), .WY(out_24), .WE(rom_2_data[29:25]), .\stała (rom_5_data[9:5]));
  bramka3_main main_28 (.Wl_WY(in_1), .WY(out_35), .WE({5{1'b0}}), .\stała ({5{1'b0}}));
  bramka3_main main_29 (.Wl_WY(in_1), .WY(out_34), .WE({5{1'b0}}), .\stała (rom_4_data[29:25]));
  bramka3_main main_30 (.Wl_WY(in_1), .WY(out_33), .WE({5{1'b0}}), .\stała (rom_4_data[24:20]));
  bramka3_main main_31 (.Wl_WY(in_1), .WY(out_32), .WE({5{1'b0}}), .\stała (rom_4_data[19:15]));
  Counter #(.width(12), .max('h3ff), .ongoal("stay")) counter_1 (
    .Q(counter_1_q), .clk(in_3[0]), .clr(in_3[1]));  // open: load, D, count, carry
  Subtractor #(.width(12)) subtractor_1 (
    .a(12'h3ff), .b({1'b0, \L__połączyć_z_L_z_licznika_czasu_main [10:0]}), .out(subtractor_1_out));  // open: bin, bout
  Comparator #(.width(12)) comparator_1 (.a(counter_1_q), .b(subtractor_1_out), .lt(Licz));  // open: gt, eq

  // Other names for the same wires on the sheet: CLK = in_3[0]; R = in_3[1]

  // Notes on the sheet:
  //   contents of rom_1 (hex, n*v repeats v):
  //   3e1f87e0 23f0043f
  //   contents of rom_2 (hex, n*v repeats v):
  //   3f0f83e0 17af41f
  //   contents of rom_3 (hex, n*v repeats v):
  //   0 56bf
  //   contents of rom_4 (hex, n*v repeats v):
  //   3f0f83e0 17af41f
  //   contents of rom_5 (hex, n*v repeats v):
  //   3e1f87e0 23f0043f
endmodule
