// Logisim project porównywacz.circ as structural Verilog: 1 circuit, main circuit main
module main (
  input  [1:0] ZEGAR,
  input  [5:0] DANE,
  input  START,
  input  [2:0] Y,
  input  [2:0] X,
  input  ENTER,
  input  RESET,
  output [3:0] DANE_2,
  output WYBUCH
);

  wire and_3_out, clock_1_out, clock_2_out, clock_3_out, clock_4_out, clock_5_out, clock_6_out, clock_7_out,
       clock_8_out, clock_9_out, clock_10_out, comparator_1_eq, comparator_2_eq, comparator_3_eq,
       comparator_4_eq, comparator_5_eq, comparator_6_eq, comparator_7_eq, comparator_8_eq,
       controlled_buffer_2_out, controlled_buffer_3_out, controlled_buffer_4_out, counter_3_carry,
       counter_5_carry, FF, FV, H9, not_1_out, not_2_out, not_3_out, not_4_out, not_5_out, not_6_out,
       not_7_out, not_8_out, not_9_out, not_10_out, not_11_out, or_1_out, or_2_out, or_3_out, or_5_out,
       or_6_out, or_7_out, or_8_out, or_9_out, or_10_out, or_11_out, or_12_out, or_13_out, or_14_out,
       or_15_out, pull_resistor_4_node, pull_resistor_8_node, pull_resistor_10_node, pull_resistor_11_node,
       S1, S4, Z1, Z2, Z4, Z5;
  wire [1:0] and_2_out, counter_4_q, ZEGAR_t;
  wire [1:1] K1;
  wire [2:0] uklad_zmiany_sterowania_z_3bit_na_5bit_1_out_x__3bit,
       uklad_zmiany_sterowania_z_3bit_na_5bit_1_out_y_3bit;
  wire [3:0] adder_1_out, adder_2_out, adder_3_out, adder_4_out, adder_5_out, adder_6_out, adder_7_out,
       counter_6_q, counter_7_q, counter_8_q, counter_9_q, counter_10_q, counter_11_q, counter_12_q,
       counter_13_q;
  wire [4:0] counter_14_q, WARTOS;
  wire [5:0] controlled_buffer_9_out, D1, D2, D3, D4, D5, D6, D7, D8, DRI;
  wire [9:0] DOMAPY;

  Pull_Resistor pull_resistor_1 (.node(Z2));
  assign Z2 = FV ? S1 : 1'bz;  // Controlled_Buffer controlled_buffer_1
  Clock clock_1 (.out(clock_1_out));
  Clock clock_2 (.out(clock_2_out));
  Clock clock_3 (.out(clock_3_out));
  Clock clock_4 (.out(clock_4_out));
  Clock clock_5 (.out(clock_5_out));
  not not_1 (not_1_out, START);
  assign controlled_buffer_2_out = not_1_out ? clock_1_out : 1'bz;  // Controlled_Buffer controlled_buffer_2
  S_R_Flip_Flop s_r_ff_1 (.S(S1), .clk(clock_2_out), .R(START), .Q(K1[1]));  // open: Qn, preset, reset, en
  not not_2 (not_2_out, Z2);
  assign controlled_buffer_3_out = not_2_out ? clock_3_out : 1'bz;  // Controlled_Buffer controlled_buffer_3
  S_R_Flip_Flop s_r_ff_2 (.S(H9), .clk(clock_4_out), .R(Z2), .Q(Z5));  // open: Qn, preset, reset, en
  S_R_Flip_Flop s_r_ff_3 (.S(START), .clk(clock_5_out), .R(S1), .Q(FV));  // open: Qn, preset, reset, en
  Pull_Resistor pull_resistor_2 (.node(controlled_buffer_2_out));
  nand nand_1 (S4, controlled_buffer_2_out, ~K1[1]);  // NAND_Gate
  Pull_Resistor pull_resistor_3 (.node(controlled_buffer_3_out));
  and and_1 (Z4, controlled_buffer_3_out, ~Z5);  // AND_Gate
  Counter #(.width(4), .max('h8), .trigger("falling")) counter_1 (
    .load(1'b1), .D(4'b1000), .count(FF), .carry(S1), .clk(or_3_out));  // open: Q, clr
  assign controlled_buffer_4_out = not_3_out ? S4 : 1'bz;  // Controlled_Buffer controlled_buffer_4
  not not_3 (not_3_out, RESET);
  Counter #(.width(5), .max('h1b), .trigger("falling")) counter_2 (
    .load(1'b1), .D(5'b11011), .count(FF), .Q(WARTOS), .carry(H9), .clk(or_1_out));  // open: clr
  or or_1 (or_1_out, Z2, pull_resistor_8_node, Z1);
  Counter #(.width(4), .max('h4), .trigger("falling")) counter_3 (
    .load(1'b1), .D(4'b0100), .count(FF), .carry(counter_3_carry), .clk(or_2_out));  // open: Q, clr
  not not_4 (not_4_out, RESET);
  or or_2 (or_2_out, Z4, pull_resistor_8_node);
  or or_3 (or_3_out, controlled_buffer_4_out, pull_resistor_4_node);
  Pull_Resistor pull_resistor_4 (.node(pull_resistor_4_node));
  assign pull_resistor_4_node = RESET ? clock_6_out : 1'bz;  // Controlled_Buffer controlled_buffer_5
  Pull_Resistor pull_resistor_5 (.node(controlled_buffer_4_out));
  Clock clock_6 (.out(clock_6_out));
  Pull_Resistor pull_resistor_6 (.node(Z1));
  assign Z1 = not_4_out ? counter_3_carry : 1'bz;  // Controlled_Buffer controlled_buffer_6
  Pull_Resistor pull_resistor_7 (.node(Z1));
  assign and_2_out = ZEGAR & ~{2{K1[1]}};  // AND_Gate and_2, 2 bits wide
  assign ZEGAR_t = and_2_out | counter_4_q;  // OR_Gate or_4, 2 bits wide
  and and_3 (and_3_out, ~K1[1], S4);  // AND_Gate
  Pull_Resistor pull_resistor_8 (.node(pull_resistor_8_node));
  assign pull_resistor_8_node = RESET ? clock_7_out : 1'bz;  // Controlled_Buffer controlled_buffer_7
  Clock clock_7 (.out(clock_7_out));
  Counter #(.width(2), .max('h2), .ongoal("continue"), .trigger("falling")) counter_4 (
    .Q(counter_4_q), .clk(Z4), .clr(Z5));  // open: load, D, count, carry
  Clock clock_8 (.out(clock_8_out));
  not not_5 (not_5_out, and_3_out);
  Uklad_zwracania_pozycji_sasiednich_bitow uklad_zwracania_pozycji_sasiednich_bitow_1 (
    .Input_Y(DOMAPY[4:0]), .Input_X(DOMAPY[9:5]), .LG(D1), .G(D2), .P(D4), .DP(D5), .D(D6), .LD(D7), .L(D8),
    .PG(D3));  // open: O_X, O_Y
  // BOOMBOX_main main_1: pin names not known; wires that end beside it: ZEGAR_t, DANE, START, ENTER, RESET, WYBUCH, {X, Y}
  RAM #(.addrWidth(2), .dataWidth(6), .bus("separate")) ram_1 (
    .addr(ZEGAR_t), .din(DANE), .data(DRI), .str(and_3_out), .sel(1'b1), .clk(clock_8_out), .ld(not_5_out),
    .clr(or_5_out));
  or or_5 (or_5_out, RESET, START);
  Counter #(.width(4), .max('h1), .ongoal("stay"), .trigger("falling")) counter_5 (
    .carry(counter_5_carry), .clk(pull_resistor_8_node), .clr(START));  // open: load, D, count, Q
  not not_6 (not_6_out, counter_5_carry);
  assign FF = not_6_out ? not_7_out : 1'bz;  // Controlled_Buffer controlled_buffer_8
  not not_7 (not_7_out, RESET);
  Pull_Resistor pull_resistor_9 (.node(FF));
  Counter #(.width(4), .max('hf), .trigger("falling")) counter_6 (
    .Q(counter_6_q), .clk(comparator_1_eq), .clr(or_6_out));  // open: load, D, count, carry
  Comparator #(.width(6), .mode("unsigned")) comparator_1 (.a(D1), .b(DRI), .eq(comparator_1_eq));  // open: gt, lt
  Counter #(.width(4), .max('hf), .trigger("falling")) counter_7 (
    .Q(counter_7_q), .clk(comparator_2_eq), .clr(or_7_out));  // open: load, D, count, carry
  Comparator #(.width(6), .mode("unsigned")) comparator_2 (.a(D2), .b(DRI), .eq(comparator_2_eq));  // open: gt, lt
  Counter #(.width(4), .max('hf), .trigger("falling")) counter_8 (
    .Q(counter_8_q), .clk(comparator_3_eq), .clr(or_8_out));  // open: load, D, count, carry
  Comparator #(.width(6), .mode("unsigned")) comparator_3 (.a(D3), .b(DRI), .eq(comparator_3_eq));  // open: gt, lt
  Counter #(.width(4), .max('hf), .trigger("falling")) counter_9 (
    .Q(counter_9_q), .clk(comparator_4_eq), .clr(or_9_out));  // open: load, D, count, carry
  Comparator #(.width(6), .mode("unsigned")) comparator_4 (.a(D4), .b(DRI), .eq(comparator_4_eq));  // open: gt, lt
  Counter #(.width(4), .max('hf), .trigger("falling")) counter_10 (
    .Q(counter_10_q), .clk(comparator_5_eq), .clr(or_10_out));  // open: load, D, count, carry
  Comparator #(.width(6), .mode("unsigned")) comparator_5 (.a(D5), .b(DRI), .eq(comparator_5_eq));  // open: gt, lt
  Counter #(.width(4), .max('hf), .trigger("falling")) counter_11 (
    .Q(counter_11_q), .clk(comparator_6_eq), .clr(or_11_out));  // open: load, D, count, carry
  Comparator #(.width(6), .mode("unsigned")) comparator_6 (.a(D6), .b(DRI), .eq(comparator_6_eq));  // open: gt, lt
  Counter #(.width(4), .max('hf), .trigger("falling")) counter_12 (
    .Q(counter_12_q), .clk(comparator_7_eq), .clr(or_12_out));  // open: load, D, count, carry
  Comparator #(.width(6), .mode("unsigned")) comparator_7 (.a(D7), .b(DRI), .eq(comparator_7_eq));  // open: gt, lt
  Counter #(.width(4), .max('hf), .trigger("falling")) counter_13 (
    .Q(counter_13_q), .clk(comparator_8_eq), .clr(or_13_out));  // open: load, D, count, carry
  Comparator #(.width(6), .mode("unsigned")) comparator_8 (.a(D8), .b(DRI), .eq(comparator_8_eq));  // open: gt, lt
  or or_6 (or_6_out, Z2, Z1);
  or or_7 (or_7_out, Z2, Z1);
  or or_8 (or_8_out, Z2, Z1);
  or or_9 (or_9_out, Z2, Z1);
  or or_10 (or_10_out, Z2, Z1);
  or or_11 (or_11_out, Z2, Z1);
  or or_12 (or_12_out, Z2, Z1);
  or or_13 (or_13_out, Z2, Z1);
  Adder #(.width(4)) adder_1 (.a(counter_6_q), .b(counter_7_q), .out(adder_1_out));  // open: cin, cout
  Adder #(.width(4)) adder_2 (.a(counter_8_q), .b(counter_9_q), .out(adder_2_out));  // open: cin, cout
  Adder #(.width(4)) adder_3 (.a(counter_10_q), .b(counter_11_q), .out(adder_3_out));  // open: cin, cout
  Adder #(.width(4)) adder_4 (.a(counter_12_q), .b(counter_13_q), .out(adder_4_out));  // open: cin, cout
  Uklad_zmiany_sterowania_z_3bit_na_5bit uklad_zmiany_sterowania_z_3bit_na_5bit_1 (
    .IN_X_5bit(DOMAPY[4:0]), .IN_Y_5bit(DOMAPY[9:5]),
    .OUT_X__3bit(uklad_zmiany_sterowania_z_3bit_na_5bit_1_out_x__3bit),
    .OUT_Y_3bit(uklad_zmiany_sterowania_z_3bit_na_5bit_1_out_y_3bit));
  Adder #(.width(4)) adder_5 (.a(adder_1_out), .b(adder_2_out), .out(adder_5_out));  // open: cin, cout
  assign controlled_buffer_9_out = H9 ? {Y, X} : 6'bz;  // Controlled_Buffer controlled_buffer_9
  assign controlled_buffer_9_out = not_8_out ? {uklad_zmiany_sterowania_z_3bit_na_5bit_1_out_y_3bit, uklad_zmiany_sterowania_z_3bit_na_5bit_1_out_x__3bit} : 6'bz;  // Controlled_Buffer controlled_buffer_10
  not not_8 (not_8_out, H9);
  Adder #(.width(4)) adder_6 (.a(adder_3_out), .b(adder_4_out), .out(adder_6_out));  // open: cin, cout
  Adder #(.width(4)) adder_7 (.a(adder_5_out), .b(adder_6_out), .out(adder_7_out));  // open: cin, cout
  Pull_Resistor pull_resistor_10 (.node(pull_resistor_10_node));
  assign pull_resistor_10_node = not_10_out ? not_9_out : 1'bz;  // Controlled_Buffer controlled_buffer_11
  not not_9 (not_9_out, Z5);
  not not_10 (not_10_out, H9);
  Clock clock_9 (.out(clock_9_out));
  not not_11 (not_11_out, pull_resistor_10_node);
  Counter #(.width(5), .max('h1b)) counter_14 (
    .load(RESET), .D(5'b00001), .count(FF), .Q(counter_14_q), .clk(or_15_out));  // open: carry, clr
  RAM #(.addrWidth(6), .dataWidth(4), .bus("separate")) ram_2 (
    .addr(controlled_buffer_9_out), .din(adder_7_out), .data(DANE_2), .str(pull_resistor_10_node),
    .sel(1'b1), .clk(clock_9_out), .clr(or_14_out));  // open: ld
  or or_14 (or_14_out, RESET, START);
  or or_15 (or_15_out, Z1, pull_resistor_11_node, Z2);
  Pull_Resistor pull_resistor_11 (.node(pull_resistor_11_node));
  assign pull_resistor_11_node = RESET ? clock_10_out : 1'bz;  // Controlled_Buffer controlled_buffer_12
  Clock clock_10 (.out(clock_10_out));
  Multiplexer #(.select(5), .width(10)) multiplexer_1 (
    .in2(10'h210), .in3(10'h110), .in4(10'h90), .in5(10'h50), .in6(10'h30), .in7(10'h208), .in8(10'h108),
    .in9(10'h88), .in10(10'h48), .in11(10'h28), .in12(10'h204), .in13(10'h104), .in14(10'h84), .in15(10'h44),
    .in16(10'h24), .in17(10'h202), .in18(10'h102), .in19(10'h82), .in20(10'h42), .in21(10'h22),
    .in22(10'h201), .in23(10'h101), .in24(10'h81), .in25(10'h41), .in26(10'h21), .out(DOMAPY),
    .sel(counter_14_q));  // open: in0, in1, in27, in28, in29, in30, in31, en

  // Other names for the same wires on the sheet: WSPŁ[5:0] = {Y, X}; X5[4:0] = DOMAPY[4:0]; Y5[4:0] = DOMAPY[9:5];
  //   K1[0] = K1[1]; S5 = K1[1]; S2 = START; uV1 = RESET

  // Notes on the sheet:
  //   wypisywanie pul
  //   BOOMBOX
endmodule
