// Logisim project ukadtest4.circ as structural Verilog: 1 circuit, main circuit main
module main (
  input  [3:0] _15,
  input  [3:0] _14,
  input  [3:0] _13,
  input  [3:0] _12,
  input  [3:0] _11,
  input  [3:0] in_6,
  input  [3:0] in_7,
  input  [3:0] in_8,
  input  [3:0] in_9,
  input  [3:0] in_10,
  input  [3:0] in_11,
  input  [3:0] in_12,
  input  [3:0] in_13,
  input  [3:0] in_14,
  input  [3:0] in_15,
  input  [3:0] in_16,
  input  [3:0] in_17,
  input  [3:0] in_18,
  input  [3:0] in_19,
  input  [3:0] in_20,
  input  [3:0] in_21,
  input  [3:0] in_22,
  input  [3:0] in_23,
  input  [3:0] in_24,
  input  [3:0] in_25,
  input  [24:0] \pamięć ,
  input  [24:0] wy,
  input  przycisk,
  input  RESET,
  output [30:0] out_30,
  output [30:0] out_31,
  output [30:0] out_32,
  output [30:0] out_33,
  output [30:0] out_34,
  output [30:0] out_35,
  output [30:0] out_36,
  output [30:0] out_37,
  output [30:0] out_38,
  output [30:0] out_39,
  output [30:0] out_40,
  output [30:0] out_41,
  output [30:0] out_42,
  output [30:0] out_43,
  output [30:0] out_44,
  output [30:0] out_45,
  output [30:0] out_46,
  output [30:0] out_47,
  output [30:0] out_48,
  output [30:0] out_49,
  output [30:0] out_50,
  output [30:0] out_51,
  output [30:0] out_52,
  output [30:0] out_53,
  output [30:0] out_54,
  output [30:0] out_55,
  output [30:0] out_56,
  output [30:0] out_57,
  output [30:0] out_58,
  output [30:0] out_59,
  output [30:0] out_60,
  output [4:0] out_61,
  output [24:0] we,
  output Win
);

  wire d_ff_1_q, d_ff_2_q, d_ff_3_q, d_ff_4_q, d_ff_5_q, d_ff_6_q, d_ff_7_q, d_ff_8_q, d_ff_9_q, d_ff_10_q,
       d_ff_11_q, d_ff_12_q, d_ff_13_q, d_ff_14_q, d_ff_15_q, d_ff_16_q, d_ff_17_q, d_ff_18_q, d_ff_19_q,
       d_ff_20_q, d_ff_21_q, d_ff_22_q, d_ff_23_q, d_ff_24_q, d_ff_25_q;
  wire [3:0] main_1_wy, main_2_wy, main_3_wy, main_4_wy, main_5_wy, main_6_wy, main_7_wy, main_8_wy,
       main_9_wy, main_10_wy, main_11_wy, main_12_wy, main_13_wy, main_14_wy, main_15_wy, main_16_wy,
       main_17_wy, main_18_wy, main_19_wy, main_20_wy, main_21_wy, main_22_wy, main_23_wy, main_24_wy,
       main_25_wy;
  wire [24:0] or_25_out;

  assign we = ~\pamięć ;  // NOT_Gate not_1, 25 bits wide
  D_Flip_Flop d_ff_1 (.clk(wy[0]), .D(1'b1), .Q(d_ff_1_q), .reset(RESET));  // open: Qn, preset, en
  D_Flip_Flop d_ff_2 (.clk(wy[1]), .D(1'b1), .Q(d_ff_2_q), .reset(RESET));  // open: Qn, preset, en
  D_Flip_Flop d_ff_3 (.clk(wy[2]), .D(1'b1), .Q(d_ff_3_q), .reset(RESET));  // open: Qn, preset, en
  D_Flip_Flop d_ff_4 (.clk(wy[3]), .D(1'b1), .Q(d_ff_4_q), .reset(RESET));  // open: Qn, preset, en
  D_Flip_Flop d_ff_5 (.clk(wy[4]), .D(1'b1), .Q(d_ff_5_q), .reset(RESET));  // open: Qn, preset, en
  D_Flip_Flop d_ff_6 (.clk(wy[5]), .D(1'b1), .Q(d_ff_6_q), .reset(RESET));  // open: Qn, preset, en
  D_Flip_Flop d_ff_7 (.clk(wy[6]), .D(1'b1), .Q(d_ff_7_q), .reset(RESET));  // open: Qn, preset, en
  D_Flip_Flop d_ff_8 (.clk(wy[7]), .D(1'b1), .Q(d_ff_8_q), .reset(RESET));  // open: Qn, preset, en
  D_Flip_Flop d_ff_9 (.clk(wy[8]), .D(1'b1), .Q(d_ff_9_q), .reset(RESET));  // open: Qn, preset, en
  D_Flip_Flop d_ff_10 (.clk(wy[9]), .D(1'b1), .Q(d_ff_10_q), .reset(RESET));  // open: Qn, preset, en
  D_Flip_Flop d_ff_11 (.clk(wy[10]), .D(1'b1), .Q(d_ff_11_q), .reset(RESET));  // open: Qn, preset, en
  D_Flip_Flop d_ff_12 (.clk(wy[11]), .D(1'b1), .Q(d_ff_12_q), .reset(RESET));  // open: Qn, preset, en
  D_Flip_Flop d_ff_13 (.clk(wy[12]), .D(1'b1), .Q(d_ff_13_q), .reset(RESET));  // open: Qn, preset, en
  D_Flip_Flop d_ff_14 (.clk(wy[13]), .D(1'b1), .Q(d_ff_14_q), .reset(RESET));  // open: Qn, preset, en
  D_Flip_Flop d_ff_15 (.clk(wy[14]), .D(1'b1), .Q(d_ff_15_q), .reset(RESET));  // open: Qn, preset, en
  D_Flip_Flop d_ff_16 (.clk(wy[15]), .D(1'b1), .Q(d_ff_16_q), .reset(RESET));  // open: Qn, preset, en
  D_Flip_Flop d_ff_17 (.clk(wy[16]), .D(1'b1), .Q(d_ff_17_q), .reset(RESET));  // open: Qn, preset, en
  D_Flip_Flop d_ff_18 (.clk(wy[17]), .D(1'b1), .Q(d_ff_18_q), .reset(RESET));  // open: Qn, preset, en
  D_Flip_Flop d_ff_19 (.clk(wy[18]), .D(1'b1), .Q(d_ff_19_q), .reset(RESET));  // open: Qn, preset, en
  D_Flip_Flop d_ff_20 (.clk(wy[19]), .D(1'b1), .Q(d_ff_20_q), .reset(RESET));  // open: Qn, preset, en
  D_Flip_Flop d_ff_21 (.clk(wy[20]), .D(1'b1), .Q(d_ff_21_q), .reset(RESET));  // open: Qn, preset, en
  D_Flip_Flop d_ff_22 (.clk(wy[21]), .D(1'b1), .Q(d_ff_22_q), .reset(RESET));  // open: Qn, preset, en
  D_Flip_Flop d_ff_23 (.clk(wy[22]), .D(1'b1), .Q(d_ff_23_q), .reset(RESET));  // open: Qn, preset, en
  D_Flip_Flop d_ff_24 (.clk(wy[23]), .D(1'b1), .Q(d_ff_24_q), .reset(RESET));  // open: Qn, preset, en
  D_Flip_Flop d_ff_25 (.clk(wy[24]), .D(1'b1), .Q(d_ff_25_q), .reset(RESET));  // open: Qn, preset, en
  or or_1 (or_25_out[24], d_ff_1_q, przycisk);
  or or_2 (or_25_out[23], d_ff_2_q, przycisk);
  or or_3 (or_25_out[22], d_ff_3_q, przycisk);
  or or_4 (or_25_out[21], d_ff_4_q, przycisk);
  or or_5 (or_25_out[20], d_ff_5_q, przycisk);
  or or_6 (or_25_out[19], d_ff_6_q, przycisk);
  or or_7 (or_25_out[18], d_ff_7_q, przycisk);
  or or_8 (or_25_out[17], d_ff_8_q, przycisk);
  or or_9 (or_25_out[16], d_ff_9_q, przycisk);
  or or_10 (or_25_out[15], d_ff_10_q, przycisk);
  or or_11 (or_25_out[14], d_ff_11_q, przycisk);
  or or_12 (or_25_out[13], d_ff_12_q, przycisk);
  or or_13 (or_25_out[12], d_ff_13_q, przycisk);
  or or_14 (or_25_out[11], d_ff_14_q, przycisk);
  or or_15 (or_25_out[10], d_ff_15_q, przycisk);
  or or_16 (or_25_out[9], d_ff_16_q, przycisk);
  or or_17 (or_25_out[8], d_ff_17_q, przycisk);
  or or_18 (or_25_out[7], d_ff_18_q, przycisk);
  or or_19 (or_25_out[6], d_ff_19_q, przycisk);
  or or_20 (or_25_out[5], d_ff_20_q, przycisk);
  or or_21 (or_25_out[4], d_ff_21_q, przycisk);
  or or_22 (or_25_out[3], d_ff_22_q, przycisk);
  or or_23 (or_25_out[2], d_ff_23_q, przycisk);
  or or_24 (or_25_out[1], d_ff_24_q, przycisk);
  or or_25 (or_25_out[0], d_ff_25_q, przycisk);
  BitAdder #(.width(25)) bitadder_1 (.in0(or_25_out), .out(out_61));
  bramka_main main_1 (.Wl_WY(or_25_out[11]), .WY(main_1_wy), .WE(in_14));
  Comparator #(.width(5)) comparator_1 (.a(out_61), .b(5'b10101), .eq(Win));  // open: gt, lt
  bramka_main main_2 (.Wl_WY(or_25_out[24]), .WY(main_2_wy), .WE(_15));
  bramka_main main_3 (.Wl_WY(or_25_out[23]), .WY(main_3_wy), .WE(_14));
  bramka_main main_4 (.Wl_WY(or_25_out[22]), .WY(main_4_wy), .WE(_13));
  bramka_main main_5 (.Wl_WY(or_25_out[21]), .WY(main_5_wy), .WE(_12));
  bramka_main main_6 (.Wl_WY(or_25_out[12]), .WY(main_6_wy), .WE(in_13));
  bramka_main main_7 (.Wl_WY(or_25_out[9]), .WY(main_7_wy), .WE(in_16));
  bramka_main main_8 (.Wl_WY(or_25_out[8]), .WY(main_8_wy), .WE(in_17));
  bramka_main main_9 (.Wl_WY(or_25_out[7]), .WY(main_9_wy), .WE(in_18));
  bramka_main main_10 (.Wl_WY(or_25_out[20]), .WY(main_10_wy), .WE(_11));
  bramka_main main_11 (.Wl_WY(or_25_out[19]), .WY(main_11_wy), .WE(in_6));
  bramka_main main_12 (.Wl_WY(or_25_out[18]), .WY(main_12_wy), .WE(in_7));
  bramka_main main_13 (.Wl_WY(or_25_out[17]), .WY(main_13_wy), .WE(in_8));
  bramka_main main_14 (.Wl_WY(or_25_out[13]), .WY(main_14_wy), .WE(in_12));
  bramka_main main_15 (.Wl_WY(or_25_out[6]), .WY(main_15_wy), .WE(in_19));
  bramka_main main_16 (.Wl_WY(or_25_out[5]), .WY(main_16_wy), .WE(in_20));
  bramka_main main_17 (.Wl_WY(or_25_out[16]), .WY(main_17_wy), .WE(in_9));
  bramka_main main_18 (.Wl_WY(or_25_out[15]), .WY(main_18_wy), .WE(in_10));
  bramka_main main_19 (.Wl_WY(or_25_out[14]), .WY(main_19_wy), .WE(in_11));
  bramka_main main_20 (.Wl_WY(or_25_out[10]), .WY(main_20_wy), .WE(in_15));
  bramka_main main_21 (.Wl_WY(or_25_out[4]), .WY(main_21_wy), .WE(in_21));
  bramka_main main_22 (.Wl_WY(or_25_out[3]), .WY(main_22_wy), .WE(in_22));
  bramka_main main_23 (.Wl_WY(or_25_out[2]), .WY(main_23_wy), .WE(in_23));
  bramka_main main_24 (.Wl_WY(or_25_out[1]), .WY(main_24_wy), .WE(in_24));
  bramka_main main_25 (.Wl_WY(or_25_out[0]), .WY(main_25_wy), .WE(in_25));
  \Układ_wyświetlania_3_main  main_26 (
    .in_1({31{1'b0}}), ._15(main_2_wy), ._14(main_3_wy), ._13(main_4_wy), ._12(main_5_wy), ._11(main_10_wy),
    .in_7(main_11_wy), .in_8(main_12_wy), .in_9(main_13_wy), .in_10(main_17_wy), .in_11(main_18_wy),
    .in_12(main_19_wy), .in_13(main_14_wy), .in_14(main_6_wy), .in_15(main_1_wy), .in_16(main_20_wy),
    .in_17(\pamięć ), .in_18(main_7_wy), .in_19(main_8_wy), .in_20(main_9_wy), .in_21(main_15_wy),
    .in_22(main_16_wy), .in_23(main_21_wy), .in_24(main_22_wy), .in_25(main_23_wy), .in_26(main_24_wy),
    .in_27(main_25_wy), .out_28(out_30), .out_29(out_31), .out_30(out_32), .out_31(out_33), .out_32(out_34),
    .out_33(out_35), .out_34(out_36), .out_35(out_37), .out_36(out_38), .out_37(out_39), .out_38(out_40),
    .out_39(out_41), .out_40(out_42), .out_41(out_43), .out_42(out_44), .out_43(out_45), .out_44(out_46),
    .out_45(out_47), .out_46(out_48), .out_47(out_49), .out_48(out_50), .out_49(out_51), .out_50(out_52),
    .out_51(out_53), .out_52(out_54), .out_53(out_55), .out_54(out_56), .out_55(out_57), .out_56(out_58),
    .out_57(out_59), .out_58(out_60));

  // Other names for the same wires on the sheet: R1 = RESET
endmodule
