// Logisim project Komparator 7bit (tylko czy rowna).circ as structural Verilog: 1 circuit, main circuit main
module main (
  input  [6:0] A,
  input  [6:0] B,
  output _1_oznacza_ze_jest_rowne
);

  wire main_1_a___b_3, main_2_a___b_3, main_3_a___b_3, main_4_a___b_3, main_5_a___b_3, main_6_a___b_3;

  komparator_1_bitowy_main main_1 (.A(A[6]), .B(B[6]), .in_3(1'b1), .A___B_3(main_1_a___b_3));  // open: A___B, A___B_2
  komparator_1_bitowy_main main_2 (
    .A(A[5]), .B(B[5]), .in_3(main_1_a___b_3), .A___B_3(main_2_a___b_3));  // open: A___B, A___B_2
  komparator_1_bitowy_main main_3 (
    .A(A[4]), .B(B[4]), .in_3(main_2_a___b_3), .A___B_3(main_3_a___b_3));  // open: A___B, A___B_2
  komparator_1_bitowy_main main_4 (
    .A(A[3]), .B(B[3]), .in_3(main_3_a___b_3), .A___B_3(main_4_a___b_3));  // open: A___B, A___B_2
  komparator_1_bitowy_main main_5 (
    .A(A[2]), .B(B[2]), .in_3(main_4_a___b_3), .A___B_3(main_5_a___b_3));  // open: A___B, A___B_2
  komparator_1_bitowy_main main_6 (
    .A(A[1]), .B(B[1]), .in_3(main_5_a___b_3), .A___B_3(main_6_a___b_3));  // open: A___B, A___B_2
  komparator_1_bitowy_main main_7 (
    .A(A[0]), .B(B[0]), .in_3(main_6_a___b_3), .A___B_3(_1_oznacza_ze_jest_rowne));  // open: A___B, A___B_2
endmodule
