// Logisim project blok wyboru focusu.circ as structural Verilog: 1 circuit, main circuit main
module main (
  input  [6:0] Wejscie_z_klawiatury,
  output [15:0] Numer_matrycy
);

  wire main_1_przemiesc_kursor;
  wire [1:0] rom_1_data;
  wire [2:0] main_1__1_a_2_s_3_d_4_w_5_enter;
  wire [3:0] main_2_podaje_numer_pola__0_15;

  blok_sterowania_main main_1 (
    .\input (Wejscie_z_klawiatury), ._1_a_2_s_3_d_4_w_5_enter(main_1__1_a_2_s_3_d_4_w_5_enter),
    .przemiesc_kursor(main_1_przemiesc_kursor));
  ROM #(.addrWidth(3), .dataWidth(2)) rom_1 (.addr(main_1__1_a_2_s_3_d_4_w_5_enter), .data(rom_1_data));  // open: sel
  uklad_przejscia_main main_2 (
    .wejscie_sterowania__wdsa___0_1_2_3(rom_1_data), .CLK(main_1_przemiesc_kursor),
    .podaje_numer_pola__0_15(main_2_podaje_numer_pola__0_15));
  ROM #(.addrWidth(4), .dataWidth(16)) rom_2 (
    .addr(main_2_podaje_numer_pola__0_15), .data(Numer_matrycy));  // open: sel

  // Notes on the sheet:
  //   contents of rom_1 (hex, n*v repeats v):
  //   0 3 2 1
  //   contents of rom_2 (hex, n*v repeats v):
  //   1 2 4 8 10 20 10 40
endmodule
