// Logisim project uklad przejscia.circ as structural Verilog: 1 circuit, main circuit main
module main (
  input  [1:0] wejscie_sterowania__wdsa___0_1_2_3,
  input  CLK,
  output [3:0] podaje_numer_pola__0_15
);

  wire [3:0] rom_1_data;

  ROM #(.addrWidth(6), .dataWidth(4)) rom_1 (
    .addr({podaje_numer_pola__0_15, wejscie_sterowania__wdsa___0_1_2_3}), .data(rom_1_data));  // open: sel
  Register #(.width(4), .trigger("falling")) register_1 (
    .D(rom_1_data), .Q(podaje_numer_pola__0_15), .clk(CLK));  // open: en, clr

  // Notes on the sheet:
  //   contents of rom_1 (hex, n*v repeats v):
  //   0 1 4 0 1 2 5 0 2 3 6 1 3 3 7 2 0 5 8 4 1 6 9 4 2 7 a 5 3 7 b 6 4 9 c 8 5 a d 8 6 b e 9 7 b f a 8 d
  //   c c 9 e d c a f e d b f f e
endmodule
