// Logisim project Sterowanie.circ as structural Verilog: 7 circuits, main circuit Sterowanie z klawiatury
module Sterowanie_z_klawiatury (
  input  [6:0] \input ,
  output [2:0] _3_a_4_s_1_d_6_w_5_enter,
  output przemiesc_kursor
);

  wire komparator_7bit_do_sterowania_1__1_oznacza_ze_jest_rowne,
       komparator_7bit_do_sterowania_2__1_oznacza_ze_jest_rowne,
       komparator_7bit_do_sterowania_3__1_oznacza_ze_jest_rowne,
       komparator_7bit_do_sterowania_4__1_oznacza_ze_jest_rowne,
       komparator_7bit_do_sterowania_6__1_oznacza_ze_jest_rowne,
       komparator_7bit_do_sterowania_7__1_oznacza_ze_jest_rowne,
       komparator_7bit_do_sterowania_8__1_oznacza_ze_jest_rowne,
       komparator_7bit_do_sterowania_9__1_oznacza_ze_jest_rowne;
  wire [4:0] or_1_out;

  Komparator_7bit_do_sterowania komparator_7bit_do_sterowania_1 (
    .A(\input ), .B(7'b1100001),
    ._1_oznacza_ze_jest_rowne(komparator_7bit_do_sterowania_1__1_oznacza_ze_jest_rowne));
  Komparator_7bit_do_sterowania komparator_7bit_do_sterowania_2 (
    .A(\input ), .B(7'b1110011),
    ._1_oznacza_ze_jest_rowne(komparator_7bit_do_sterowania_2__1_oznacza_ze_jest_rowne));
  Komparator_7bit_do_sterowania komparator_7bit_do_sterowania_3 (
    .A(\input ), .B(7'b1100100),
    ._1_oznacza_ze_jest_rowne(komparator_7bit_do_sterowania_3__1_oznacza_ze_jest_rowne));
  Komparator_7bit_do_sterowania komparator_7bit_do_sterowania_4 (
    .A(\input ), .B(7'b1110111),
    ._1_oznacza_ze_jest_rowne(komparator_7bit_do_sterowania_4__1_oznacza_ze_jest_rowne));
  Komparator_7bit_do_sterowania komparator_7bit_do_sterowania_5 (
    .A(\input ), .B(7'b0001010), ._1_oznacza_ze_jest_rowne(or_1_out[4]));
  Komparator_7bit_do_sterowania komparator_7bit_do_sterowania_6 (
    .A(\input ), .B(7'b1000001),
    ._1_oznacza_ze_jest_rowne(komparator_7bit_do_sterowania_6__1_oznacza_ze_jest_rowne));
  Komparator_7bit_do_sterowania komparator_7bit_do_sterowania_7 (
    .A(\input ), .B(7'b1010011),
    ._1_oznacza_ze_jest_rowne(komparator_7bit_do_sterowania_7__1_oznacza_ze_jest_rowne));
  Komparator_7bit_do_sterowania komparator_7bit_do_sterowania_8 (
    .A(\input ), .B(7'b1000100),
    ._1_oznacza_ze_jest_rowne(komparator_7bit_do_sterowania_8__1_oznacza_ze_jest_rowne));
  Komparator_7bit_do_sterowania komparator_7bit_do_sterowania_9 (
    .A(\input ), .B(7'b1010111),
    ._1_oznacza_ze_jest_rowne(komparator_7bit_do_sterowania_9__1_oznacza_ze_jest_rowne));
  or or_1 (or_1_out[0], komparator_7bit_do_sterowania_1__1_oznacza_ze_jest_rowne, komparator_7bit_do_sterowania_6__1_oznacza_ze_jest_rowne);
  or or_2 (or_1_out[1], komparator_7bit_do_sterowania_2__1_oznacza_ze_jest_rowne, komparator_7bit_do_sterowania_7__1_oznacza_ze_jest_rowne);
  or or_3 (or_1_out[2], komparator_7bit_do_sterowania_3__1_oznacza_ze_jest_rowne, komparator_7bit_do_sterowania_8__1_oznacza_ze_jest_rowne);
  or or_4 (or_1_out[3], komparator_7bit_do_sterowania_4__1_oznacza_ze_jest_rowne, komparator_7bit_do_sterowania_9__1_oznacza_ze_jest_rowne);
  or or_5 (przemiesc_kursor, or_1_out[0], or_1_out[1], or_1_out[2], or_1_out[3]);
  ROM #(.addrWidth(5), .dataWidth(3)) rom_1 (.addr(or_1_out), .data(_3_a_4_s_1_d_6_w_5_enter));  // open: sel

  // Notes on the sheet:
  //   contents of rom_1 (hex, n*v repeats v):
  //   0 3 4 0 1 0 0 0 6 7*0 5
endmodule

module uklad_zwracajacy_pozycje (
  input  [2:0] Sterowanie,
  input  Move,
  output [4:0] Poz_X,
  output [4:0] Poz_Y
);

  wire and_1_out, buffer_1_out, buffer_2_out, buffer_3_out, not_1_out;
  wire [2:0] counter_1_q, counter_2_q;

  not not_1 (not_1_out, Sterowanie[0]);
  buf buffer_1 (buffer_1_out, Sterowanie[1]);
  Counter #(.width(3), .max('h4), .trigger("falling")) counter_1 (
    .load(Sterowanie[1]), .D(counter_1_q), .count(Sterowanie[0]), .Q(counter_1_q), .clk(buffer_2_out));  // open: carry, clr
  buf buffer_2 (buffer_2_out, Move);
  Counter #(.width(3), .max('h4), .trigger("falling")) counter_2 (
    .load(buffer_1_out), .D(counter_2_q), .count(and_1_out), .Q(counter_2_q), .clk(buffer_3_out));  // open: carry, clr
  buf buffer_3 (buffer_3_out, Move);
  and and_1 (and_1_out, not_1_out, Sterowanie[2]);
  Shifter #(.width(5), .shift("rr")) shifter_1 (.in(5'b10000), .\dist (counter_1_q), .out(Poz_X));
  Shifter #(.width(5), .shift("rr")) shifter_2 (.in(5'b10000), .\dist (counter_2_q), .out(Poz_Y));

  // Other names for the same wires on the sheet: Control[2:0] = Sterowanie; M = Move
endmodule

module Uklad_zmiany_sterowania_z_3bit_na_5bit (
  input  [4:0] IN_X_5bit,
  input  [4:0] IN_Y_5bit,
  output [2:0] OUT_X__3bit,
  output [2:0] OUT_XY_3bit
);

  assign OUT_X__3bit = IN_X_5bit[0] ? 3'b100 : 3'bz;  // Controlled_Buffer controlled_buffer_1
  assign OUT_X__3bit = IN_X_5bit[1] ? 3'b011 : 3'bz;  // Controlled_Buffer controlled_buffer_2
  assign OUT_X__3bit = IN_X_5bit[4] ? 3'b000 : 3'bz;  // Controlled_Buffer controlled_buffer_3
  assign OUT_XY_3bit = IN_Y_5bit[0] ? 3'b100 : 3'bz;  // Controlled_Buffer controlled_buffer_4
  assign OUT_XY_3bit = IN_Y_5bit[1] ? 3'b011 : 3'bz;  // Controlled_Buffer controlled_buffer_5
  assign OUT_XY_3bit = IN_Y_5bit[4] ? 3'b000 : 3'bz;  // Controlled_Buffer controlled_buffer_6
  assign OUT_X__3bit = IN_X_5bit[2] ? 3'b010 : 3'bz;  // Controlled_Buffer controlled_buffer_7
  assign OUT_X__3bit = IN_X_5bit[3] ? 3'b001 : 3'bz;  // Controlled_Buffer controlled_buffer_8
  assign OUT_XY_3bit = IN_Y_5bit[2] ? 3'b010 : 3'bz;  // Controlled_Buffer controlled_buffer_9
  assign OUT_XY_3bit = IN_Y_5bit[3] ? 3'b001 : 3'bz;  // Controlled_Buffer controlled_buffer_10
endmodule

module Uklad_zwracania_pozycji_sasiednich_bitow (
  input  [4:0] Input_Y,
  input  [4:0] Input_X,
  output [2:0] O_X,
  output [5:0] LG,
  output [5:0] DP,
  output [2:0] O_Y,
  output [5:0] G,
  output [5:0] D,
  output [5:0] PG,
  output [5:0] LD,
  output [5:0] L,
  output [5:0] P
);

  wire DY, LX, not_1_out, not_2_out, not_3_out, not_4_out, not_5_out, not_6_out, not_7_out, not_8_out,
       not_9_out, not_10_out, not_11_out, not_12_out, PX, UY;
  wire [2:0] O_D_Y, O_L_X, O_P_X, O_U_Y;

  Comparator #(.width(3)) comparator_1 (.a(L[5:3]), .b(O_U_Y), .eq(UY));  // open: gt, lt
  Comparator #(.width(3)) comparator_2 (.a(L[5:3]), .b(O_L_X), .eq(LX));  // open: gt, lt
  Comparator #(.width(3)) comparator_3 (.a(L[5:3]), .b(O_D_Y), .eq(DY));  // open: gt, lt
  Comparator #(.width(3)) comparator_4 (.a(L[5:3]), .b(O_P_X), .eq(PX));  // open: gt, lt
  Uklad_zwracania_sasiednich_pomocniczy uklad_zwracania_sasiednich_pomocniczy_1 (
    .Input(Input_X), .Output_up(O_L_X), .Output_down(O_P_X));
  Uklad_zwracania_sasiednich_pomocniczy uklad_zwracania_sasiednich_pomocniczy_2 (
    .Input(Input_Y), .Output_up(O_U_Y), .Output_down(O_D_Y));
  Uklad_zmiany_sterowania_z_3bit_na_5bit uklad_zmiany_sterowania_z_3bit_na_5bit_1 (
    .IN_X_5bit(Input_X), .IN_Y_5bit(Input_Y), .OUT_X__3bit(D[2:0]), .OUT_XY_3bit(L[5:3]));
  assign LG[2:0] = LX ? 3'b111 : 3'bz;  // Controlled_Buffer controlled_buffer_1
  assign LG[5:3] = UY ? 3'b111 : 3'bz;  // Controlled_Buffer controlled_buffer_2
  assign LG[5:3] = not_1_out ? O_U_Y : 3'bz;  // Controlled_Buffer controlled_buffer_3
  not not_1 (not_1_out, UY);
  assign G[5:3] = UY ? 3'b111 : 3'bz;  // Controlled_Buffer controlled_buffer_4
  assign G[5:3] = not_2_out ? O_U_Y : 3'bz;  // Controlled_Buffer controlled_buffer_5
  not not_2 (not_2_out, UY);
  assign PG[2:0] = PX ? 3'b111 : 3'bz;  // Controlled_Buffer controlled_buffer_6
  assign PG[5:3] = UY ? 3'b111 : 3'bz;  // Controlled_Buffer controlled_buffer_7
  assign PG[5:3] = not_3_out ? O_U_Y : 3'bz;  // Controlled_Buffer controlled_buffer_8
  not not_3 (not_3_out, UY);
  not not_4 (not_4_out, PX);
  assign P[2:0] = PX ? 3'b111 : 3'bz;  // Controlled_Buffer controlled_buffer_9
  not not_5 (not_5_out, LX);
  assign LG[2:0] = not_5_out ? O_L_X : 3'bz;  // Controlled_Buffer controlled_buffer_10
  not not_6 (not_6_out, PX);
  assign PG[2:0] = not_6_out ? O_P_X : 3'bz;  // Controlled_Buffer controlled_buffer_11
  assign P[2:0] = not_4_out ? O_P_X : 3'bz;  // Controlled_Buffer controlled_buffer_12
  not not_7 (not_7_out, DY);
  not not_8 (not_8_out, DY);
  not not_9 (not_9_out, LX);
  assign L[2:0] = not_9_out ? O_L_X : 3'bz;  // Controlled_Buffer controlled_buffer_13
  assign L[2:0] = LX ? 3'b111 : 3'bz;  // Controlled_Buffer controlled_buffer_14
  not not_10 (not_10_out, PX);
  assign DP[2:0] = not_10_out ? O_P_X : 3'bz;  // Controlled_Buffer controlled_buffer_15
  assign DP[2:0] = PX ? 3'b111 : 3'bz;  // Controlled_Buffer controlled_buffer_16
  assign DP[5:3] = DY ? 3'b111 : 3'bz;  // Controlled_Buffer controlled_buffer_17
  assign DP[5:3] = not_7_out ? O_D_Y : 3'bz;  // Controlled_Buffer controlled_buffer_18
  assign D[5:3] = DY ? 3'b111 : 3'bz;  // Controlled_Buffer controlled_buffer_19
  assign D[5:3] = not_11_out ? O_D_Y : 3'bz;  // Controlled_Buffer controlled_buffer_20
  not not_11 (not_11_out, DY);
  not not_12 (not_12_out, LX);
  assign LD[2:0] = not_12_out ? O_L_X : 3'bz;  // Controlled_Buffer controlled_buffer_21
  assign LD[2:0] = LX ? 3'b111 : 3'bz;  // Controlled_Buffer controlled_buffer_22
  assign LD[5:3] = DY ? 3'b111 : 3'bz;  // Controlled_Buffer controlled_buffer_23
  assign LD[5:3] = not_8_out ? O_D_Y : 3'bz;  // Controlled_Buffer controlled_buffer_24

  assign G[2:0] = D[2:0];
  assign O_X = D[2:0];
  assign O_Y = L[5:3];
  assign P[5:3] = L[5:3];

  // Other names for the same wires on the sheet: INX[2:0] = D[2:0]; IN_X[4:0] = Input_X; IN_Y[4:0] = Input_Y;
  //   INY[2:0] = L[5:3]
endmodule

module Uklad_zwracania_sasiednich_pomocniczy (
  input  [4:0] Input,
  output [2:0] Output_up,
  output [2:0] Output_down
);

  Multiplexer #(.select(5), .width(3)) multiplexer_1 (
    .in1(3'b011), .in2(3'b010), .in4(3'b001), .in8(3'b000), .in16(3'b000), .out(Output_up), .sel(Input));  // open: in0, in3, in5, in6, in7, in9, in10, in11, in12, in13, in14, in15, in17, in18, in19, in20, in21, in22, in23, in24, in25, in26, in27, in28, in29, in30, in31, en
  Multiplexer #(.select(5), .width(3)) multiplexer_2 (
    .in1(3'b100), .in2(3'b100), .in4(3'b011), .in8(3'b010), .in16(3'b001), .out(Output_down), .sel(Input));  // open: in0, in3, in5, in6, in7, in9, in10, in11, in12, in13, in14, in15, in17, in18, in19, in20, in21, in22, in23, in24, in25, in26, in27, in28, in29, in30, in31, en
endmodule

module Uklad_przesylu_wartosci_do_wyswietlania (
  input  [3:0] IN_Value,
  input  [2:0] IN_X,
  input  [2:0] IN_Y,
  output [3:0] O_00,
  output [3:0] O_01,
  output [3:0] O_02,
  output [3:0] O_03,
  output [3:0] O_04,
  output [3:0] O_05,
  output [3:0] O_06,
  output [3:0] O_07,
  output [3:0] O_08,
  output [3:0] O_09,
  output [3:0] O_10,
  output [3:0] O_11,
  output [3:0] O_12,
  output [3:0] O_13,
  output [3:0] O_14,
  output [3:0] O_15,
  output [3:0] O_16,
  output [3:0] O_17,
  output [3:0] O_18,
  output [3:0] O_19,
  output [3:0] O_20,
  output [3:0] O_21,
  output [3:0] O_22,
  output [3:0] O_23,
  output [3:0] O_24
);

  wire not_1_out;
  wire [4:0] controlled_buffer_1_out, Sterowanie_MUX;

  Multiplexer #(.select(3), .width(5)) multiplexer_1 (
    .in0(5'b00101), .in1(5'b00110), .in2(5'b00111), .in3(5'b11110), .in4({5{1'b1}}), .out(Sterowanie_MUX),
    .sel(IN_X));  // open: in5, in6, in7, en
  Demultiplexer #(.select(5), .width(4)) demultiplexer_1 (
    .out0(O_00), .out1(O_01), .out2(O_02), .out3(O_03), .out4(O_04), .out5(O_20), .out6(O_21), .out7(O_22),
    .out8(O_05), .out9(O_06), .out10(O_07), .out11(O_08), .out12(O_09), .out16(O_10), .out17(O_11),
    .out18(O_12), .out19(O_13), .out20(O_14), .out24(O_15), .out25(O_16), .out26(O_17), .out27(O_18),
    .out28(O_19), .out30(O_23), .out31(O_24), .in(IN_Value), .sel(controlled_buffer_1_out));  // open: out13, out14, out15, out21, out22, out23, out29, en
  assign controlled_buffer_1_out = not_1_out ? {IN_Y[1:0], IN_X} : 5'bz;  // Controlled_Buffer controlled_buffer_1
  not not_1 (not_1_out, IN_Y[2]);
  assign controlled_buffer_1_out = IN_Y[2] ? Sterowanie_MUX : 5'bz;  // Controlled_Buffer controlled_buffer_2

  // Other names for the same wires on the sheet: IN_V[3:0] = IN_Value; STER = IN_Y[2];
  //   Sterowanie_XY[4:0] = {IN_Y[1:0], IN_X}
endmodule

module \Sterowanie_dużo  (
  input  [6:0] Wejscie_Klawiatury,
  output [24:0] Nr_Zaznaczonego_pola,
  output Enter,
  output M,
  output [4:0] X,
  output [4:0] Y
);

  wire and_2_out;
  wire [2:0] sterowanie_z_klawiatury_1__3_a_4_s_1_d_6_w_5_enter, undriven;

  Sterowanie_z_klawiatury sterowanie_z_klawiatury_1 (
    .\input (Wejscie_Klawiatury),
    ._3_a_4_s_1_d_6_w_5_enter(sterowanie_z_klawiatury_1__3_a_4_s_1_d_6_w_5_enter), .przemiesc_kursor(M));
  uklad_zwracajacy_pozycje uklad_zwracajacy_pozycje_1 (
    .Sterowanie(sterowanie_z_klawiatury_1__3_a_4_s_1_d_6_w_5_enter), .Move(M), .Poz_X(X), .Poz_Y(Y));
  and and_1 (Enter, sterowanie_z_klawiatury_1__3_a_4_s_1_d_6_w_5_enter[0], sterowanie_z_klawiatury_1__3_a_4_s_1_d_6_w_5_enter[2]);
  and and_2 (and_2_out, undriven[0], undriven[2]);
  ROM #(.addrWidth(10), .dataWidth(25)) rom_1 (.addr({Y, X}), .data(Nr_Zaznaczonego_pola));  // open: sel
  ROM #(.addrWidth(10), .dataWidth(25)) rom_2 ();  // open: addr, data, sel

  // Notes on the sheet:
  //   contents of rom_1 (hex, n*v repeats v):
  //   33*0 1efffff 1dfffff 0 1bfffff 0 0 0 17fffff 7*0 ffffff 16*0 1ff7fff 1feffff 0 1fdffff 0 0 0 1fbffff
  //   7*0 1f7ffff 48*0 1fffbff 1fff7ff 0 1ffefff 0 0 0 1ffdfff 7*0 1ffbfff 111*0 1fffdff 1ffffdf 1ffffbf 0
  //   1ffff7f 0 0 0 1fffeff 7*0 1fffdff 1ffffdf 1ffffbf 0 1ffff7f 236*0 1fffffe 1fffffd 0 1fffffb 0 0 0
  //   1fffff7 7*0 1ffffef
  //   contents of rom_2 (hex, n*v repeats v):
  //   33*0 1efffff 1dfffff 0 1bfffff 0 0 0 17fffff 7*0 ffffff 16*0 1ff7fff 1feffff 0 1fdffff 0 0 0 1fbffff
  //   7*0 1f7ffff 48*0 1fffbff 1fff7ff 0 1ffefff 0 0 0 1ffdfff 7*0 1ffbfff 111*0 1fffdff 1ffffdf 1ffffbf 0
  //   1ffff7f 0 0 0 1fffeff 7*0 1fffdff 1ffffdf 1ffffbf 0 1ffff7f 236*0 1fffffe 1fffffd 0 1fffffb 0 0 0
  //   1fffff7 7*0 1ffffef
endmodule
