// Logisim project Układ zmieny sygnaly sterowania z 5bit na 3bit.circ as structural Verilog: 1 circuit, main circuit main
module main (
  input  [4:0] IN_X_5bit,
  input  [4:0] IN_Y_5bit,
  output [2:0] OUT_X__3bit,
  output [2:0] OUT_XY_3bit
);

  assign OUT_X__3bit = IN_X_5bit[0] ? 3'b100 : 3'bz;  // Controlled_Buffer controlled_buffer_1
  assign OUT_X__3bit = IN_X_5bit[1] ? 3'b011 : 3'bz;  // Controlled_Buffer controlled_buffer_2
  assign OUT_X__3bit = IN_X_5bit[4] ? 3'b000 : 3'bz;  // Controlled_Buffer controlled_buffer_3
  assign OUT_XY_3bit = IN_Y_5bit[0] ? 3'b100 : 3'bz;  // Controlled_Buffer controlled_buffer_4
  assign OUT_XY_3bit = IN_Y_5bit[1] ? 3'b011 : 3'bz;  // Controlled_Buffer controlled_buffer_5
  assign OUT_XY_3bit = IN_Y_5bit[4] ? 3'b000 : 3'bz;  // Controlled_Buffer controlled_buffer_6
  assign OUT_X__3bit = IN_X_5bit[2] ? 3'b010 : 3'bz;  // Controlled_Buffer controlled_buffer_7
  assign OUT_X__3bit = IN_X_5bit[3] ? 3'b001 : 3'bz;  // Controlled_Buffer controlled_buffer_8
  assign OUT_XY_3bit = IN_Y_5bit[2] ? 3'b010 : 3'bz;  // Controlled_Buffer controlled_buffer_9
  assign OUT_XY_3bit = IN_Y_5bit[3] ? 3'b001 : 3'bz;  // Controlled_Buffer controlled_buffer_10
endmodule
