// Logisim project blok sterowania z klawiatury.circ as structural Verilog: 1 circuit, main circuit main
module main (
  input  [6:0] \input ,
  output [2:0] _3_a_4_s_1_d_6_w_5_enter,
  output przemiesc_kursor
);

  wire [4:0] main_1__1_oznacza_ze_jest_rowne;

  Komparator_7bit__tylko_czy_rowna__main main_1 (
    .A(\input ), .B(7'b1100001), ._1_oznacza_ze_jest_rowne(main_1__1_oznacza_ze_jest_rowne[0]));
  Komparator_7bit__tylko_czy_rowna__main main_2 (
    .A(\input ), .B(7'b1110011), ._1_oznacza_ze_jest_rowne(main_1__1_oznacza_ze_jest_rowne[1]));
  Komparator_7bit__tylko_czy_rowna__main main_3 (
    .A(\input ), .B(7'b1100100), ._1_oznacza_ze_jest_rowne(main_1__1_oznacza_ze_jest_rowne[2]));
  Komparator_7bit__tylko_czy_rowna__main main_4 (
    .A(\input ), .B(7'b1110111), ._1_oznacza_ze_jest_rowne(main_1__1_oznacza_ze_jest_rowne[3]));
  Komparator_7bit__tylko_czy_rowna__main main_5 (
    .A(\input ), .B(7'b0001010), ._1_oznacza_ze_jest_rowne(main_1__1_oznacza_ze_jest_rowne[4]));
  or or_1 (przemiesc_kursor, main_1__1_oznacza_ze_jest_rowne[0], main_1__1_oznacza_ze_jest_rowne[1], main_1__1_oznacza_ze_jest_rowne[2], main_1__1_oznacza_ze_jest_rowne[3]);
  ROM #(.addrWidth(5), .dataWidth(3)) rom_1 (
    .addr(main_1__1_oznacza_ze_jest_rowne), .data(_3_a_4_s_1_d_6_w_5_enter));  // open: sel

  // Notes on the sheet:
  //   contents of rom_1 (hex, n*v repeats v):
  //   0 3 4 0 1 0 0 0 6 7*0 5
endmodule
