// Logisim project blok zwracajacy pozycje.circ as structural Verilog: 1 circuit, main circuit main
module main (
  input  [2:0] Sterowanie,
  input  Move,
  output [4:0] Poz_X,
  output [4:0] Poz_Y
);

  wire and_1_out, buffer_1_out, buffer_2_out, buffer_3_out, not_1_out;
  wire [2:0] counter_1_q, counter_2_q;

  not not_1 (not_1_out, Sterowanie[0]);
  buf buffer_1 (buffer_1_out, Sterowanie[1]);
  Counter #(.width(3), .max('h4), .trigger("falling")) counter_1 (
    .load(Sterowanie[1]), .D(counter_1_q), .count(Sterowanie[0]), .Q(counter_1_q), .clk(buffer_2_out));  // open: carry, clr
  buf buffer_2 (buffer_2_out, Move);
  Counter #(.width(3), .max('h4), .trigger("falling")) counter_2 (
    .load(buffer_1_out), .D(counter_2_q), .count(and_1_out), .Q(counter_2_q), .clk(buffer_3_out));  // open: carry, clr
  buf buffer_3 (buffer_3_out, Move);
  and and_1 (and_1_out, not_1_out, Sterowanie[2]);
  Shifter #(.width(5), .shift("rr")) shifter_1 (.in(5'b10000), .\dist (counter_1_q), .out(Poz_X));
  Shifter #(.width(5), .shift("rr")) shifter_2 (.in(5'b10000), .\dist (counter_2_q), .out(Poz_Y));

  // Other names for the same wires on the sheet: Control[2:0] = Sterowanie; M = Move
endmodule
