// Logisim project TEst licznika czasu.circ as structural Verilog: 1 circuit, main circuit main
module main (
  input  in_1,
  input  in_2,
  output [11:0] out_3
);

  wire clock_1_out;
  wire [1:0] DISP;
  wire [2:0] W1D, W2D, W3D, W4D;
  wire [3:0] W1U, W2U, W3U, W4U;

  Clock clock_1 (.out(clock_1_out));
  licznik_czasu_main main_1 (.Czas(out_3), .CLK(clock_1_out), .Stop(in_1), .Start(in_2), .out_5(DISP));
  _7_Segment_Display u_7_segment_display_1 (
    .g(W4U[3]), .f(W4U[2]), .a(W4U[1]), .b(W4U[0]), .e(W4D[2]), .d(W4D[1]), .c(W4D[0]));  // open: dp
  _7_Segment_Display u_7_segment_display_2 (
    .g(W3U[3]), .f(W3U[2]), .a(W3U[1]), .b(W3U[0]), .e(W3D[2]), .d(W3D[1]), .c(W3D[0]));  // open: dp
  _7_Segment_Display u_7_segment_display_3 (
    .g(W2U[3]), .f(W2U[2]), .a(W2U[1]), .b(W2U[0]), .e(W2D[2]), .d(W2D[1]), .c(W2D[0]));  // open: dp
  _7_Segment_Display u_7_segment_display_4 (
    .g(W1U[3]), .f(W1U[2]), .a(W1U[1]), .b(W1U[0]), .e(W1D[2]), .d(W1D[1]), .c(W1D[0]));  // open: dp
  wyswietlacz_czasu wyswietlacz_czasu_1 (
    .DISP_IN__1bit_reset_0bit_clk(DISP), .O3D(W4D), .O2D(W3D), .O1D(W2D), .O0D(W1D), .O3U(W4U), .O2U(W3U),
    .O1U(W2U), .O0U(W1U));
endmodule
