// Logisim project Test nowego sterowania focusem.circ as structural Verilog: 1 circuit, main circuit main
module main (
  output [2:0] out_1,
  output [2:0] out_2,
  output [2:0] out_3,
  output [4:0] out_4
);

  wire clock_1_out, sterowanie_z_klawiatury_1_przemiesc_kursor;
  wire [4:0] uklad_zwracajacy_pozycje_1_poz_x;
  wire [6:0] keyboard_1_data;

  Clock #(.highDuration(4), .lowDuration(2)) clock_1 (.out(clock_1_out));
  Keyboard #(.buflen(1)) keyboard_1 (.clk(clock_1_out), .data(keyboard_1_data));  // open: re, clr, avail
  Sterowanie_z_klawiatury sterowanie_z_klawiatury_1 (
    .\input (keyboard_1_data), ._3_a_4_s_1_d_6_w_5_enter(out_3),
    .przemiesc_kursor(sterowanie_z_klawiatury_1_przemiesc_kursor));
  uklad_zwracajacy_pozycje uklad_zwracajacy_pozycje_1 (
    .Sterowanie(out_3), .Move(sterowanie_z_klawiatury_1_przemiesc_kursor),
    .Poz_X(uklad_zwracajacy_pozycje_1_poz_x), .Poz_Y(out_4));
  Uklad_zmiany_sterowania_z_3bit_na_5bit uklad_zmiany_sterowania_z_3bit_na_5bit_1 (
    .IN_X_5bit(uklad_zwracajacy_pozycje_1_poz_x), .IN_Y_5bit(out_4), .OUT_X__3bit(out_1), .OUT_XY_3bit(out_2));
  DotMatrix #(.inputtype("row"), .matrixrows(1)) dotmatrix_1 (.row0(uklad_zwracajacy_pozycje_1_poz_x));
  DotMatrix #(.matrixcols(1), .matrixrows(5)) dotmatrix_2 (.col0(out_4));
endmodule
