// Logisim project Test stary układ.circ as structural Verilog: 1 circuit, main circuit main
// 1
module main (
  input  [4:0] in_1,
  input  [4:0] in_2
);

  wire clock_1_out, not_1_out, not_2_out, not_3_out, not_4_out;
  wire [4:0] controlled_buffer_1_out, controlled_buffer_3_out, controlled_buffer_5_out,
       controlled_buffer_6_out;
  wire [6:0] keyboard_1_data;
  wire [15:0] main_1_numer_matrycy;
  wire [20:0] blok_z_focusem_1_wyjscia_dolne, main_2_out_3, main_3_out_3, main_4_out_3, main_5_out_3;
  wire [27:0] blok_z_focusem_1_wyjscia_gorne, main_2_out_2, main_3_out_2, main_4_out_2, main_5_out_2;

  Clock clock_1 (.out(clock_1_out));
  Keyboard keyboard_1 (.clk(clock_1_out), .data(keyboard_1_data));  // open: re, clr, avail
  Random random_1 ();  // open: clk, next, out, clr
  blok_wyboru_focusu_main main_1 (.Wejscie_z_klawiatury(keyboard_1_data), .Numer_matrycy(main_1_numer_matrycy));
  blok_z_focusem blok_z_focusem_1 (
    .in_1(in_1), .focus(main_1_numer_matrycy[0]), .wyjscia_gorne(blok_z_focusem_1_wyjscia_gorne),
    .wyjscia_dolne(blok_z_focusem_1_wyjscia_dolne));
  assign controlled_buffer_1_out = main_1_numer_matrycy[0] ? in_1 : 5'bz;  // Controlled_Buffer controlled_buffer_1
  not not_1 (not_1_out, main_1_numer_matrycy[0]);
  DotMatrix #(.inputtype("row"), .matrixcols(7)) dotmatrix_1 (
    .row0(blok_z_focusem_1_wyjscia_gorne[6:0]), .row1(blok_z_focusem_1_wyjscia_gorne[13:7]),
    .row2(blok_z_focusem_1_wyjscia_gorne[20:14]), .row3(blok_z_focusem_1_wyjscia_gorne[27:21]),
    .row4(blok_z_focusem_1_wyjscia_dolne[6:0]), .row5(blok_z_focusem_1_wyjscia_dolne[13:7]),
    .row6(blok_z_focusem_1_wyjscia_dolne[20:14]));
  assign controlled_buffer_1_out = not_1_out ? in_2 : 5'bz;  // Controlled_Buffer controlled_buffer_2
  assign controlled_buffer_3_out = main_1_numer_matrycy[4] ? in_1 : 5'bz;  // Controlled_Buffer controlled_buffer_3
  assign controlled_buffer_3_out = not_2_out ? in_2 : 5'bz;  // Controlled_Buffer controlled_buffer_4
  not not_2 (not_2_out, main_1_numer_matrycy[4]);
  DotMatrix #(.inputtype("row"), .matrixcols(7)) dotmatrix_2 (
    .row0(main_2_out_2[6:0]), .row1(main_2_out_2[13:7]), .row2(main_2_out_2[20:14]),
    .row3(main_2_out_2[27:21]), .row4(main_2_out_3[6:0]), .row5(main_2_out_3[13:7]),
    .row6(main_2_out_3[20:14]));
  ukadz1_main main_2 (.in_1(controlled_buffer_1_out), .out_2(main_2_out_2), .out_3(main_2_out_3));
  DotMatrix #(.inputtype("row"), .matrixcols(7)) dotmatrix_3 (
    .row0(main_3_out_2[6:0]), .row1(main_3_out_2[13:7]), .row2(main_3_out_2[20:14]),
    .row3(main_3_out_2[27:21]), .row4(main_3_out_3[6:0]), .row5(main_3_out_3[13:7]),
    .row6(main_3_out_3[20:14]));
  ukadz1_main main_3 (.in_1(controlled_buffer_3_out), .out_2(main_3_out_2), .out_3(main_3_out_3));
  assign controlled_buffer_5_out = main_1_numer_matrycy[1] ? in_1 : 5'bz;  // Controlled_Buffer controlled_buffer_5
  not not_3 (not_3_out, main_1_numer_matrycy[1]);
  assign controlled_buffer_6_out = main_1_numer_matrycy[5] ? in_1 : 5'bz;  // Controlled_Buffer controlled_buffer_6
  not not_4 (not_4_out, main_1_numer_matrycy[5]);
  ukadz1_main main_4 (.in_1(controlled_buffer_5_out), .out_2(main_4_out_2), .out_3(main_4_out_3));
  assign controlled_buffer_5_out = not_3_out ? in_2 : 5'bz;  // Controlled_Buffer controlled_buffer_7
  assign controlled_buffer_6_out = not_4_out ? in_2 : 5'bz;  // Controlled_Buffer controlled_buffer_8
  DotMatrix #(.inputtype("row"), .matrixcols(7)) dotmatrix_4 (
    .row0(main_4_out_2[6:0]), .row1(main_4_out_2[13:7]), .row2(main_4_out_2[20:14]),
    .row3(main_4_out_2[27:21]), .row4(main_4_out_3[6:0]), .row5(main_4_out_3[13:7]),
    .row6(main_4_out_3[20:14]));
  DotMatrix #(.inputtype("row"), .matrixcols(7)) dotmatrix_5 (
    .row0(main_5_out_2[6:0]), .row1(main_5_out_2[13:7]), .row2(main_5_out_2[20:14]),
    .row3(main_5_out_2[27:21]), .row4(main_5_out_3[6:0]), .row5(main_5_out_3[13:7]),
    .row6(main_5_out_3[20:14]));
  ukadz1_main main_5 (.in_1(controlled_buffer_6_out), .out_2(main_5_out_2), .out_3(main_5_out_3));

  // Other names for the same wires on the sheet: C[4:0] = in_2; D[4:0] = in_1
endmodule
