// Logisim project układtest2.circ as structural Verilog: 1 circuit, main circuit main
module main (
  input  [24:0] in_1,
  input  [3:0] in_2,
  input  [3:0] in_3,
  input  [3:0] in_4,
  input  [3:0] in_5,
  input  [3:0] in_6,
  input  [3:0] in_7,
  input  [3:0] in_8,
  input  [3:0] in_9,
  input  [3:0] in_10,
  input  [3:0] in_11,
  input  [3:0] in_12,
  input  [3:0] in_13,
  input  [3:0] in_14,
  input  [3:0] in_15,
  input  [3:0] in_16,
  input  [3:0] in_17,
  input  [3:0] in_18,
  input  [3:0] in_19,
  input  [3:0] in_20,
  input  [3:0] in_21,
  input  [3:0] in_22,
  input  [3:0] in_23,
  input  [3:0] in_24,
  input  [3:0] in_25,
  input  [3:0] in_26
);

  wire [30:0] main_1_out_28, main_1_out_29, main_1_out_30, main_1_out_31, main_1_out_32, main_1_out_33,
       main_1_out_34, main_1_out_35, main_1_out_36, main_1_out_37, main_1_out_38, main_1_out_39,
       main_1_out_40, main_1_out_41, main_1_out_42, main_1_out_43, main_1_out_44, main_1_out_45,
       main_1_out_46, main_1_out_47, main_1_out_48, main_1_out_49, main_1_out_50, main_1_out_51,
       main_1_out_52, main_1_out_53, main_1_out_54, main_1_out_55, main_1_out_56, main_1_out_57,
       main_1_out_58;

  \Układ_wyświetlania_3_main  main_1 (
    .in_1({31{1'b0}}), ._15(in_2), ._14(in_3), ._13(in_4), ._12(in_5), ._11(in_6), .in_7(in_7), .in_8(in_8),
    .in_9(in_9), .in_10(in_10), .in_11(in_11), .in_12(in_12), .in_13(in_13), .in_14(in_14), .in_15(in_15),
    .in_16(in_16), .in_17(in_1), .in_18(in_17), .in_19(in_18), .in_20(in_19), .in_21(in_20), .in_22(in_21),
    .in_23(in_22), .in_24(in_23), .in_25(in_24), .in_26(in_25), .in_27(in_26), .out_28(main_1_out_28),
    .out_29(main_1_out_29), .out_30(main_1_out_30), .out_31(main_1_out_31), .out_32(main_1_out_32),
    .out_33(main_1_out_33), .out_34(main_1_out_34), .out_35(main_1_out_35), .out_36(main_1_out_36),
    .out_37(main_1_out_37), .out_38(main_1_out_38), .out_39(main_1_out_39), .out_40(main_1_out_40),
    .out_41(main_1_out_41), .out_42(main_1_out_42), .out_43(main_1_out_43), .out_44(main_1_out_44),
    .out_45(main_1_out_45), .out_46(main_1_out_46), .out_47(main_1_out_47), .out_48(main_1_out_48),
    .out_49(main_1_out_49), .out_50(main_1_out_50), .out_51(main_1_out_51), .out_52(main_1_out_52),
    .out_53(main_1_out_53), .out_54(main_1_out_54), .out_55(main_1_out_55), .out_56(main_1_out_56),
    .out_57(main_1_out_57), .out_58(main_1_out_58));
  DotMatrix #(.inputtype("row"), .matrixcols(31), .matrixrows(31)) dotmatrix_1 (
    .row0(main_1_out_28), .row1(main_1_out_29), .row2(main_1_out_30), .row3(main_1_out_31),
    .row4(main_1_out_32), .row5(main_1_out_33), .row6(main_1_out_34), .row7(main_1_out_35),
    .row8(main_1_out_36), .row9(main_1_out_37), .row10(main_1_out_38), .row11(main_1_out_39),
    .row12(main_1_out_40), .row13(main_1_out_41), .row14(main_1_out_42), .row15(main_1_out_43),
    .row16(main_1_out_44), .row17(main_1_out_45), .row18(main_1_out_46), .row19(main_1_out_47),
    .row20(main_1_out_48), .row21(main_1_out_49), .row22(main_1_out_50), .row23(main_1_out_51),
    .row24(main_1_out_52), .row25(main_1_out_53), .row26(main_1_out_54), .row27(main_1_out_55),
    .row28(main_1_out_56), .row29(main_1_out_57), .row30(main_1_out_58));
endmodule
