// Logisim project układtest22.circ as structural Verilog: 1 circuit, main circuit main
module main (
  input  [24:0] in_1,
  input  [3:0] in_2,
  input  [3:0] in_3,
  input  [3:0] in_4,
  input  [3:0] in_5,
  input  [3:0] in_6,
  input  [3:0] in_7,
  input  [3:0] in_8,
  input  [3:0] in_9,
  input  [3:0] in_10,
  input  [3:0] in_11,
  input  [3:0] in_12,
  input  [3:0] in_13,
  input  [3:0] in_14,
  input  [3:0] in_15,
  input  [3:0] in_16,
  input  [3:0] in_17,
  input  [3:0] in_18,
  input  [3:0] in_19,
  input  [3:0] in_20,
  input  [3:0] in_21,
  input  [3:0] in_22,
  input  [3:0] in_23,
  input  [3:0] in_24,
  input  [3:0] in_25,
  input  [3:0] in_26
);

  wire clock_1_out, main_1_p3;
  wire [2:0] main_1_p2;
  wire [4:0] main_2_poz_x, main_2_poz_y;
  wire [6:0] keyboard_1_data;
  wire [24:0] rom_1_data;
  wire [30:0] main_3_out_28, main_3_out_29, main_3_out_30, main_3_out_31, main_3_out_32, main_3_out_33,
       main_3_out_34, main_3_out_35, main_3_out_36, main_3_out_37, main_3_out_38, main_3_out_39,
       main_3_out_40, main_3_out_41, main_3_out_42, main_3_out_43, main_3_out_44, main_3_out_45,
       main_3_out_46, main_3_out_47, main_3_out_48, main_3_out_49, main_3_out_50, main_3_out_51,
       main_3_out_52, main_3_out_53, main_3_out_54, main_3_out_55, main_3_out_56, main_3_out_57,
       main_3_out_58;

  Clock clock_1 (.out(clock_1_out));
  Keyboard #(.buflen(1)) keyboard_1 (.clk(clock_1_out), .data(keyboard_1_data));  // open: re, clr, avail
  // blok_sterowania2_main main_1: pin names not known; wires that end beside it: keyboard_1_data, main_1_p2, main_1_p3
  blok_zwracajacy_pozycje_main main_2 (
    .Sterowanie(main_1_p2), .Move(main_1_p3), .Poz_X(main_2_poz_x), .Poz_Y(main_2_poz_y));
  DotMatrix #(.inputtype("row"), .matrixrows(1)) dotmatrix_1 (.row0(main_2_poz_x));
  DotMatrix #(.matrixcols(1), .matrixrows(5)) dotmatrix_2 (.col0(main_2_poz_y));
  ROM #(.addrWidth(10), .dataWidth(25)) rom_1 (.addr({main_2_poz_y, main_2_poz_x}), .data(rom_1_data));  // open: sel
  \Układ_wyświetlania_3_main  main_3 (
    .in_1({31{1'b0}}), ._15(in_2), ._14(in_3), ._13(in_4), ._12(in_5), ._11(in_6), .in_7(in_7), .in_8(in_8),
    .in_9(in_9), .in_10(in_10), .in_11(in_11), .in_12(in_12), .in_13(in_13), .in_14(in_14), .in_15(in_15),
    .in_16(in_16), .in_17(rom_1_data), .in_18(in_17), .in_19(in_18), .in_20(in_19), .in_21(in_20),
    .in_22(in_21), .in_23(in_22), .in_24(in_23), .in_25(in_24), .in_26(in_25), .in_27(in_26),
    .out_28(main_3_out_28), .out_29(main_3_out_29), .out_30(main_3_out_30), .out_31(main_3_out_31),
    .out_32(main_3_out_32), .out_33(main_3_out_33), .out_34(main_3_out_34), .out_35(main_3_out_35),
    .out_36(main_3_out_36), .out_37(main_3_out_37), .out_38(main_3_out_38), .out_39(main_3_out_39),
    .out_40(main_3_out_40), .out_41(main_3_out_41), .out_42(main_3_out_42), .out_43(main_3_out_43),
    .out_44(main_3_out_44), .out_45(main_3_out_45), .out_46(main_3_out_46), .out_47(main_3_out_47),
    .out_48(main_3_out_48), .out_49(main_3_out_49), .out_50(main_3_out_50), .out_51(main_3_out_51),
    .out_52(main_3_out_52), .out_53(main_3_out_53), .out_54(main_3_out_54), .out_55(main_3_out_55),
    .out_56(main_3_out_56), .out_57(main_3_out_57), .out_58(main_3_out_58));
  DotMatrix #(.inputtype("row"), .matrixcols(31), .matrixrows(31)) dotmatrix_3 (
    .row0(main_3_out_28), .row1(main_3_out_29), .row2(main_3_out_30), .row3(main_3_out_31),
    .row4(main_3_out_32), .row5(main_3_out_33), .row6(main_3_out_34), .row7(main_3_out_35),
    .row8(main_3_out_36), .row9(main_3_out_37), .row10(main_3_out_38), .row11(main_3_out_39),
    .row12(main_3_out_40), .row13(main_3_out_41), .row14(main_3_out_42), .row15(main_3_out_43),
    .row16(main_3_out_44), .row17(main_3_out_45), .row18(main_3_out_46), .row19(main_3_out_47),
    .row20(main_3_out_48), .row21(main_3_out_49), .row22(main_3_out_50), .row23(main_3_out_51),
    .row24(main_3_out_52), .row25(main_3_out_53), .row26(main_3_out_54), .row27(main_3_out_55),
    .row28(main_3_out_56), .row29(main_3_out_57), .row30(main_3_out_58));

  // Notes on the sheet:
  //   contents of rom_1 (hex, n*v repeats v):
  //   513*0 1fffffe 1fffffd 0 1fffffb 0 0 0 1fffff7 7*0 1ffffef
endmodule
