// Logisim project proba1.circ as structural Verilog: 1 circuit, main circuit main
module main (
  input  [4:0] in_1
);

  wire [20:0] main_1_p3;
  wire [27:0] main_1_p2;

  // układzł1_main main_1: pin names not known; wires that end beside it: in_1, main_1_p2, main_1_p3
  DotMatrix #(.inputtype("row"), .matrixcols(7)) dotmatrix_1 (
    .row0(main_1_p2[6:0]), .row1(main_1_p2[13:7]), .row2(main_1_p2[20:14]), .row3(main_1_p2[27:21]),
    .row4(main_1_p3[6:0]), .row5(main_1_p3[13:7]), .row6(main_1_p3[20:14]));
endmodule
