// Logisim project sterowanie matryca 5x5.circ as structural Verilog: 1 circuit, main circuit main
module main (
  input  [3:0] stan,
  input  focus,
  output [4:0] O1,
  output [4:0] O2,
  output [4:0] O3,
  output [4:0] O4,
  output [4:0] O5
);

  wire [24:0] or_1_out, rom_1_data;

  ROM #(.addrWidth(4), .dataWidth(25)) rom_1 (.addr(stan), .data(rom_1_data));  // open: sel
  assign or_1_out = rom_1_data | {25{1'b0}};  // OR_Gate or_1, 25 bits wide
  Multiplexer #(.width(25)) multiplexer_1 (
    .in0(rom_1_data), .in1(or_1_out), .out({O5, O4, O3, O2, O1}), .sel(focus));  // open: en

  // Notes on the sheet:
  //   contents of rom_1 (hex, n*v repeats v):
  //   23434
endmodule
