// Logisim project ukadz1.circ as structural Verilog: 2 circuits, main circuit main
module main (
  input  [4:0] in_1,
  output [27:0] out_2,
  output [20:0] out_3
);

  ROM #(.addrWidth(5), .dataWidth(28)) rom_1 (.addr(in_1), .data(out_2));  // open: sel
  ROM #(.addrWidth(5), .dataWidth(21)) rom_2 (.addr(in_1), .data(out_3));  // open: sel

  // Notes on the sheet:
  //   contents of rom_1 (hex, n*v repeats v):
  //   41 1020400 3810e00 3810e00 3850a00 3840e00 3840e00 810e00 3850e00 1020441 3810e41 3810e41 3850a41
  //   3840e41 3840e41 810e41 3850e41
  //   contents of rom_2 (hex, n*v repeats v):
  //   104000 408 e10 e04 204 e04 e14 204 e14 104408 104e10 104e04 104204 104e04 104e14 104204 104e14
endmodule

module blok_z_focusem (
  input  [4:0] in_1,
  input  focus,
  output [27:0] wyjscia_gorne,
  output [20:0] wyjscia_dolne
);

  wire not_1_out, not_2_out;
  wire [6:0] rom_1_data;
  wire [20:14] rom_2_data;

  ROM #(.addrWidth(5), .dataWidth(28)) rom_1 (.addr(in_1), .data({wyjscia_gorne[27:7], rom_1_data}));  // open: sel
  ROM #(.addrWidth(5), .dataWidth(21)) rom_2 (.addr(in_1), .data({rom_2_data, wyjscia_dolne[13:0]}));  // open: sel
  assign wyjscia_gorne[6:0] = focus ? 7'b1000001 : 7'bz;  // Controlled_Buffer controlled_buffer_1
  assign wyjscia_gorne[6:0] = not_1_out ? {7{1'b0}} : 7'bz;  // Controlled_Buffer controlled_buffer_2
  not not_1 (not_1_out, focus);
  assign wyjscia_dolne[20:14] = focus ? 7'b1000001 : 7'bz;  // Controlled_Buffer controlled_buffer_3
  assign wyjscia_dolne[20:14] = not_2_out ? {7{1'b0}} : 7'bz;  // Controlled_Buffer controlled_buffer_4
  not not_2 (not_2_out, focus);

  // Other names for the same wires on the sheet: f = focus; d2[13:0] = wyjscia_dolne[13:0];
  //   d1[20:0] = wyjscia_gorne[27:7]

  // Notes on the sheet:
  //   contents of rom_1 (hex, n*v repeats v):
  //   41 1020400 3810e00 3810e00 3850a00 3840e00 3840e00 810e00 3850e00 1020441 3810e41 3810e41 3850a41
  //   3840e41 3840e41 810e41 3850e41
  //   contents of rom_2 (hex, n*v repeats v):
  //   104000 408 e10 e04 204 e04 e14 204 e14 104408 104e10 104e04 104204 104e04 104e14 104204 104e14
endmodule
