// Logisim project uklad wysweitlania 1 koluny pol.circ as structural Verilog: 1 circuit, main circuit main
module main (
  input  [3:0] State,
  input  f,
  output [29:0] O1,
  output [29:0] O2,
  output [29:0] O3,
  output [29:0] O4,
  output [29:0] O5
);

  sterowanie_matryca_5x5_main main_1 (
    .stan(State), .focus(f), .O1(O1[4:0]), .O2(O2[4:0]), .O3(O3[4:0]), .O4(O4[4:0]), .O5(O5[4:0]));
  sterowanie_matryca_5x5_main main_2 (
    .stan(State), .focus(f), .O1(O1[19:15]), .O2(O2[19:15]), .O3(O3[19:15]), .O4(O4[19:15]), .O5(O5[19:15]));
  sterowanie_matryca_5x5_main main_3 (
    .stan(State), .focus(f), .O1(O1[9:5]), .O2(O2[9:5]), .O3(O3[9:5]), .O4(O4[9:5]), .O5(O5[9:5]));
  sterowanie_matryca_5x5_main main_4 (
    .stan(State), .focus(f), .O1(O1[24:20]), .O2(O2[24:20]), .O3(O3[24:20]), .O4(O4[24:20]), .O5(O5[24:20]));
  sterowanie_matryca_5x5_main main_5 (
    .stan(State), .focus(f), .O1(O1[14:10]), .O2(O2[14:10]), .O3(O3[14:10]), .O4(O4[14:10]), .O5(O5[14:10]));
  sterowanie_matryca_5x5_main main_6 (
    .stan(State), .focus(f), .O1(O1[29:25]), .O2(O2[29:25]), .O3(O3[29:25]), .O4(O4[29:25]), .O5(O5[29:25]));
  DotMatrix #(.matrixrows(30)) dotmatrix_1 (.col0(O1), .col1(O2), .col2(O3), .col3(O4), .col4(O5));

  // Other names for the same wires on the sheet: d1[29:0] = O1; P1_1[4:0] = O1[4:0]; P2_1[4:0] = O1[9:5];
  //   P3_1[4:0] = O1[14:10]; P4_1[4:0] = O1[19:15]; P5_1[4:0] = O1[24:20]; P6_1[4:0] = O1[29:25]; d2[29:0] = O2;
  //   P1_2[4:0] = O2[4:0]; P2_2[4:0] = O2[9:5]; P3_2[4:0] = O2[14:10]; P4_2[4:0] = O2[19:15]; P5_2[4:0] = O2[24:20];
  //   P6_2[4:0] = O2[29:25]; d3[29:0] = O3; P1_3[4:0] = O3[4:0]; P2_3[4:0] = O3[9:5]; P3_3[4:0] = O3[14:10];
  //   P4_3[4:0] = O3[19:15]; P5_3[4:0] = O3[24:20]; P6_3[4:0] = O3[29:25]; d4[29:0] = O4; P1_4[4:0] = O4[4:0];
  //   P2_4[4:0] = O4[9:5]; P3_4[4:0] = O4[14:10]; P4_4[4:0] = O4[19:15]; P5_4[4:0] = O4[24:20]; P6_4[4:0] = O4[29:25];
  //   d5[29:0] = O5; P1_5[4:0] = O5[4:0]; P2_5[4:0] = O5[9:5]; P3_5[4:0] = O5[14:10]; P4_5[4:0] = O5[19:15];
  //   P5_5[4:0] = O5[24:20]; P6_5[4:0] = O5[29:25]; f_1 = f; S_1[3:0] = State
endmodule
