// Logisim project Układ wyświetlania 3.circ as structural Verilog: 1 circuit, main circuit main
module main (
  input  [30:0] in_1,
  input  [3:0] in_2,
  input  [3:0] in_3,
  input  [3:0] in_4,
  input  [3:0] in_5,
  input  [3:0] in_6,
  input  [3:0] in_7,
  input  [3:0] in_8,
  input  [3:0] in_9,
  input  [3:0] in_10,
  input  [3:0] in_11,
  input  [3:0] in_12,
  input  [3:0] in_13,
  input  [3:0] in_14,
  input  [3:0] in_15,
  input  [3:0] in_16,
  input  [24:0] in_17,
  input  [3:0] in_18,
  input  [3:0] in_19,
  input  [3:0] in_20,
  input  [3:0] in_21,
  input  [3:0] in_22,
  input  [3:0] in_23,
  input  [3:0] in_24,
  input  [3:0] in_25,
  input  [3:0] in_26,
  input  [3:0] in_27,
  output [30:0] out_28,
  output [30:0] out_29,
  output [30:0] out_30,
  output [30:0] out_31,
  output [30:0] out_32,
  output [30:0] out_33,
  output [30:0] out_34,
  output [30:0] out_35,
  output [30:0] out_36,
  output [30:0] out_37,
  output [30:0] out_38,
  output [30:0] out_39,
  output [30:0] out_40,
  output [30:0] out_41,
  output [30:0] out_42,
  output [30:0] out_43,
  output [30:0] out_44,
  output [30:0] out_45,
  output [30:0] out_46,
  output [30:0] out_47,
  output [30:0] out_48,
  output [30:0] out_49,
  output [30:0] out_50,
  output [30:0] out_51,
  output [30:0] out_52,
  output [30:0] out_53,
  output [30:0] out_54,
  output [30:0] out_55,
  output [30:0] out_56,
  output [30:0] out_57,
  output [30:0] out_58
);

  wire [24:0] main_1_out_3, main_2_out_3, main_3_out_3, main_4_out_3, main_5_out_3, main_6_out_3,
       main_7_out_3, main_8_out_3, main_9_out_3, main_10_out_3, main_11_out_3, main_12_out_3, main_13_out_3,
       main_14_out_3, main_15_out_3, main_16_out_3, main_17_out_3, main_18_out_3, main_19_out_3,
       main_20_out_3, main_21_out_3, main_22_out_3, main_23_out_3, main_24_out_3, main_25_out_3;

  \Układ_wyświetlania2_main  main_1 (.f(in_17[14]), .in_2(in_16), .out_3(main_1_out_3));
  \Układ_wyświetlania2_main  main_2 (.f(in_17[18]), .in_2(in_21), .out_3(main_2_out_3));
  \Układ_wyświetlania2_main  main_3 (.f(in_17[19]), .in_2(in_22), .out_3(main_3_out_3));
  \Układ_wyświetlania2_main  main_4 (.f(in_17[20]), .in_2(in_23), .out_3(main_4_out_3));
  \Układ_wyświetlania2_main  main_5 (.f(in_17[21]), .in_2(in_24), .out_3(main_5_out_3));
  \Układ_wyświetlania2_main  main_6 (.f(in_17[22]), .in_2(in_25), .out_3(main_6_out_3));
  \Układ_wyświetlania2_main  main_7 (.f(in_17[23]), .in_2(in_26), .out_3(main_7_out_3));
  \Układ_wyświetlania2_main  main_8 (.f(in_17[24]), .in_2(in_27), .out_3(main_8_out_3));
  \Układ_wyświetlania2_main  main_9 (.f(in_17[5]), .in_2(in_7), .out_3(main_9_out_3));
  \Układ_wyświetlania2_main  main_10 (.f(in_17[6]), .in_2(in_8), .out_3(main_10_out_3));
  \Układ_wyświetlania2_main  main_11 (.f(in_17[7]), .in_2(in_9), .out_3(main_11_out_3));
  \Układ_wyświetlania2_main  main_12 (.f(in_17[8]), .in_2(in_10), .out_3(main_12_out_3));
  \Układ_wyświetlania2_main  main_13 (.f(in_17[9]), .in_2(in_11), .out_3(main_13_out_3));
  \Układ_wyświetlania2_main  main_14 (.f(in_17[10]), .in_2(in_12), .out_3(main_14_out_3));
  \Układ_wyświetlania2_main  main_15 (.f(in_17[11]), .in_2(in_13), .out_3(main_15_out_3));
  \Układ_wyświetlania2_main  main_16 (.f(in_17[12]), .in_2(in_14), .out_3(main_16_out_3));
  \Układ_wyświetlania2_main  main_17 (.f(in_17[13]), .in_2(in_15), .out_3(main_17_out_3));
  \Układ_wyświetlania2_main  main_18 (.f(in_17[15]), .in_2(in_18), .out_3(main_18_out_3));
  \Układ_wyświetlania2_main  main_19 (.f(in_17[16]), .in_2(in_19), .out_3(main_19_out_3));
  \Układ_wyświetlania2_main  main_20 (.f(in_17[17]), .in_2(in_20), .out_3(main_20_out_3));
  \Układ_wyświetlania2_main  main_21 (.f(in_17[0]), .in_2(in_2), .out_3(main_21_out_3));
  \Układ_wyświetlania2_main  main_22 (.f(in_17[1]), .in_2(in_3), .out_3(main_22_out_3));
  \Układ_wyświetlania2_main  main_23 (.f(in_17[2]), .in_2(in_4), .out_3(main_23_out_3));
  \Układ_wyświetlania2_main  main_24 (.f(in_17[3]), .in_2(in_5), .out_3(main_24_out_3));
  \Układ_wyświetlania2_main  main_25 (.f(in_17[4]), .in_2(in_6), .out_3(main_25_out_3));
  \Układ_wyświetlania1_main  main_26 (
    .in_1(main_21_out_3), .in_2(main_22_out_3), .in_3(main_23_out_3), .in_4(main_24_out_3),
    .in_5(main_25_out_3), .out_6(out_29), .out_7(out_30), .out_8(out_31), .out_9(out_32), .out_10(out_33));
  \Układ_wyświetlania1_main  main_27 (
    .in_1(main_9_out_3), .in_2(main_10_out_3), .in_3(main_11_out_3), .in_4(main_12_out_3),
    .in_5(main_13_out_3), .out_6(out_35), .out_7(out_36), .out_8(out_37), .out_9(out_38), .out_10(out_39));
  \Układ_wyświetlania1_main  main_28 (
    .in_1(main_14_out_3), .in_2(main_15_out_3), .in_3(main_16_out_3), .in_4(main_17_out_3),
    .in_5(main_1_out_3), .out_6(out_41), .out_7(out_42), .out_8(out_43), .out_9(out_44), .out_10(out_45));
  \Układ_wyświetlania1_main  main_29 (
    .in_1(main_18_out_3), .in_2(main_19_out_3), .in_3(main_20_out_3), .in_4(main_2_out_3),
    .in_5(main_3_out_3), .out_6(out_47), .out_7(out_48), .out_8(out_49), .out_9(out_50), .out_10(out_51));
  \Układ_wyświetlania1_main  main_30 (
    .in_1(main_4_out_3), .in_2(main_5_out_3), .in_3(main_6_out_3), .in_4(main_7_out_3), .in_5(main_8_out_3),
    .out_6(out_53), .out_7(out_54), .out_8(out_55), .out_9(out_56), .out_10(out_57));

  assign out_28 = in_1;
  assign out_34 = in_1;
  assign out_40 = in_1;
  assign out_46 = in_1;
  assign out_52 = in_1;
  assign out_58 = in_1;
  // also tied to VCC on the sheet: {in_1[0], in_1[1], in_1[2], in_1[3], in_1[4], in_1[5], in_1[6], in_1[7], in_1[8], in_1[9], in_1[10], in_1[11], in_1[12], in_1[13], in_1[14], in_1[15], in_1[16], in_1[17], in_1[18], in_1[19], in_1[20], in_1[21], in_1[22], in_1[23], in_1[24], in_1[25], in_1[26], in_1[27], in_1[28], in_1[29], in_1[30]}
endmodule
