// Logisim project licznik 16bit.circ as structural Verilog: 1 circuit, main circuit main
module main (
  input  CLK,
  input  Reset,
  output [15:0] out_3
);

  wire d_ff_1_qn, d_ff_2_qn, d_ff_3_qn, d_ff_4_qn, d_ff_5_qn, d_ff_6_qn, d_ff_7_qn, d_ff_8_qn, d_ff_9_qn,
       d_ff_10_qn, d_ff_11_qn, d_ff_12_qn, d_ff_13_qn, d_ff_14_qn, d_ff_15_qn, d_ff_16_qn;

  D_Flip_Flop d_ff_1 (.clk(CLK), .D(d_ff_1_qn), .Q(out_3[0]), .Qn(d_ff_1_qn), .reset(Reset));  // open: preset, en
  D_Flip_Flop d_ff_2 (
    .clk(d_ff_14_qn), .D(d_ff_2_qn), .Q(out_3[4]), .Qn(d_ff_2_qn), .reset(Reset));  // open: preset, en
  D_Flip_Flop d_ff_3 (
    .clk(d_ff_15_qn), .D(d_ff_3_qn), .Q(out_3[8]), .Qn(d_ff_3_qn), .reset(Reset));  // open: preset, en
  D_Flip_Flop d_ff_4 (
    .clk(d_ff_16_qn), .D(d_ff_4_qn), .Q(out_3[12]), .Qn(d_ff_4_qn), .reset(Reset));  // open: preset, en
  D_Flip_Flop d_ff_5 (
    .clk(d_ff_4_qn), .D(d_ff_5_qn), .Q(out_3[13]), .Qn(d_ff_5_qn), .reset(Reset));  // open: preset, en
  D_Flip_Flop d_ff_6 (.clk(d_ff_1_qn), .D(d_ff_6_qn), .Q(out_3[1]), .Qn(d_ff_6_qn), .reset(Reset));  // open: preset, en
  D_Flip_Flop d_ff_7 (.clk(d_ff_2_qn), .D(d_ff_7_qn), .Q(out_3[5]), .Qn(d_ff_7_qn), .reset(Reset));  // open: preset, en
  D_Flip_Flop d_ff_8 (.clk(d_ff_3_qn), .D(d_ff_8_qn), .Q(out_3[9]), .Qn(d_ff_8_qn), .reset(Reset));  // open: preset, en
  D_Flip_Flop d_ff_9 (.clk(d_ff_6_qn), .D(d_ff_9_qn), .Q(out_3[2]), .Qn(d_ff_9_qn), .reset(Reset));  // open: preset, en
  D_Flip_Flop d_ff_10 (
    .clk(d_ff_7_qn), .D(d_ff_10_qn), .Q(out_3[6]), .Qn(d_ff_10_qn), .reset(Reset));  // open: preset, en
  D_Flip_Flop d_ff_11 (
    .clk(d_ff_8_qn), .D(d_ff_11_qn), .Q(out_3[10]), .Qn(d_ff_11_qn), .reset(Reset));  // open: preset, en
  D_Flip_Flop d_ff_12 (
    .clk(d_ff_5_qn), .D(d_ff_12_qn), .Q(out_3[14]), .Qn(d_ff_12_qn), .reset(Reset));  // open: preset, en
  D_Flip_Flop d_ff_13 (
    .clk(d_ff_12_qn), .D(d_ff_13_qn), .Q(out_3[15]), .Qn(d_ff_13_qn), .reset(Reset));  // open: preset, en
  D_Flip_Flop d_ff_14 (
    .clk(d_ff_9_qn), .D(d_ff_14_qn), .Q(out_3[3]), .Qn(d_ff_14_qn), .reset(Reset));  // open: preset, en
  D_Flip_Flop d_ff_15 (
    .clk(d_ff_10_qn), .D(d_ff_15_qn), .Q(out_3[7]), .Qn(d_ff_15_qn), .reset(Reset));  // open: preset, en
  D_Flip_Flop d_ff_16 (
    .clk(d_ff_11_qn), .D(d_ff_16_qn), .Q(out_3[11]), .Qn(d_ff_16_qn), .reset(Reset));  // open: preset, en
endmodule
