// Logisim project licznik czasu.circ as structural Verilog: 1 circuit, main circuit main
module main (
  input  CLK,
  input  Stop,
  input  Start,
  output [11:0] Czas
);

  wire controlled_buffer_1_out, d_ff_1_qn, d_ff_2_qn, d_ff_3_qn, d_ff_4_qn, d_ff_5_qn, d_ff_6_qn, d_ff_7_qn,
       d_ff_8_qn, d_ff_9_qn, d_ff_10_qn, d_ff_11_qn, d_ff_12_qn, not_1_out, Stop_t;

  not not_1 (not_1_out, Stop_t);
  assign controlled_buffer_1_out = not_1_out ? CLK : 1'bz;  // Controlled_Buffer controlled_buffer_1
  S_R_Flip_Flop #(.trigger("high")) s_r_ff_1 (
    .S(Stop), .clk(1'b1), .R(Start), .Q(Stop_t));  // open: Qn, preset, reset, en
  D_Flip_Flop d_ff_1 (
    .clk(controlled_buffer_1_out), .D(d_ff_1_qn), .Q(Czas[0]), .Qn(d_ff_1_qn), .reset(Start));  // open: preset, en
  D_Flip_Flop d_ff_2 (.clk(d_ff_10_qn), .D(d_ff_2_qn), .Q(Czas[4]), .Qn(d_ff_2_qn), .reset(Start));  // open: preset, en
  D_Flip_Flop d_ff_3 (.clk(d_ff_11_qn), .D(d_ff_3_qn), .Q(Czas[8]), .Qn(d_ff_3_qn), .reset(Start));  // open: preset, en
  D_Flip_Flop d_ff_4 (.clk(d_ff_1_qn), .D(d_ff_4_qn), .Q(Czas[1]), .Qn(d_ff_4_qn), .reset(Start));  // open: preset, en
  D_Flip_Flop d_ff_5 (.clk(d_ff_2_qn), .D(d_ff_5_qn), .Q(Czas[5]), .Qn(d_ff_5_qn), .reset(Start));  // open: preset, en
  D_Flip_Flop d_ff_6 (.clk(d_ff_3_qn), .D(d_ff_6_qn), .Q(Czas[9]), .Qn(d_ff_6_qn), .reset(Start));  // open: preset, en
  D_Flip_Flop d_ff_7 (.clk(d_ff_4_qn), .D(d_ff_7_qn), .Q(Czas[2]), .Qn(d_ff_7_qn), .reset(Start));  // open: preset, en
  D_Flip_Flop d_ff_8 (.clk(d_ff_5_qn), .D(d_ff_8_qn), .Q(Czas[6]), .Qn(d_ff_8_qn), .reset(Start));  // open: preset, en
  D_Flip_Flop d_ff_9 (.clk(d_ff_6_qn), .D(d_ff_9_qn), .Q(Czas[10]), .Qn(d_ff_9_qn), .reset(Start));  // open: preset, en
  D_Flip_Flop d_ff_10 (
    .clk(d_ff_7_qn), .D(d_ff_10_qn), .Q(Czas[3]), .Qn(d_ff_10_qn), .reset(Start));  // open: preset, en
  D_Flip_Flop d_ff_11 (
    .clk(d_ff_8_qn), .D(d_ff_11_qn), .Q(Czas[7]), .Qn(d_ff_11_qn), .reset(Start));  // open: preset, en
  D_Flip_Flop d_ff_12 (
    .clk(d_ff_9_qn), .D(d_ff_12_qn), .Q(Czas[11]), .Qn(d_ff_12_qn), .reset(Start));  // open: preset, en
endmodule
