// Logisim project przyklad przełacznika.circ as structural Verilog: 1 circuit, main circuit main
module main (
  input  [3:0] in_1,
  input  in_2,
  output [3:0] out_3
);

  wire not_1_out;

  not not_1 (not_1_out, in_2);
  assign out_3 = not_1_out ? 4'b1000 : 4'bz;  // Controlled_Buffer controlled_buffer_1
  assign out_3 = in_2 ? in_1 : 4'bz;  // Controlled_Buffer controlled_buffer_2

  // Other names for the same wires on the sheet: Sygnal = in_2
endmodule
