// Logisim project test.circ as structural Verilog: 1 circuit, main circuit main
// 1
module main (
  input  [4:0] in_1,
  input  [4:0] in_2
);

  wire clock_1_out, main_1_przemiesc_kursor, not_1_out, not_2_out, not_3_out, not_4_out;
  wire [1:0] rom_1_data;
  wire [2:0] main_1__1_a_2_s_3_d_4_w_5_enter;
  wire [3:0] main_2_podaje_numer_pola__0_15;
  wire [4:0] controlled_buffer_1_out, controlled_buffer_3_out, controlled_buffer_5_out,
       controlled_buffer_6_out;
  wire [6:0] keyboard_1_data;
  wire [15:0] rom_2_data;
  wire [20:0] main_3_out_3, main_4_out_3, main_5_out_3, main_6_out_3;
  wire [27:0] main_3_out_2, main_4_out_2, main_5_out_2, main_6_out_2;

  blok_sterowania_main main_1 (
    .\input (keyboard_1_data), ._1_a_2_s_3_d_4_w_5_enter(main_1__1_a_2_s_3_d_4_w_5_enter),
    .przemiesc_kursor(main_1_przemiesc_kursor));
  Clock clock_1 (.out(clock_1_out));
  Keyboard keyboard_1 (.clk(clock_1_out), .data(keyboard_1_data));  // open: re, clr, avail
  uklad_przejscia_main main_2 (
    .wejscie_sterowania__wdsa___0_1_2_3(rom_1_data), .CLK(main_1_przemiesc_kursor),
    .podaje_numer_pola__0_15(main_2_podaje_numer_pola__0_15));
  ROM #(.addrWidth(3), .dataWidth(2)) rom_1 (.addr(main_1__1_a_2_s_3_d_4_w_5_enter), .data(rom_1_data));  // open: sel
  ROM #(.addrWidth(4), .dataWidth(16)) rom_2 (.addr(main_2_podaje_numer_pola__0_15), .data(rom_2_data));  // open: sel
  assign controlled_buffer_1_out = rom_2_data[0] ? in_1 : 5'bz;  // Controlled_Buffer controlled_buffer_1
  not not_1 (not_1_out, rom_2_data[0]);
  assign controlled_buffer_1_out = not_1_out ? in_2 : 5'bz;  // Controlled_Buffer controlled_buffer_2
  assign controlled_buffer_3_out = rom_2_data[4] ? in_1 : 5'bz;  // Controlled_Buffer controlled_buffer_3
  assign controlled_buffer_3_out = not_2_out ? in_2 : 5'bz;  // Controlled_Buffer controlled_buffer_4
  not not_2 (not_2_out, rom_2_data[4]);
  DotMatrix #(.inputtype("row"), .matrixcols(7)) dotmatrix_1 (
    .row0(main_3_out_2[6:0]), .row1(main_3_out_2[13:7]), .row2(main_3_out_2[20:14]),
    .row3(main_3_out_2[27:21]), .row4(main_3_out_3[6:0]), .row5(main_3_out_3[13:7]),
    .row6(main_3_out_3[20:14]));
  ukadz1_main main_3 (.in_1(controlled_buffer_1_out), .out_2(main_3_out_2), .out_3(main_3_out_3));
  DotMatrix #(.inputtype("row"), .matrixcols(7)) dotmatrix_2 (
    .row0(main_4_out_2[6:0]), .row1(main_4_out_2[13:7]), .row2(main_4_out_2[20:14]),
    .row3(main_4_out_2[27:21]), .row4(main_4_out_3[6:0]), .row5(main_4_out_3[13:7]),
    .row6(main_4_out_3[20:14]));
  ukadz1_main main_4 (.in_1(controlled_buffer_3_out), .out_2(main_4_out_2), .out_3(main_4_out_3));
  assign controlled_buffer_5_out = rom_2_data[1] ? in_1 : 5'bz;  // Controlled_Buffer controlled_buffer_5
  not not_3 (not_3_out, rom_2_data[1]);
  assign controlled_buffer_6_out = rom_2_data[5] ? in_1 : 5'bz;  // Controlled_Buffer controlled_buffer_6
  not not_4 (not_4_out, rom_2_data[5]);
  ukadz1_main main_5 (.in_1(controlled_buffer_5_out), .out_2(main_5_out_2), .out_3(main_5_out_3));
  assign controlled_buffer_5_out = not_3_out ? in_2 : 5'bz;  // Controlled_Buffer controlled_buffer_7
  assign controlled_buffer_6_out = not_4_out ? in_2 : 5'bz;  // Controlled_Buffer controlled_buffer_8
  DotMatrix #(.inputtype("row"), .matrixcols(7)) dotmatrix_3 (
    .row0(main_5_out_2[6:0]), .row1(main_5_out_2[13:7]), .row2(main_5_out_2[20:14]),
    .row3(main_5_out_2[27:21]), .row4(main_5_out_3[6:0]), .row5(main_5_out_3[13:7]),
    .row6(main_5_out_3[20:14]));
  DotMatrix #(.inputtype("row"), .matrixcols(7)) dotmatrix_4 (
    .row0(main_6_out_2[6:0]), .row1(main_6_out_2[13:7]), .row2(main_6_out_2[20:14]),
    .row3(main_6_out_2[27:21]), .row4(main_6_out_3[6:0]), .row5(main_6_out_3[13:7]),
    .row6(main_6_out_3[20:14]));
  ukadz1_main main_6 (.in_1(controlled_buffer_6_out), .out_2(main_6_out_2), .out_3(main_6_out_3));

  // Other names for the same wires on the sheet: C[4:0] = in_2; D[4:0] = in_1

  // Notes on the sheet:
  //   contents of rom_1 (hex, n*v repeats v):
  //   0 3 2 1
  //   contents of rom_2 (hex, n*v repeats v):
  //   1 2 4 8 10 20 10 40
endmodule
