// Logisim project wypisanie pul.circ as structural Verilog: 1 circuit, main circuit main
// 0x18
module main (
  input  CLK,
  output [9:0] \Wyjścia_X_pierwszy_Y_drugi__2x_5_bit 
);

  wire [4:0] counter_1_q;

  Counter #(.width(5), .max('h19)) counter_1 (.Q(counter_1_q), .clk(CLK));  // open: load, D, count, carry, clr
  Multiplexer #(.select(5), .width(10)) multiplexer_1 (
    .in0(10'h210), .in1(10'h110), .in2(10'h90), .in3(10'h50), .in4(10'h30), .in5(10'h208), .in6(10'h108),
    .in7(10'h88), .in8(10'h48), .in9(10'h28), .in10(10'h204), .in11(10'h104), .in12(10'h84), .in13(10'h44),
    .in14(10'h24), .in15(10'h202), .in16(10'h102), .in17(10'h82), .in18(10'h42), .in19(10'h22),
    .in20(10'h201), .in21(10'h101), .in22(10'h81), .in23(10'h41), .in24(10'h21),
    .out(\Wyjścia_X_pierwszy_Y_drugi__2x_5_bit ), .sel(counter_1_q));  // open: in25, in26, in27, in28, in29, in30, in31, en
endmodule
